// Logisim project PC_with_ROM_CU_test_ASM.circ as structural Verilog
module CPU (
  input  in_1,
  input  in_2,
  input  in_3,
  input  in_4,
  input  [15:0] in_5,
  output O_Clock,
  output [15:0] AddressMemory
);

  wire ALU_AND_EN, ALU_AND_OUT_0, ALU_AND_OUT_1, ALU_AND_OUT_2, ALU_AND_OUT_3, ALU_AND_OUT_4, ALU_AND_OUT_5,
       ALU_AND_OUT_6, ALU_AND_OUT_7, ALU_NEGATIVE_FLAG, ALU_NOT_EN, ALU_OR_EN, ALU_OR_OUT_0, ALU_OR_OUT_1,
       ALU_OR_OUT_2, ALU_OR_OUT_3, ALU_OR_OUT_4, ALU_OR_OUT_5, ALU_OR_OUT_6, ALU_OR_OUT_7, ALU_OVERFLOW_FLAG,
       ALU_SHL_EN, ALU_SHR_EN, ALU_SUM_CARRY_FLAG, ALU_SUM_EN, ALU_SUM_OUT_0, ALU_SUM_OUT_1, ALU_SUM_OUT_2,
       ALU_SUM_OUT_3, ALU_SUM_OUT_4, ALU_SUM_OUT_5, ALU_SUM_OUT_6, ALU_SUM_OUT_7, ALU_XOR_EN, ALU_XOR_OUT_0,
       ALU_XOR_OUT_1, ALU_XOR_OUT_2, ALU_XOR_OUT_3, ALU_XOR_OUT_4, ALU_XOR_OUT_5, ALU_XOR_OUT_6,
       ALU_XOR_OUT_7, ALU_ZERO_FLAG, CARRY, CommandsCounter_n_Clear, CommandsCounter_n_Enable_Counter,
       CommandsCounter_n_Enable_Load, CurrentAddressRegister_n_EN1, CurrentAddressRegister_n_EN2,
       CurrentAddressRegister_n_EN_Out, EN_WRITE_FLAGS, FLAGS_Clock, FLAGS_REGISTER_pin1, FLASH_CE, FLASH_OE,
       FLASH_WE, FM_ADDRESS_REGISTER_SELECT_0, FM_ADDRESS_REGISTER_SELECT_1, FM_REG_1, FM_REG_2, FM_REG_3,
       IN_REG_0_O0, IN_REG_0_O1, IN_REG_0_O2, IN_REG_0_O3, IN_REG_0_O4, IN_REG_0_O5, IN_REG_0_O6,
       IN_REG_0_O7, MEMORY_CE, MEMORY_OE, MEMORY_WE, MicroCommandsCounter_n_Clear,
       MicroCommandsCounter_n_Enable_Counter, MicroCommandsCounter_n_Enable_Load, n7408_3_pin9,
       n7408_3_pin10, n7408_3_pin12, n7408_3_pin13, n7427_2_pin8, n7427_2_pin9, n7427_2_pin10, n7427_2_pin11,
       n7432_2_pin9, n7432_2_pin10, n7486_1_pin9, n7486_1_pin10, n7486_1_pin12, n7486_1_pin13, n74138_1_pin6,
       n74138_1_pin15, n74138_2_pin4, n74138_2_pin5, n74138_2_pin6, n74139_1_pin4, n74139_1_pin9,
       n74139_1_pin10, n74139_1_pin11, n74139_1_pin12, n74139_1_pin13, n74139_1_pin14, n74139_1_pin15,
       n74244_6_pin17, n74244_9_pin3, n74244_9_pin5, n74244_9_pin7, n74244_9_pin8, n74244_9_pin9,
       n74244_9_pin11, n74244_9_pin12, n74244_9_pin13, n74244_9_pin15, n74244_9_pin17, n74244_12_pin7,
       n74244_12_pin9, n74244_12_pin11, n74244_12_pin12, n74244_12_pin13, n74244_12_pin15, n74244_12_pin17,
       n74244_15_pin7, n74244_15_pin9, n74244_15_pin11, n74244_15_pin12, n74244_15_pin13, n74244_15_pin15,
       n74244_15_pin17, n74283_1_pin9, n74377_4_pin9, n74377_4_pin12, n74377_4_pin15, n74377_4_pin16,
       n74377_4_pin19, n74377_7_pin9, n74377_7_pin12, n74377_7_pin15, n74377_7_pin16, n74377_7_pin19,
       n74377_11_pin9, n74377_11_pin12, n74377_11_pin15, n74377_11_pin16, n74377_11_pin19, n74377_13_pin9,
       n74377_13_pin12, n74377_13_pin13, n74377_13_pin14, n74377_13_pin15, n74377_13_pin16, n74377_13_pin17,
       n74377_13_pin18, n74377_13_pin19, n_ALU_AND_EN, n_ALU_NOT_EN, n_ALU_OR_EN, n_ALU_SHL_EN, n_ALU_SHR_EN,
       n_ALU_SUM_EN, n_ALU_XOR_EN, n_B13, n_Clock, N_OUT_0_OUT_1_OUT_2, N_OUT_3_OUT_4_OUT_5, n_R_INNER_REG,
       n_R_UREG_0, n_R_UREG_1, n_R_UREG_2, n_REG_A_EN, n_REG_B_EN, n_W_INNER_REG, n_W_UREG_0, n_W_UREG_1,
       n_W_UREG_2, NEGATIVE, not_1_out, not_2_out, not_3_out, not_4_out, NOT_OR_OR, OpcodeRegister_n_EN1,
       OpcodeRegister_n_EN2, OpcodeRegister_n_EN_Out, OUT_0_OUT_1_OUT_2, OUT_3_OUT_4_OUT_5, OUT_6_OUT_7,
       OVERFLOW, pull_resistor_1_node, pull_resistor_2_node, pull_resistor_3_node, pull_resistor_4_node,
       pull_resistor_13_node, pull_resistor_14_node, pull_resistor_20_node, pull_resistor_21_node,
       pull_resistor_32_node, pull_resistor_33_node, pull_resistor_34_node, pull_resistor_39_node,
       pull_resistor_40_node, pull_resistor_41_node, pull_resistor_46_node, pull_resistor_47_node,
       pull_resistor_48_node, R_INNER_REG, R_REG_0, R_REG_1, R_REG_2, R_REG_3, R_REG_4, R_REG_5, R_REG_6,
       R_REG_7, R_UREG_0, R_UREG_1, R_UREG_2, RAM_CE, RAM_EN, RAM_OE, RAM_WE, REG_0, REG_0_O0, REG_0_O1,
       REG_0_O2, REG_0_O3, REG_0_O4, REG_0_O5, REG_0_O6, REG_0_O7, REG_1, REG_1_O0, REG_1_O1, REG_1_O2,
       REG_1_O3, REG_1_O4, REG_1_O5, REG_1_O6, REG_1_O7, REG_2, REG_2_O0, REG_2_O1, REG_2_O2, REG_2_O3,
       REG_2_O4, REG_2_O5, REG_2_O6, REG_2_O7, REG_3, REG_3_O0, REG_3_O1, REG_3_O2, REG_3_O3, REG_3_O4,
       REG_3_O5, REG_3_O6, REG_3_O7, REG_4, REG_4_O0, REG_4_O1, REG_4_O2, REG_4_O3, REG_4_O4, REG_4_O5,
       REG_4_O6, REG_4_O7, REG_5, REG_5_O0, REG_5_O1, REG_5_O2, REG_5_O3, REG_5_O4, REG_5_O5, REG_5_O6,
       REG_5_O7, REG_6, REG_6_O0, REG_6_O1, REG_6_O2, REG_6_O3, REG_6_O4, REG_6_O5, REG_6_O6, REG_6_O7,
       REG_7, REG_7_O0, REG_7_O1, REG_7_O2, REG_7_O3, REG_7_O4, REG_7_O5, REG_7_O6, REG_7_O7, REG_A_0,
       REG_A_1, REG_A_2, REG_A_3, REG_A_4, REG_A_5, REG_A_6, REG_A_7, REG_A_EN, REG_B_0, REG_B_1, REG_B_2,
       REG_B_3, REG_B_4, REG_B_5, REG_B_6, REG_B_7, REG_B_EN, REG_IM_0, REG_IM_1, REG_IM_2, REG_IM_3,
       REG_IM_4, REG_IM_5, REG_IM_6, REG_IM_7, ROM_EN, ROM_OE, SUM_OR_AND, SUM_OR_AND_OR_NOT_OR_OR,
       UREG_0_O0, UREG_0_O1, UREG_0_O2, UREG_1_O0, UREG_1_O1, UREG_1_O2, UREG_2_O0, UREG_2_O1, UREG_2_O2,
       URN_0, URN_1, URN_2, UserAddressRegister_n_EN1, UserAddressRegister_n_EN2,
       UserAddressRegister_n_EN_Out, UserRegistersBlock_READ, UserRegistersBlock_WRITE, W_INNER_REG, W_REG_0,
       W_REG_1, W_REG_2, W_REG_3, W_REG_4, W_REG_5, W_REG_6, W_REG_7, W_REG_IM_0, W_REG_IM_1, W_REG_IM_2,
       W_REG_IM_3, W_REG_IM_4, W_REG_IM_5, W_REG_IM_6, W_REG_IM_7, W_UREG_0, W_UREG_1, W_UREG_2, XOR_OR_SHL,
       XOR_OR_SHL_OR_SHR, ZERO;
  wire [2:0] ALU_MODE;
  wire [6:0] DATA_BUS;
  wire [15:0] counter16bits_1_counter_output, MicroCommandAddress, OpcodeRegister_out1,
       UserAddressRegister_out1;
  wire [18:0] FLASH_MEMORY_ADDRESS_BUS;

  // Probe on {ALU_NEGATIVE_FLAG, DATA_BUS}
  Clock clock_1 (.out(O_Clock));
  _74377 #(.ShowInternalStructure("true")) REG_A (
    .pin1(n_REG_A_EN), .pin2(REG_A_0), .pin3(DATA_BUS[0]), .pin4(DATA_BUS[1]), .pin5(REG_A_1),
    .pin6(REG_A_2), .pin7(DATA_BUS[2]), .pin8(DATA_BUS[3]), .pin9(REG_A_3), .pin19(REG_A_7),
    .pin18(ALU_NEGATIVE_FLAG), .pin17(DATA_BUS[6]), .pin16(REG_A_6), .pin15(REG_A_5), .pin14(DATA_BUS[5]),
    .pin13(DATA_BUS[4]), .pin12(REG_A_4), .pin11(O_Clock));
  _7408 #(.ShowInternalStructure("true")) u_7408_1 (
    .pin1(REG_A_0), .pin2(REG_B_0), .pin3(ALU_AND_OUT_0), .pin4(REG_A_1), .pin5(REG_B_1),
    .pin6(ALU_AND_OUT_1), .pin13(REG_A_3), .pin12(REG_B_3), .pin11(ALU_AND_OUT_3), .pin10(REG_A_2),
    .pin9(REG_B_2), .pin8(ALU_AND_OUT_2));
  _74244 #(.ShowInternalStructure("true")) u_74244_1 (
    .pin1(ALU_AND_EN), .pin2(ALU_AND_OUT_0), .pin3(ALU_NEGATIVE_FLAG), .pin4(ALU_AND_OUT_1),
    .pin5(DATA_BUS[6]), .pin6(ALU_AND_OUT_2), .pin7(DATA_BUS[5]), .pin8(ALU_AND_OUT_3), .pin9(DATA_BUS[4]),
    .pin19(ALU_AND_EN), .pin18(DATA_BUS[0]), .pin17(ALU_AND_OUT_7), .pin16(DATA_BUS[1]),
    .pin15(ALU_AND_OUT_6), .pin14(DATA_BUS[2]), .pin13(ALU_AND_OUT_5), .pin12(DATA_BUS[3]),
    .pin11(ALU_AND_OUT_4));
  _74240 #(.ShowInternalStructure("true")) u_74240_1 (
    .pin1(ALU_NOT_EN), .pin2(REG_A_0), .pin3(ALU_NEGATIVE_FLAG), .pin4(REG_A_1), .pin5(DATA_BUS[6]),
    .pin6(REG_A_2), .pin7(DATA_BUS[5]), .pin8(REG_A_3), .pin9(DATA_BUS[4]), .pin19(ALU_NOT_EN),
    .pin18(DATA_BUS[0]), .pin17(REG_A_7), .pin16(DATA_BUS[1]), .pin15(REG_A_6), .pin14(DATA_BUS[2]),
    .pin13(REG_A_5), .pin12(DATA_BUS[3]), .pin11(REG_A_4));
  CU cu_1 (
    .MicroCommandAddress(MicroCommandAddress), .ZERO(ZERO), .OVERFLOW(OVERFLOW), .NEGATIVE(NEGATIVE),
    .CARRY(CARRY), .OpcodeRegister_n_EN1(OpcodeRegister_n_EN1), .OpcodeRegister_n_EN2(OpcodeRegister_n_EN2),
    .OpcodeRegister_n_EN_Out(OpcodeRegister_n_EN_Out), .UserAddressRegister_n_EN1(UserAddressRegister_n_EN1),
    .UserAddressRegister_n_EN2(UserAddressRegister_n_EN2),
    .UserAddressRegister_n_EN_Out(UserAddressRegister_n_EN_Out),
    .CurrentAddressRegister_n_EN1(CurrentAddressRegister_n_EN1),
    .CurrentAddressRegister_n_EN2(CurrentAddressRegister_n_EN2),
    .CurrentAddressRegister_n_EN_Out(CurrentAddressRegister_n_EN_Out),
    .MicroCommandsCounter_n_Enable_Counter(MicroCommandsCounter_n_Enable_Counter),
    .MicroCommandsCounter_n_Clear(MicroCommandsCounter_n_Clear),
    .MicroCommandsCounter_n_Enable_Load(MicroCommandsCounter_n_Enable_Load),
    .CommandsCounter_n_Enable_Counter(CommandsCounter_n_Enable_Counter),
    .CommandsCounter_n_Clear(CommandsCounter_n_Clear),
    .CommandsCounter_n_Enable_Load(CommandsCounter_n_Enable_Load),
    .UserRegistersBlock_READ(UserRegistersBlock_READ), .UserRegistersBlock_WRITE(UserRegistersBlock_WRITE),
    .W_UREG_0(W_UREG_0), .W_UREG_1(W_UREG_1), .W_UREG_2(W_UREG_2), .R_UREG_0(R_UREG_0), .R_UREG_1(R_UREG_1),
    .R_UREG_2(R_UREG_2), .W_INNER_REG(W_INNER_REG), .R_INNER_REG(R_INNER_REG), .MEMORY_WE(MEMORY_WE),
    .MEMORY_OE(MEMORY_OE), .MEMORY_CE(MEMORY_CE), .FLASH_WE(FLASH_WE), .FLASH_OE(FLASH_OE),
    .FLASH_CE(FLASH_CE), .FM_ADDRESS_REGISTER_SELECT_0(FM_ADDRESS_REGISTER_SELECT_0),
    .FM_ADDRESS_REGISTER_SELECT_1(FM_ADDRESS_REGISTER_SELECT_1), .REG_A_EN(REG_A_EN), .REG_B_EN(REG_B_EN),
    .ALU_MODE(ALU_MODE));
  _74377 #(.ShowInternalStructure("true")) u_74377_1 (
    .pin1(n_REG_B_EN), .pin2(REG_B_0), .pin3(DATA_BUS[0]), .pin4(DATA_BUS[1]), .pin5(REG_B_1),
    .pin6(REG_B_2), .pin7(DATA_BUS[2]), .pin8(DATA_BUS[3]), .pin9(REG_B_3), .pin19(REG_B_7),
    .pin18(ALU_NEGATIVE_FLAG), .pin17(DATA_BUS[6]), .pin16(REG_B_6), .pin15(REG_B_5), .pin14(DATA_BUS[5]),
    .pin13(DATA_BUS[4]), .pin12(REG_B_4), .pin11(O_Clock));
  _7408 #(.ShowInternalStructure("true")) u_7408_2 (
    .pin1(REG_A_4), .pin2(REG_B_4), .pin3(ALU_AND_OUT_4), .pin4(REG_A_5), .pin5(REG_B_5),
    .pin6(ALU_AND_OUT_5), .pin13(REG_A_7), .pin12(REG_B_7), .pin11(ALU_AND_OUT_7), .pin10(REG_A_6),
    .pin9(REG_B_6), .pin8(ALU_AND_OUT_6));
  _74175 #(.ShowInternalStructure("true")) FLAGS_REGISTER (
    .pin1(FLAGS_REGISTER_pin1), .pin2(NEGATIVE), .pin4(ALU_NEGATIVE_FLAG), .pin5(ALU_SUM_CARRY_FLAG),
    .pin7(CARRY), .pin15(ZERO), .pin13(ALU_ZERO_FLAG), .pin12(ALU_OVERFLOW_FLAG), .pin10(OVERFLOW),
    .pin9(FLAGS_Clock));  // open: pin3, pin6, pin14, pin11
  Pull_Resistor pull_resistor_1 (.node(pull_resistor_1_node));
  Pull_Resistor pull_resistor_2 (.node(pull_resistor_2_node));
  Pull_Resistor pull_resistor_3 (.node(pull_resistor_3_node));
  Pull_Resistor pull_resistor_4 (.node(pull_resistor_4_node));
  _7427 #(.ShowInternalStructure("true")) u_7427_1 (
    .pin1(DATA_BUS[0]), .pin2(DATA_BUS[1]), .pin3(DATA_BUS[3]), .pin4(DATA_BUS[4]), .pin5(DATA_BUS[5]),
    .pin6(OUT_3_OUT_4_OUT_5), .pin13(DATA_BUS[2]), .pin12(OUT_0_OUT_1_OUT_2), .pin11(N_OUT_0_OUT_1_OUT_2),
    .pin10(N_OUT_3_OUT_4_OUT_5), .pin9(OUT_6_OUT_7), .pin8(ALU_ZERO_FLAG));
  _7432 #(.ShowInternalStructure("true")) u_7432_1 (
    .pin1(DATA_BUS[6]), .pin2(ALU_NEGATIVE_FLAG), .pin3(OUT_6_OUT_7), .pin4(n_ALU_SUM_EN),
    .pin5(n_ALU_AND_EN), .pin6(SUM_OR_AND), .pin13(n_ALU_NOT_EN), .pin12(n_ALU_OR_EN), .pin11(NOT_OR_OR),
    .pin10(n_ALU_XOR_EN), .pin9(n_ALU_SHL_EN), .pin8(XOR_OR_SHL));
  _7486 #(.ShowInternalStructure("true")) u_7486_1 (
    .pin1(ALU_SUM_CARRY_FLAG), .pin2(ALU_NEGATIVE_FLAG), .pin3(ALU_OVERFLOW_FLAG),
    .pin4(pull_resistor_1_node), .pin5(pull_resistor_2_node), .pin13(n7486_1_pin13), .pin12(n7486_1_pin12),
    .pin10(n7486_1_pin10), .pin9(n7486_1_pin9));  // open: pin6, pin11, pin8
  _7408 #(.ShowInternalStructure("true")) u_7408_3 (
    .pin1(O_Clock), .pin2(EN_WRITE_FLAGS), .pin3(FLAGS_Clock), .pin4(pull_resistor_3_node),
    .pin5(pull_resistor_4_node), .pin13(n7408_3_pin13), .pin12(n7408_3_pin12), .pin10(n7408_3_pin10),
    .pin9(n7408_3_pin9));  // open: pin6, pin11, pin8
  Pull_Resistor pull_resistor_5 (.node(n7408_3_pin13));
  Pull_Resistor pull_resistor_6 (.node(n7408_3_pin12));
  Pull_Resistor pull_resistor_7 (.node(n7408_3_pin10));
  Pull_Resistor pull_resistor_8 (.node(n7408_3_pin9));
  Pull_Resistor pull_resistor_9 (.node(n7486_1_pin13));
  Pull_Resistor pull_resistor_10 (.node(n7486_1_pin12));
  Pull_Resistor pull_resistor_11 (.node(n7486_1_pin10));
  Pull_Resistor pull_resistor_12 (.node(n7486_1_pin9));
  _7419 #(.ShowInternalStructure("true")) u_7419_1 (
    .pin1(O_Clock), .pin2(n_Clock), .pin3(AddressMemory[13]), .pin4(n_B13), .pin5(REG_A_EN),
    .pin6(n_REG_A_EN), .pin13(REG_B_EN), .pin12(n_REG_B_EN), .pin11(OUT_0_OUT_1_OUT_2),
    .pin10(N_OUT_0_OUT_1_OUT_2), .pin9(OUT_3_OUT_4_OUT_5), .pin8(N_OUT_3_OUT_4_OUT_5));
  _7419 #(.ShowInternalStructure("true")) u_7419_2 (
    .pin1(W_INNER_REG), .pin2(n_W_INNER_REG), .pin3(R_INNER_REG), .pin4(n_R_INNER_REG));  // open: pin5, pin6, pin13, pin12, pin11, pin10, pin9, pin8
  _7486 #(.ShowInternalStructure("true")) u_7486_2 (
    .pin1(REG_A_0), .pin2(REG_B_0), .pin3(ALU_XOR_OUT_0), .pin4(REG_A_1), .pin5(REG_B_1),
    .pin6(ALU_XOR_OUT_1), .pin13(REG_A_3), .pin12(REG_B_3), .pin11(ALU_XOR_OUT_3), .pin10(REG_A_2),
    .pin9(REG_B_2), .pin8(ALU_XOR_OUT_2));
  Pull_Resistor pull_resistor_13 (.node(pull_resistor_13_node));
  Pull_Resistor pull_resistor_14 (.node(pull_resistor_14_node));
  _74283 #(.ShowInternalStructure("true")) u_74283_1 (
    .pin1(ALU_SUM_OUT_1), .pin2(REG_A_1), .pin3(REG_B_1), .pin4(ALU_SUM_OUT_0), .pin5(REG_A_0),
    .pin6(REG_B_0), .pin15(REG_A_2), .pin14(REG_B_2), .pin13(ALU_SUM_OUT_2), .pin12(REG_A_3),
    .pin11(REG_B_3), .pin10(ALU_SUM_OUT_3), .pin9(n74283_1_pin9));  // open: pin7
  _74138 #(.ShowInternalStructure("true")) u_74138_1 (
    .pin1(ALU_MODE[0]), .pin2(ALU_MODE[1]), .pin3(ALU_MODE[2]), .pin4(pull_resistor_13_node),
    .pin5(pull_resistor_14_node), .pin6(n74138_1_pin6), .pin7(ALU_SHR_EN), .pin15(n74138_1_pin15),
    .pin14(ALU_SUM_EN), .pin13(ALU_AND_EN), .pin12(ALU_OR_EN), .pin11(ALU_NOT_EN), .pin10(ALU_XOR_EN),
    .pin9(ALU_SHL_EN));
  _74244 #(.ShowInternalStructure("true")) u_74244_2 (
    .pin1(ALU_SUM_EN), .pin2(ALU_SUM_OUT_0), .pin3(ALU_NEGATIVE_FLAG), .pin4(ALU_SUM_OUT_1),
    .pin5(DATA_BUS[6]), .pin6(ALU_SUM_OUT_2), .pin7(DATA_BUS[5]), .pin8(ALU_SUM_OUT_3), .pin9(DATA_BUS[4]),
    .pin19(ALU_SUM_EN), .pin18(DATA_BUS[0]), .pin17(ALU_SUM_OUT_7), .pin16(DATA_BUS[1]),
    .pin15(ALU_SUM_OUT_6), .pin14(DATA_BUS[2]), .pin13(ALU_SUM_OUT_5), .pin12(DATA_BUS[3]),
    .pin11(ALU_SUM_OUT_4));
  _74244 #(.ShowInternalStructure("true")) u_74244_3 (
    .pin1(ALU_XOR_EN), .pin2(ALU_XOR_OUT_0), .pin3(ALU_NEGATIVE_FLAG), .pin4(ALU_XOR_OUT_1),
    .pin5(DATA_BUS[6]), .pin6(ALU_XOR_OUT_2), .pin7(DATA_BUS[5]), .pin8(ALU_XOR_OUT_3), .pin9(DATA_BUS[4]),
    .pin19(ALU_XOR_EN), .pin18(DATA_BUS[0]), .pin17(ALU_XOR_OUT_7), .pin16(DATA_BUS[1]),
    .pin15(ALU_XOR_OUT_6), .pin14(DATA_BUS[2]), .pin13(ALU_XOR_OUT_5), .pin12(DATA_BUS[3]),
    .pin11(ALU_XOR_OUT_4));
  _7432 #(.ShowInternalStructure("true")) u_7432_2 (
    .pin1(SUM_OR_AND), .pin2(NOT_OR_OR), .pin3(SUM_OR_AND_OR_NOT_OR_OR), .pin4(XOR_OR_SHL),
    .pin5(n_ALU_SHR_EN), .pin6(XOR_OR_SHL_OR_SHR), .pin13(SUM_OR_AND_OR_NOT_OR_OR),
    .pin12(XOR_OR_SHL_OR_SHR), .pin11(EN_WRITE_FLAGS), .pin10(n7432_2_pin10), .pin9(n7432_2_pin9));  // open: pin8
  Pull_Resistor pull_resistor_15 (.node(n7432_2_pin10));
  Pull_Resistor pull_resistor_16 (.node(n7432_2_pin9));
  _7419 #(.ShowInternalStructure("true")) u_7419_3 (
    .pin1(ALU_SUM_EN), .pin2(n_ALU_SUM_EN), .pin3(ALU_AND_EN), .pin4(n_ALU_AND_EN), .pin5(ALU_OR_EN),
    .pin6(n_ALU_OR_EN), .pin13(ALU_NOT_EN), .pin12(n_ALU_NOT_EN), .pin11(ALU_XOR_EN), .pin10(n_ALU_XOR_EN),
    .pin9(ALU_SHL_EN), .pin8(n_ALU_SHL_EN));
  _7419 #(.ShowInternalStructure("true")) u_7419_4 (
    .pin1(ALU_SHR_EN), .pin2(n_ALU_SHR_EN));  // open: pin3, pin4, pin5, pin6, pin13, pin12, pin11, pin10, pin9, pin8
  _7427 #(.ShowInternalStructure("true")) u_7427_2 (
    .pin1(AddressMemory[14]), .pin2(AddressMemory[13]), .pin3(n_B13), .pin4(AddressMemory[14]),
    .pin5(AddressMemory[15]), .pin6(RAM_EN), .pin13(AddressMemory[15]), .pin12(ROM_EN),
    .pin11(n7427_2_pin11), .pin10(n7427_2_pin10), .pin9(n7427_2_pin9), .pin8(n7427_2_pin8));
  _7400 #(.ShowInternalStructure("true")) u_7400_1 (
    .pin1(ROM_EN), .pin2(MEMORY_OE), .pin3(ROM_OE), .pin4(RAM_EN), .pin5(MEMORY_OE), .pin6(RAM_OE),
    .pin13(RAM_EN), .pin12(MEMORY_WE), .pin11(RAM_WE), .pin10(RAM_EN), .pin9(MEMORY_CE), .pin8(RAM_CE));
  // NoConnect on n74138_1_pin15
  Pull_Resistor pull_resistor_17 (.node(n7427_2_pin11));
  Pull_Resistor pull_resistor_18 (.node(n7427_2_pin10));
  Pull_Resistor pull_resistor_19 (.node(n7427_2_pin9));
  // NoConnect on n7427_2_pin8
  _74283 #(.ShowInternalStructure("true")) u_74283_2 (
    .pin1(ALU_SUM_OUT_5), .pin2(REG_A_5), .pin3(REG_B_5), .pin4(ALU_SUM_OUT_4), .pin5(REG_A_4),
    .pin6(REG_B_4), .pin7(n74283_1_pin9), .pin15(REG_A_6), .pin14(REG_B_6), .pin13(ALU_SUM_OUT_6),
    .pin12(REG_A_7), .pin11(REG_B_7), .pin10(ALU_SUM_OUT_7), .pin9(ALU_SUM_CARRY_FLAG));
  _7486 #(.ShowInternalStructure("true")) u_7486_3 (
    .pin1(REG_A_4), .pin2(REG_B_4), .pin3(ALU_XOR_OUT_4), .pin4(REG_A_5), .pin5(REG_B_5),
    .pin6(ALU_XOR_OUT_5), .pin13(REG_A_7), .pin12(REG_B_7), .pin11(ALU_XOR_OUT_7), .pin10(REG_A_6),
    .pin9(REG_B_6), .pin8(ALU_XOR_OUT_6));
  Pull_Resistor pull_resistor_20 (.node(pull_resistor_20_node));
  not not_1 (not_1_out, ROM_OE);
  not not_2 (not_2_out, 1'b1);
  Pull_Resistor pull_resistor_21 (.node(pull_resistor_21_node));
  RAM #(.addrWidth(13), .databus("bidir"), .enables("line"), .trigger("low")) ROM_AT28C64B (
    .addr(AddressMemory[12:0]), .we(not_2_out), .oe(not_1_out), .clk(pull_resistor_20_node),
    .data({ALU_NEGATIVE_FLAG, DATA_BUS}));
  _7432 #(.ShowInternalStructure("true")) u_7432_3 (
    .pin1(REG_A_0), .pin2(REG_B_0), .pin3(ALU_OR_OUT_0), .pin4(REG_A_1), .pin5(REG_B_1), .pin6(ALU_OR_OUT_1),
    .pin13(REG_A_3), .pin12(REG_B_3), .pin11(ALU_OR_OUT_3), .pin10(REG_A_2), .pin9(REG_B_2),
    .pin8(ALU_OR_OUT_2));
  _74244 #(.ShowInternalStructure("true")) u_74244_4 (
    .pin1(ALU_SHL_EN), .pin2(pull_resistor_21_node), .pin3(ALU_NEGATIVE_FLAG), .pin4(REG_A_0),
    .pin5(DATA_BUS[6]), .pin6(REG_A_1), .pin7(DATA_BUS[5]), .pin8(REG_A_2), .pin9(DATA_BUS[4]),
    .pin19(ALU_SHL_EN), .pin18(DATA_BUS[0]), .pin17(REG_A_6), .pin16(DATA_BUS[1]), .pin15(REG_A_5),
    .pin14(DATA_BUS[2]), .pin13(REG_A_4), .pin12(DATA_BUS[3]), .pin11(REG_A_3));
  _74244 #(.ShowInternalStructure("true")) u_74244_5 (
    .pin1(ALU_OR_EN), .pin2(ALU_OR_OUT_0), .pin3(ALU_NEGATIVE_FLAG), .pin4(ALU_OR_OUT_1), .pin5(DATA_BUS[6]),
    .pin6(ALU_OR_OUT_2), .pin7(DATA_BUS[5]), .pin8(ALU_OR_OUT_3), .pin9(DATA_BUS[4]), .pin19(ALU_OR_EN),
    .pin18(DATA_BUS[0]), .pin17(ALU_OR_OUT_7), .pin16(DATA_BUS[1]), .pin15(ALU_OR_OUT_6),
    .pin14(DATA_BUS[2]), .pin13(ALU_OR_OUT_5), .pin12(DATA_BUS[3]), .pin11(ALU_OR_OUT_4));
  _7432 #(.ShowInternalStructure("true")) u_7432_4 (
    .pin1(REG_A_4), .pin2(REG_B_4), .pin3(ALU_OR_OUT_4), .pin4(REG_A_5), .pin5(REG_B_5), .pin6(ALU_OR_OUT_5),
    .pin13(REG_A_7), .pin12(REG_B_7), .pin11(ALU_OR_OUT_7), .pin10(REG_A_6), .pin9(REG_B_6),
    .pin8(ALU_OR_OUT_6));
  _74244 #(.ShowInternalStructure("true")) u_74244_6 (
    .pin1(ALU_SHR_EN), .pin2(REG_A_1), .pin3(ALU_NEGATIVE_FLAG), .pin4(REG_A_2), .pin5(DATA_BUS[6]),
    .pin6(REG_A_3), .pin7(DATA_BUS[5]), .pin8(REG_A_4), .pin9(DATA_BUS[4]), .pin19(ALU_SHR_EN),
    .pin18(DATA_BUS[0]), .pin17(n74244_6_pin17), .pin16(DATA_BUS[1]), .pin15(REG_A_7), .pin14(DATA_BUS[2]),
    .pin13(REG_A_6), .pin12(DATA_BUS[3]), .pin11(REG_A_5));
  Pull_Resistor pull_resistor_22 (.node(n74244_6_pin17));
  not not_3 (not_3_out, RAM_OE);
  not not_4 (not_4_out, RAM_WE);
  RAM #(.addrWidth(15), .databus("bidir"), .enables("line"), .trigger("low")) SRAM_AS6C62256 (
    .addr(AddressMemory[14:0]), .we(not_4_out), .oe(not_3_out), .clk(RAM_CE),
    .data({ALU_NEGATIVE_FLAG, DATA_BUS}));
  Counter16bits counter16bits_1 (
    .n_Clear(in_2), .C_Clock(in_3), .n_Enable_Load(in_4), .DI(in_5), .n_Enable_Count(in_1),
    .Counter_Output(counter16bits_1_counter_output));
  Register16bits OpcodeRegister (
    .Clock(O_Clock), .n_EN_1(OpcodeRegister_n_EN1), .n_EN_2(OpcodeRegister_n_EN2),
    .n_EN_Out(OpcodeRegister_n_EN_Out), .IN2({ALU_NEGATIVE_FLAG, DATA_BUS}),
    .IN1({ALU_NEGATIVE_FLAG, DATA_BUS}), .OUT1(OpcodeRegister_out1));
  // NoConnect on n74377_4_pin9
  // Probe on counter16bits_1_counter_output
  // Probe on OpcodeRegister_out1
  _74138 #(.ShowInternalStructure("true")) u_74138_2 (
    .pin1(URN_0), .pin2(URN_1), .pin3(URN_2), .pin4(n74138_2_pin4), .pin5(n74138_2_pin5),
    .pin6(n74138_2_pin6), .pin7(REG_7), .pin15(REG_0), .pin14(REG_1), .pin13(REG_2), .pin12(REG_3),
    .pin11(REG_4), .pin10(REG_5), .pin9(REG_6));
  Pull_Resistor pull_resistor_23 (.node(n74138_2_pin4));
  Pull_Resistor pull_resistor_24 (.node(n74138_2_pin5));
  _74377 #(.ShowInternalStructure("true")) u_74377_2 (
    .pin1(W_REG_0), .pin2(REG_0_O0), .pin3(DATA_BUS[0]), .pin4(DATA_BUS[1]), .pin5(REG_0_O1),
    .pin6(REG_0_O2), .pin7(DATA_BUS[2]), .pin8(DATA_BUS[3]), .pin9(REG_0_O3), .pin19(REG_0_O7),
    .pin18(ALU_NEGATIVE_FLAG), .pin17(DATA_BUS[6]), .pin16(REG_0_O6), .pin15(REG_0_O5), .pin14(DATA_BUS[5]),
    .pin13(DATA_BUS[4]), .pin12(REG_0_O4), .pin11(O_Clock));
  _74244 #(.ShowInternalStructure("true")) u_74244_7 (
    .pin1(R_REG_0), .pin2(REG_0_O0), .pin3(ALU_NEGATIVE_FLAG), .pin4(REG_0_O1), .pin5(DATA_BUS[6]),
    .pin6(REG_0_O2), .pin7(DATA_BUS[5]), .pin8(REG_0_O3), .pin9(DATA_BUS[4]), .pin19(R_REG_0),
    .pin18(DATA_BUS[0]), .pin17(REG_0_O7), .pin16(DATA_BUS[1]), .pin15(REG_0_O6), .pin14(DATA_BUS[2]),
    .pin13(REG_0_O5), .pin12(DATA_BUS[3]), .pin11(REG_0_O4));
  _74377 #(.ShowInternalStructure("true")) u_74377_3 (
    .pin1(W_REG_4), .pin2(REG_4_O0), .pin3(DATA_BUS[0]), .pin4(DATA_BUS[1]), .pin5(REG_4_O1),
    .pin6(REG_4_O2), .pin7(DATA_BUS[2]), .pin8(DATA_BUS[3]), .pin9(REG_4_O3), .pin19(REG_4_O7),
    .pin18(ALU_NEGATIVE_FLAG), .pin17(DATA_BUS[6]), .pin16(REG_4_O6), .pin15(REG_4_O5), .pin14(DATA_BUS[5]),
    .pin13(DATA_BUS[4]), .pin12(REG_4_O4), .pin11(O_Clock));
  _74244 #(.ShowInternalStructure("true")) u_74244_8 (
    .pin1(R_REG_4), .pin2(REG_4_O0), .pin3(ALU_NEGATIVE_FLAG), .pin4(REG_4_O1), .pin5(DATA_BUS[6]),
    .pin6(REG_4_O2), .pin7(DATA_BUS[5]), .pin8(REG_4_O3), .pin9(DATA_BUS[4]), .pin19(R_REG_4),
    .pin18(DATA_BUS[0]), .pin17(REG_4_O7), .pin16(DATA_BUS[1]), .pin15(REG_4_O6), .pin14(DATA_BUS[2]),
    .pin13(REG_4_O5), .pin12(DATA_BUS[3]), .pin11(REG_4_O4));
  _74377 #(.ShowInternalStructure("true")) u_74377_4 (
    .pin1(n_W_UREG_0), .pin2(UREG_0_O0), .pin3(DATA_BUS[0]), .pin4(DATA_BUS[1]), .pin5(UREG_0_O1),
    .pin6(UREG_0_O2), .pin7(DATA_BUS[2]), .pin8(DATA_BUS[3]), .pin9(n74377_4_pin9), .pin19(n74377_4_pin19),
    .pin18(ALU_NEGATIVE_FLAG), .pin17(DATA_BUS[6]), .pin16(n74377_4_pin16), .pin15(n74377_4_pin15),
    .pin14(DATA_BUS[5]), .pin13(DATA_BUS[4]), .pin12(n74377_4_pin12), .pin11(O_Clock));
  _74244 #(.ShowInternalStructure("true")) u_74244_9 (
    .pin1(n_R_UREG_0), .pin2(UREG_0_O0), .pin3(n74244_9_pin3), .pin4(UREG_0_O1), .pin5(n74244_9_pin5),
    .pin6(UREG_0_O2), .pin7(n74244_9_pin7), .pin8(n74244_9_pin8), .pin9(n74244_9_pin9), .pin19(R_UREG_0),
    .pin18(URN_0), .pin17(n74244_9_pin17), .pin16(URN_1), .pin15(n74244_9_pin15), .pin14(URN_2),
    .pin13(n74244_9_pin13), .pin12(n74244_9_pin12), .pin11(n74244_9_pin11));
  Pull_Resistor pull_resistor_25 (.node(n74244_9_pin3));
  Pull_Resistor pull_resistor_26 (.node(n74244_9_pin5));
  // NoConnect on n74244_9_pin7
  Pull_Resistor pull_resistor_27 (.node(n74244_9_pin8));
  // NoConnect on n74244_9_pin9
  // Probe on MicroCommandAddress
  // NoConnect on n74377_4_pin19
  // NoConnect on n74377_4_pin16
  // NoConnect on n74377_4_pin15
  // NoConnect on n74377_4_pin12
  Pull_Resistor pull_resistor_28 (.node(n74244_9_pin17));
  Pull_Resistor pull_resistor_29 (.node(n74244_9_pin15));
  Pull_Resistor pull_resistor_30 (.node(n74244_9_pin13));
  // NoConnect on n74244_9_pin12
  Pull_Resistor pull_resistor_31 (.node(n74244_9_pin11));
  Counter16bits MicroCommands (
    .n_Clear(MicroCommandsCounter_n_Clear), .C_Clock(n_Clock),
    .n_Enable_Load(MicroCommandsCounter_n_Enable_Load), .DI(OpcodeRegister_out1),
    .n_Enable_Count(MicroCommandsCounter_n_Enable_Counter), .Counter_Output(MicroCommandAddress));
  // NoConnect on n74377_7_pin9
  Pull_Resistor pull_resistor_32 (.node(pull_resistor_32_node));
  Pull_Resistor pull_resistor_33 (.node(pull_resistor_33_node));
  // NoConnect on n74244_12_pin7
  Pull_Resistor pull_resistor_34 (.node(pull_resistor_34_node));
  // NoConnect on n74244_12_pin9
  RAM #(.addrWidth(19), .databus("bidir"), .enables("line"), .trigger("low")) FLASH (
    .addr(FLASH_MEMORY_ADDRESS_BUS), .we(FLASH_WE), .oe(FLASH_OE), .clk(FLASH_CE),
    .data({ALU_NEGATIVE_FLAG, DATA_BUS}));
  _74377 #(.ShowInternalStructure("true")) u_74377_5 (
    .pin1(W_REG_1), .pin2(REG_1_O0), .pin3(DATA_BUS[0]), .pin4(DATA_BUS[1]), .pin5(REG_1_O1),
    .pin6(REG_1_O2), .pin7(DATA_BUS[2]), .pin8(DATA_BUS[3]), .pin9(REG_1_O3), .pin19(REG_1_O7),
    .pin18(ALU_NEGATIVE_FLAG), .pin17(DATA_BUS[6]), .pin16(REG_1_O6), .pin15(REG_1_O5), .pin14(DATA_BUS[5]),
    .pin13(DATA_BUS[4]), .pin12(REG_1_O4), .pin11(O_Clock));
  _74244 #(.ShowInternalStructure("true")) u_74244_10 (
    .pin1(R_REG_1), .pin2(REG_1_O0), .pin3(ALU_NEGATIVE_FLAG), .pin4(REG_1_O1), .pin5(DATA_BUS[6]),
    .pin6(REG_1_O2), .pin7(DATA_BUS[5]), .pin8(REG_1_O3), .pin9(DATA_BUS[4]), .pin19(R_REG_1),
    .pin18(DATA_BUS[0]), .pin17(REG_1_O7), .pin16(DATA_BUS[1]), .pin15(REG_1_O6), .pin14(DATA_BUS[2]),
    .pin13(REG_1_O5), .pin12(DATA_BUS[3]), .pin11(REG_1_O4));
  _74377 #(.ShowInternalStructure("true")) u_74377_6 (
    .pin1(W_REG_5), .pin2(REG_5_O0), .pin3(DATA_BUS[0]), .pin4(DATA_BUS[1]), .pin5(REG_5_O1),
    .pin6(REG_5_O2), .pin7(DATA_BUS[2]), .pin8(DATA_BUS[3]), .pin9(REG_5_O3), .pin19(REG_5_O7),
    .pin18(ALU_NEGATIVE_FLAG), .pin17(DATA_BUS[6]), .pin16(REG_5_O6), .pin15(REG_5_O5), .pin14(DATA_BUS[5]),
    .pin13(DATA_BUS[4]), .pin12(REG_5_O4), .pin11(O_Clock));
  _74244 #(.ShowInternalStructure("true")) u_74244_11 (
    .pin1(R_REG_5), .pin2(REG_5_O0), .pin3(ALU_NEGATIVE_FLAG), .pin4(REG_5_O1), .pin5(DATA_BUS[6]),
    .pin6(REG_5_O2), .pin7(DATA_BUS[5]), .pin8(REG_5_O3), .pin9(DATA_BUS[4]), .pin19(R_REG_5),
    .pin18(DATA_BUS[0]), .pin17(REG_5_O7), .pin16(DATA_BUS[1]), .pin15(REG_5_O6), .pin14(DATA_BUS[2]),
    .pin13(REG_5_O5), .pin12(DATA_BUS[3]), .pin11(REG_5_O4));
  _74377 #(.ShowInternalStructure("true")) u_74377_7 (
    .pin1(n_W_UREG_1), .pin2(UREG_1_O0), .pin3(DATA_BUS[0]), .pin4(DATA_BUS[1]), .pin5(UREG_1_O1),
    .pin6(UREG_1_O2), .pin7(DATA_BUS[2]), .pin8(DATA_BUS[3]), .pin9(n74377_7_pin9), .pin19(n74377_7_pin19),
    .pin18(ALU_NEGATIVE_FLAG), .pin17(DATA_BUS[6]), .pin16(n74377_7_pin16), .pin15(n74377_7_pin15),
    .pin14(DATA_BUS[5]), .pin13(DATA_BUS[4]), .pin12(n74377_7_pin12), .pin11(O_Clock));
  _74244 #(.ShowInternalStructure("true")) u_74244_12 (
    .pin1(n_R_UREG_1), .pin2(UREG_1_O0), .pin3(pull_resistor_32_node), .pin4(UREG_1_O1),
    .pin5(pull_resistor_33_node), .pin6(UREG_1_O2), .pin7(n74244_12_pin7), .pin8(pull_resistor_34_node),
    .pin9(n74244_12_pin9), .pin19(R_UREG_1), .pin18(URN_0), .pin17(n74244_12_pin17), .pin16(URN_1),
    .pin15(n74244_12_pin15), .pin14(URN_2), .pin13(n74244_12_pin13), .pin12(n74244_12_pin12),
    .pin11(n74244_12_pin11));
  _7436 #(.ShowInternalStructure("true")) u_7436_1 (
    .pin1(UserRegistersBlock_READ), .pin2(REG_0), .pin3(REG_IM_0), .pin4(UserRegistersBlock_READ),
    .pin5(REG_1), .pin6(REG_IM_1), .pin13(UserRegistersBlock_READ), .pin12(REG_3), .pin11(REG_IM_3),
    .pin10(UserRegistersBlock_READ), .pin9(REG_2), .pin8(REG_IM_2));
  _7432 #(.ShowInternalStructure("true")) u_7432_5 (
    .pin1(REG_IM_0), .pin2(REG_0), .pin3(R_REG_0), .pin4(REG_IM_1), .pin5(REG_1), .pin6(R_REG_1),
    .pin13(REG_IM_3), .pin12(REG_3), .pin11(R_REG_3), .pin10(REG_IM_2), .pin9(REG_2), .pin8(R_REG_2));
  _7436 #(.ShowInternalStructure("true")) u_7436_2 (
    .pin1(UserRegistersBlock_READ), .pin2(REG_4), .pin3(REG_IM_4), .pin4(UserRegistersBlock_READ),
    .pin5(REG_5), .pin6(REG_IM_5), .pin13(UserRegistersBlock_READ), .pin12(REG_7), .pin11(REG_IM_7),
    .pin10(UserRegistersBlock_READ), .pin9(REG_6), .pin8(REG_IM_6));
  _7432 #(.ShowInternalStructure("true")) u_7432_6 (
    .pin1(REG_IM_4), .pin2(REG_4), .pin3(R_REG_4), .pin4(REG_IM_5), .pin5(REG_5), .pin6(R_REG_5),
    .pin13(REG_IM_7), .pin12(REG_7), .pin11(R_REG_7), .pin10(REG_IM_6), .pin9(REG_6), .pin8(R_REG_6));
  // NoConnect on n74377_7_pin19
  // NoConnect on n74377_7_pin16
  // NoConnect on n74377_7_pin15
  // NoConnect on n74377_7_pin12
  Pull_Resistor pull_resistor_35 (.node(n74244_12_pin17));
  Pull_Resistor pull_resistor_36 (.node(n74244_12_pin15));
  Pull_Resistor pull_resistor_37 (.node(n74244_12_pin13));
  // NoConnect on n74244_12_pin12
  Pull_Resistor pull_resistor_38 (.node(n74244_12_pin11));
  _74377 #(.ShowInternalStructure("true")) u_74377_8 (
    .pin1(FM_REG_1), .pin2(FLASH_MEMORY_ADDRESS_BUS[0]), .pin3(DATA_BUS[0]), .pin4(DATA_BUS[1]),
    .pin5(FLASH_MEMORY_ADDRESS_BUS[1]), .pin6(FLASH_MEMORY_ADDRESS_BUS[2]), .pin7(DATA_BUS[2]),
    .pin8(DATA_BUS[3]), .pin9(FLASH_MEMORY_ADDRESS_BUS[3]), .pin19(FLASH_MEMORY_ADDRESS_BUS[7]),
    .pin18(ALU_NEGATIVE_FLAG), .pin17(DATA_BUS[6]), .pin16(FLASH_MEMORY_ADDRESS_BUS[6]),
    .pin15(FLASH_MEMORY_ADDRESS_BUS[5]), .pin14(DATA_BUS[5]), .pin13(DATA_BUS[4]),
    .pin12(FLASH_MEMORY_ADDRESS_BUS[4]), .pin11(O_Clock));
  Register16bits UserAddressRegister (
    .Clock(O_Clock), .n_EN_1(UserAddressRegister_n_EN1), .n_EN_2(UserAddressRegister_n_EN2),
    .n_EN_Out(UserAddressRegister_n_EN_Out), .IN2({ALU_NEGATIVE_FLAG, DATA_BUS}),
    .IN1({ALU_NEGATIVE_FLAG, DATA_BUS}), .OUT1(UserAddressRegister_out1));
  // NoConnect on n74377_11_pin9
  Pull_Resistor pull_resistor_39 (.node(pull_resistor_39_node));
  Pull_Resistor pull_resistor_40 (.node(pull_resistor_40_node));
  // NoConnect on n74244_15_pin7
  Pull_Resistor pull_resistor_41 (.node(pull_resistor_41_node));
  // NoConnect on n74244_15_pin9
  _74377 #(.ShowInternalStructure("true")) u_74377_9 (
    .pin1(W_REG_2), .pin2(REG_2_O0), .pin3(DATA_BUS[0]), .pin4(DATA_BUS[1]), .pin5(REG_2_O1),
    .pin6(REG_2_O2), .pin7(DATA_BUS[2]), .pin8(DATA_BUS[3]), .pin9(REG_2_O3), .pin19(REG_2_O7),
    .pin18(ALU_NEGATIVE_FLAG), .pin17(DATA_BUS[6]), .pin16(REG_2_O6), .pin15(REG_2_O5), .pin14(DATA_BUS[5]),
    .pin13(DATA_BUS[4]), .pin12(REG_2_O4), .pin11(O_Clock));
  _74244 #(.ShowInternalStructure("true")) u_74244_13 (
    .pin1(R_REG_2), .pin2(REG_2_O0), .pin3(ALU_NEGATIVE_FLAG), .pin4(REG_2_O1), .pin5(DATA_BUS[6]),
    .pin6(REG_2_O2), .pin7(DATA_BUS[5]), .pin8(REG_2_O3), .pin9(DATA_BUS[4]), .pin19(R_REG_2),
    .pin18(DATA_BUS[0]), .pin17(REG_2_O7), .pin16(DATA_BUS[1]), .pin15(REG_2_O6), .pin14(DATA_BUS[2]),
    .pin13(REG_2_O5), .pin12(DATA_BUS[3]), .pin11(REG_2_O4));
  _74377 #(.ShowInternalStructure("true")) u_74377_10 (
    .pin1(W_REG_6), .pin2(REG_6_O0), .pin3(DATA_BUS[0]), .pin4(DATA_BUS[1]), .pin5(REG_6_O1),
    .pin6(REG_6_O2), .pin7(DATA_BUS[2]), .pin8(DATA_BUS[3]), .pin9(REG_6_O3), .pin19(REG_6_O7),
    .pin18(ALU_NEGATIVE_FLAG), .pin17(DATA_BUS[6]), .pin16(REG_6_O6), .pin15(REG_6_O5), .pin14(DATA_BUS[5]),
    .pin13(DATA_BUS[4]), .pin12(REG_6_O4), .pin11(O_Clock));
  _74244 #(.ShowInternalStructure("true")) u_74244_14 (
    .pin1(R_REG_6), .pin2(REG_6_O0), .pin3(ALU_NEGATIVE_FLAG), .pin4(REG_6_O1), .pin5(DATA_BUS[6]),
    .pin6(REG_6_O2), .pin7(DATA_BUS[5]), .pin8(REG_6_O3), .pin9(DATA_BUS[4]), .pin19(R_REG_6),
    .pin18(DATA_BUS[0]), .pin17(REG_6_O7), .pin16(DATA_BUS[1]), .pin15(REG_6_O6), .pin14(DATA_BUS[2]),
    .pin13(REG_6_O5), .pin12(DATA_BUS[3]), .pin11(REG_6_O4));
  _74377 #(.ShowInternalStructure("true")) u_74377_11 (
    .pin1(n_W_UREG_2), .pin2(UREG_2_O0), .pin3(DATA_BUS[0]), .pin4(DATA_BUS[1]), .pin5(UREG_2_O1),
    .pin6(UREG_2_O2), .pin7(DATA_BUS[2]), .pin8(DATA_BUS[3]), .pin9(n74377_11_pin9), .pin19(n74377_11_pin19),
    .pin18(ALU_NEGATIVE_FLAG), .pin17(DATA_BUS[6]), .pin16(n74377_11_pin16), .pin15(n74377_11_pin15),
    .pin14(DATA_BUS[5]), .pin13(DATA_BUS[4]), .pin12(n74377_11_pin12), .pin11(O_Clock));
  _74244 #(.ShowInternalStructure("true")) u_74244_15 (
    .pin1(n_R_UREG_2), .pin2(UREG_2_O0), .pin3(pull_resistor_39_node), .pin4(UREG_2_O1),
    .pin5(pull_resistor_40_node), .pin6(UREG_2_O2), .pin7(n74244_15_pin7), .pin8(pull_resistor_41_node),
    .pin9(n74244_15_pin9), .pin19(R_UREG_2), .pin18(URN_0), .pin17(n74244_15_pin17), .pin16(URN_1),
    .pin15(n74244_15_pin15), .pin14(URN_2), .pin13(n74244_15_pin13), .pin12(n74244_15_pin12),
    .pin11(n74244_15_pin11));
  _74377 #(.ShowInternalStructure("true")) u_74377_12 (
    .pin1(FM_REG_2), .pin2(FLASH_MEMORY_ADDRESS_BUS[8]), .pin3(DATA_BUS[0]), .pin4(DATA_BUS[1]),
    .pin5(FLASH_MEMORY_ADDRESS_BUS[9]), .pin6(FLASH_MEMORY_ADDRESS_BUS[10]), .pin7(DATA_BUS[2]),
    .pin8(DATA_BUS[3]), .pin9(FLASH_MEMORY_ADDRESS_BUS[11]), .pin19(FLASH_MEMORY_ADDRESS_BUS[15]),
    .pin18(ALU_NEGATIVE_FLAG), .pin17(DATA_BUS[6]), .pin16(FLASH_MEMORY_ADDRESS_BUS[14]),
    .pin15(FLASH_MEMORY_ADDRESS_BUS[13]), .pin14(DATA_BUS[5]), .pin13(DATA_BUS[4]),
    .pin12(FLASH_MEMORY_ADDRESS_BUS[12]), .pin11(O_Clock));
  // NoConnect on n74377_11_pin19
  // NoConnect on n74377_11_pin16
  // NoConnect on n74377_11_pin15
  // NoConnect on n74377_11_pin12
  Pull_Resistor pull_resistor_42 (.node(n74244_15_pin17));
  Pull_Resistor pull_resistor_43 (.node(n74244_15_pin15));
  Pull_Resistor pull_resistor_44 (.node(n74244_15_pin13));
  // NoConnect on n74244_15_pin12
  Pull_Resistor pull_resistor_45 (.node(n74244_15_pin11));
  Counter16bits Commands (
    .n_Clear(CommandsCounter_n_Clear), .C_Clock(O_Clock), .n_Enable_Load(CommandsCounter_n_Enable_Load),
    .DI(UserAddressRegister_out1), .n_Enable_Count(CommandsCounter_n_Enable_Counter),
    .Counter_Output(AddressMemory));
  _7436 #(.ShowInternalStructure("true")) u_7436_3 (
    .pin1(UserRegistersBlock_WRITE), .pin2(REG_0), .pin3(W_REG_IM_0), .pin4(UserRegistersBlock_WRITE),
    .pin5(REG_1), .pin6(W_REG_IM_1), .pin13(UserRegistersBlock_WRITE), .pin12(REG_3), .pin11(W_REG_IM_3),
    .pin10(UserRegistersBlock_WRITE), .pin9(REG_2), .pin8(W_REG_IM_2));
  _7432 #(.ShowInternalStructure("true")) u_7432_7 (
    .pin1(W_REG_IM_0), .pin2(REG_0), .pin3(W_REG_0), .pin4(W_REG_IM_1), .pin5(REG_1), .pin6(W_REG_1),
    .pin13(W_REG_IM_3), .pin12(REG_3), .pin11(W_REG_3), .pin10(W_REG_IM_2), .pin9(REG_2), .pin8(W_REG_2));
  _7436 #(.ShowInternalStructure("true")) u_7436_4 (
    .pin1(UserRegistersBlock_WRITE), .pin2(REG_4), .pin3(W_REG_IM_4), .pin4(UserRegistersBlock_WRITE),
    .pin5(REG_5), .pin6(W_REG_IM_5), .pin13(UserRegistersBlock_WRITE), .pin12(REG_7), .pin11(W_REG_IM_7),
    .pin10(UserRegistersBlock_WRITE), .pin9(REG_6), .pin8(W_REG_IM_6));
  _7432 #(.ShowInternalStructure("true")) u_7432_8 (
    .pin1(W_REG_IM_4), .pin2(REG_4), .pin3(W_REG_4), .pin4(W_REG_IM_5), .pin5(REG_5), .pin6(W_REG_5),
    .pin13(W_REG_IM_7), .pin12(REG_7), .pin11(W_REG_7), .pin10(W_REG_IM_6), .pin9(REG_6), .pin8(W_REG_6));
  Pull_Resistor pull_resistor_46 (.node(pull_resistor_46_node));
  // NoConnect on n74139_1_pin4
  Pull_Resistor pull_resistor_47 (.node(pull_resistor_47_node));
  Pull_Resistor pull_resistor_48 (.node(pull_resistor_48_node));
  // NoConnect on n74377_13_pin9
  // Probe on AddressMemory
  _74139 #(.ShowInternalStructure("true")) u_74139_1 (
    .pin1(pull_resistor_46_node), .pin2(FM_ADDRESS_REGISTER_SELECT_0), .pin3(FM_ADDRESS_REGISTER_SELECT_1),
    .pin4(n74139_1_pin4), .pin5(FM_REG_1), .pin6(FM_REG_2), .pin7(FM_REG_3), .pin15(n74139_1_pin15),
    .pin14(n74139_1_pin14), .pin13(n74139_1_pin13), .pin12(n74139_1_pin12), .pin11(n74139_1_pin11),
    .pin10(n74139_1_pin10), .pin9(n74139_1_pin9));
  Pull_Resistor pull_resistor_49 (.node(n74139_1_pin15));
  Pull_Resistor pull_resistor_50 (.node(n74139_1_pin14));
  Pull_Resistor pull_resistor_51 (.node(n74139_1_pin13));
  // NoConnect on n74139_1_pin12
  // NoConnect on n74139_1_pin11
  // NoConnect on n74139_1_pin10
  // NoConnect on n74139_1_pin9
  _74377 #(.ShowInternalStructure("true")) u_74377_13 (
    .pin1(FM_REG_3), .pin2(FLASH_MEMORY_ADDRESS_BUS[16]), .pin3(DATA_BUS[0]), .pin4(DATA_BUS[1]),
    .pin5(FLASH_MEMORY_ADDRESS_BUS[17]), .pin6(FLASH_MEMORY_ADDRESS_BUS[18]), .pin7(pull_resistor_47_node),
    .pin8(pull_resistor_48_node), .pin9(n74377_13_pin9), .pin19(n74377_13_pin19), .pin18(n74377_13_pin18),
    .pin17(n74377_13_pin17), .pin16(n74377_13_pin16), .pin15(n74377_13_pin15), .pin14(n74377_13_pin14),
    .pin13(n74377_13_pin13), .pin12(n74377_13_pin12), .pin11(O_Clock));
  _74377 #(.ShowInternalStructure("true")) u_74377_14 (
    .pin1(W_REG_3), .pin2(REG_3_O0), .pin3(DATA_BUS[0]), .pin4(DATA_BUS[1]), .pin5(REG_3_O1),
    .pin6(REG_3_O2), .pin7(DATA_BUS[2]), .pin8(DATA_BUS[3]), .pin9(REG_3_O3), .pin19(REG_3_O7),
    .pin18(ALU_NEGATIVE_FLAG), .pin17(DATA_BUS[6]), .pin16(REG_3_O6), .pin15(REG_3_O5), .pin14(DATA_BUS[5]),
    .pin13(DATA_BUS[4]), .pin12(REG_3_O4), .pin11(O_Clock));
  _74244 #(.ShowInternalStructure("true")) u_74244_16 (
    .pin1(R_REG_3), .pin2(REG_3_O0), .pin3(ALU_NEGATIVE_FLAG), .pin4(REG_3_O1), .pin5(DATA_BUS[6]),
    .pin6(REG_3_O2), .pin7(DATA_BUS[5]), .pin8(REG_3_O3), .pin9(DATA_BUS[4]), .pin19(R_REG_3),
    .pin18(DATA_BUS[0]), .pin17(REG_3_O7), .pin16(DATA_BUS[1]), .pin15(REG_3_O6), .pin14(DATA_BUS[2]),
    .pin13(REG_3_O5), .pin12(DATA_BUS[3]), .pin11(REG_3_O4));
  _74377 #(.ShowInternalStructure("true")) u_74377_15 (
    .pin1(W_REG_7), .pin2(REG_7_O0), .pin3(DATA_BUS[0]), .pin4(DATA_BUS[1]), .pin5(REG_7_O1),
    .pin6(REG_7_O2), .pin7(DATA_BUS[2]), .pin8(DATA_BUS[3]), .pin9(REG_7_O3), .pin19(REG_7_O7),
    .pin18(ALU_NEGATIVE_FLAG), .pin17(DATA_BUS[6]), .pin16(REG_7_O6), .pin15(REG_7_O5), .pin14(DATA_BUS[5]),
    .pin13(DATA_BUS[4]), .pin12(REG_7_O4), .pin11(O_Clock));
  _74244 #(.ShowInternalStructure("true")) u_74244_17 (
    .pin1(R_REG_7), .pin2(REG_7_O0), .pin3(ALU_NEGATIVE_FLAG), .pin4(REG_7_O1), .pin5(DATA_BUS[6]),
    .pin6(REG_7_O2), .pin7(DATA_BUS[5]), .pin8(REG_7_O3), .pin9(DATA_BUS[4]), .pin19(R_REG_7),
    .pin18(DATA_BUS[0]), .pin17(REG_7_O7), .pin16(DATA_BUS[1]), .pin15(REG_7_O6), .pin14(DATA_BUS[2]),
    .pin13(REG_7_O5), .pin12(DATA_BUS[3]), .pin11(REG_7_O4));
  _7419 #(.ShowInternalStructure("true")) u_7419_5 (
    .pin1(W_UREG_0), .pin2(n_W_UREG_0), .pin3(W_UREG_1), .pin4(n_W_UREG_1), .pin5(W_UREG_2),
    .pin6(n_W_UREG_2), .pin13(R_UREG_0), .pin12(n_R_UREG_0), .pin11(R_UREG_1), .pin10(n_R_UREG_1),
    .pin9(R_UREG_2), .pin8(n_R_UREG_2));
  // NoConnect on n74377_13_pin19
  Pull_Resistor pull_resistor_52 (.node(n74377_13_pin18));
  Pull_Resistor pull_resistor_53 (.node(n74377_13_pin17));
  // NoConnect on n74377_13_pin16
  // NoConnect on n74377_13_pin15
  Pull_Resistor pull_resistor_54 (.node(n74377_13_pin14));
  Pull_Resistor pull_resistor_55 (.node(n74377_13_pin13));
  // NoConnect on n74377_13_pin12
  Register16bits CurrentAddressRegister (
    .Clock(n_Clock), .n_EN_1(CurrentAddressRegister_n_EN1), .n_EN_2(CurrentAddressRegister_n_EN2),
    .n_EN_Out(CurrentAddressRegister_n_EN_Out), .IN2(AddressMemory[15:8]), .IN1(AddressMemory[7:0]),
    .OUT1(UserAddressRegister_out1));
  // Probe on UserAddressRegister_out1
  _74377 #(.ShowInternalStructure("true")) u_74377_16 (
    .pin1(n_W_INNER_REG), .pin2(IN_REG_0_O0), .pin3(DATA_BUS[0]), .pin4(DATA_BUS[1]), .pin5(IN_REG_0_O1),
    .pin6(IN_REG_0_O2), .pin7(DATA_BUS[2]), .pin8(DATA_BUS[3]), .pin9(IN_REG_0_O3), .pin19(IN_REG_0_O7),
    .pin18(ALU_NEGATIVE_FLAG), .pin17(DATA_BUS[6]), .pin16(IN_REG_0_O6), .pin15(IN_REG_0_O5),
    .pin14(DATA_BUS[5]), .pin13(DATA_BUS[4]), .pin12(IN_REG_0_O4), .pin11(O_Clock));
  _74244 #(.ShowInternalStructure("true")) u_74244_18 (
    .pin1(n_R_INNER_REG), .pin2(IN_REG_0_O0), .pin3(ALU_NEGATIVE_FLAG), .pin4(IN_REG_0_O1),
    .pin5(DATA_BUS[6]), .pin6(IN_REG_0_O2), .pin7(DATA_BUS[5]), .pin8(IN_REG_0_O3), .pin9(DATA_BUS[4]),
    .pin19(n_R_INNER_REG), .pin18(DATA_BUS[0]), .pin17(IN_REG_0_O7), .pin16(DATA_BUS[1]),
    .pin15(IN_REG_0_O6), .pin14(DATA_BUS[2]), .pin13(IN_REG_0_O5), .pin12(DATA_BUS[3]), .pin11(IN_REG_0_O4));
  // also tied to VCC on the sheet: {FLAGS_REGISTER_pin1, n74138_1_pin6, n74138_2_pin6}

  // Other names for the same wires on the sheet: ADDRESS_BUS[15:0] = AddressMemory; B15 = AddressMemory[15];
  //   ADDRESS_BUS_RAM[14:0] = AddressMemory[14:0]; ADDRESS_BUS_ROM[12:0] = AddressMemory[12:0]; B0 = AddressMemory[0];
  //   B1 = AddressMemory[1]; B2 = AddressMemory[2]; B3 = AddressMemory[3]; B4 = AddressMemory[4];
  //   B5 = AddressMemory[5]; B6 = AddressMemory[6]; B7 = AddressMemory[7]; B8 = AddressMemory[8];
  //   B9 = AddressMemory[9]; B10 = AddressMemory[10]; B11 = AddressMemory[11]; B12 = AddressMemory[12];
  //   B13 = AddressMemory[13]; B14 = AddressMemory[14]; AMA = ALU_MODE[0]; AMB = ALU_MODE[1]; AMC = ALU_MODE[2];
  //   CPU_Clock = O_Clock; IQ0 = DATA_BUS[0]; IQ1 = DATA_BUS[1]; IQ2 = DATA_BUS[2]; IQ3 = DATA_BUS[3];
  //   IQ4 = DATA_BUS[4]; IQ5 = DATA_BUS[5]; IQ6 = DATA_BUS[6]; DATA_BUS[7] = ALU_NEGATIVE_FLAG;
  //   IQ7 = ALU_NEGATIVE_FLAG; FM0 = FLASH_MEMORY_ADDRESS_BUS[0]; FM1 = FLASH_MEMORY_ADDRESS_BUS[1];
  //   FM2 = FLASH_MEMORY_ADDRESS_BUS[2]; FM3 = FLASH_MEMORY_ADDRESS_BUS[3]; FM4 = FLASH_MEMORY_ADDRESS_BUS[4];
  //   FM5 = FLASH_MEMORY_ADDRESS_BUS[5]; FM6 = FLASH_MEMORY_ADDRESS_BUS[6]; FM7 = FLASH_MEMORY_ADDRESS_BUS[7];
  //   FM8 = FLASH_MEMORY_ADDRESS_BUS[8]; FM9 = FLASH_MEMORY_ADDRESS_BUS[9]; FM10 = FLASH_MEMORY_ADDRESS_BUS[10];
  //   FM11 = FLASH_MEMORY_ADDRESS_BUS[11]; FM12 = FLASH_MEMORY_ADDRESS_BUS[12]; FM13 = FLASH_MEMORY_ADDRESS_BUS[13];
  //   FM14 = FLASH_MEMORY_ADDRESS_BUS[14]; FM15 = FLASH_MEMORY_ADDRESS_BUS[15]; FM16 = FLASH_MEMORY_ADDRESS_BUS[16];
  //   FM17 = FLASH_MEMORY_ADDRESS_BUS[17]; FM18 = FLASH_MEMORY_ADDRESS_BUS[18]

  // Notes on the sheet:
  //   ALU AND
  //   ALU NOT
  //   ALU REGISTERS
  //   FLAGS REGISTER
  //   ALU Device
  //   ALU MODE SELECTOR
  //   ALU SUM
  //   ALU XOR
  //   ROM/RAM ENABLING
  //   ALU SHL
  //   ALU OR
  //   ALU SHR
  //   USER REGISTER NUMBERS STORAGE 
  //   USER REGISTERS BLOCK
  //   or(REG_N, not(or(EN, REG_N))
  //   INNER REGISTER
endmodule

module CU (
  input  [15:0] MicroCommandAddress,
  input  ZERO,
  input  OVERFLOW,
  input  NEGATIVE,
  input  CARRY,
  output OpcodeRegister_n_EN1,
  output OpcodeRegister_n_EN2,
  output OpcodeRegister_n_EN_Out,
  output UserAddressRegister_n_EN1,
  output UserAddressRegister_n_EN2,
  output UserAddressRegister_n_EN_Out,
  output CurrentAddressRegister_n_EN1,
  output CurrentAddressRegister_n_EN2,
  output CurrentAddressRegister_n_EN_Out,
  output MicroCommandsCounter_n_Enable_Counter,
  output MicroCommandsCounter_n_Clear,
  output MicroCommandsCounter_n_Enable_Load,
  output CommandsCounter_n_Enable_Counter,
  output CommandsCounter_n_Clear,
  output CommandsCounter_n_Enable_Load,
  output UserRegistersBlock_READ,
  output UserRegistersBlock_WRITE,
  output W_UREG_0,
  output W_UREG_1,
  output W_UREG_2,
  output R_UREG_0,
  output R_UREG_1,
  output R_UREG_2,
  output W_INNER_REG,
  output R_INNER_REG,
  output MEMORY_WE,
  output MEMORY_OE,
  output MEMORY_CE,
  output FLASH_WE,
  output FLASH_OE,
  output FLASH_CE,
  output FM_ADDRESS_REGISTER_SELECT_0,
  output FM_ADDRESS_REGISTER_SELECT_1,
  output REG_A_EN,
  output REG_B_EN,
  output [2:0] ALU_MODE
);

  wire A0, A1, A2, A3, CC, CC_CS_NE_DEF_EQ, CommandsCounter_n_Enable_Load_t, CS, CS_NE_DEF_EQ, DEF_EQ,
       EN_USER_ADDRESS_LOADING, ENUAL_NOR_CCEL, ENUAL_NOR_UAREO, EQ, GE, GE_LS_HI_VC_PL_MI_CC_CS_NE_DEF_EQ,
       GT, GT_LT_GE_LS_HI_VC_PL_MI_CC_CS_NE_DEF_EQ, HI, HI_1, HI_2, HI_VC_PL_MI_CC_CS_NE_DEF_EQ, LE, LS,
       LS_HI_VC_PL_MI_CC_CS_NE_DEF_EQ, LT, LT_GE_LS_HI_VC_PL_MI_CC_CS_NE_DEF_EQ, MI, MI_CC_CS_NE_DEF_EQ,
       MUL_0, MUL_1, MUL_2, MUL_3, MUL_4, MUL_5, MUL_6, MUL_7, MUL_8, MUL_9, MUL_10, MUL_11, MUL_12, MUL_13,
       MUL_14, MUL_15, MUL_CC_OUT, MUL_CS_OUT, MUL_DEF_OUT, MUL_EQ_OUT, MUL_GE_OUT, MUL_GT_OUT, MUL_HI_OUT,
       MUL_LE_OUT, MUL_LS_OUT, MUL_LT_OUT, MUL_MI_OUT, MUL_NE_OUT, MUL_PL_OUT, MUL_VC_OUT, MUL_VS_OUT,
       n7408_1_pin2, n7408_1_pin12, n7408_2_pin2, n7408_3_pin1, n7408_6_pin8, n7408_6_pin9, n7408_6_pin10,
       n7424_1_pin2, n7424_1_pin4, n7424_1_pin5, n7424_1_pin6, n7424_1_pin8, n7424_1_pin9, n7424_1_pin10,
       n7424_1_pin11, n7424_1_pin12, n7424_1_pin13, n7432_1_pin8, n7432_1_pin9, n7432_1_pin10, n7432_1_pin11,
       n7432_1_pin12, n7432_1_pin13, n7432_2_pin9, n7432_2_pin10, n7436_1_pin9, n7436_1_pin12, n7436_2_pin8,
       n7436_2_pin9, n7436_2_pin10, n7436_2_pin11, n7436_2_pin12, n7436_2_pin13, n7486_1_pin8, n7486_1_pin9,
       n7486_1_pin10, n7486_1_pin11, n7486_1_pin12, n7486_1_pin13, n74138_1_pin5, n74138_1_pin6,
       n74138_2_pin5, n_A3, n_GE, n_MUL_0, n_MUL_1, n_MUL_2, n_MUL_3, n_MUL_4, n_MUL_5, n_MUL_6, n_MUL_7,
       n_MUL_8, n_MUL_9, n_MUL_10, n_MUL_11, n_MUL_12, n_MUL_13, n_MUL_14, n_MUL_15, NE, NE_DEF_EQ, PL,
       PL_MI_CC_CS_NE_DEF_EQ, pull_resistor_1_node, pull_resistor_2_node, VC, VC_PL_MI_CC_CS_NE_DEF_EQ, VS,
       VS_PL_MI_CC_CS_NE_DEF_EQ;
  wire [2:2] ControlSignals_1;
  wire [5:0] ControlSignals_6;

  Pull_Resistor pull_resistor_1 (.node(pull_resistor_1_node));
  Pull_Resistor pull_resistor_2 (.node(pull_resistor_2_node));
  _7408 #(.ShowInternalStructure("true")) u_7408_1 (
    .pin1(ZERO), .pin2(n7408_1_pin2), .pin3(EQ), .pin4(CARRY), .pin5(n7408_1_pin2), .pin6(CS),
    .pin13(NEGATIVE), .pin12(n7408_1_pin12), .pin11(MI), .pin10(OVERFLOW), .pin9(n7408_1_pin12), .pin8(VS));
  _7436 #(.ShowInternalStructure("true")) u_7436_1 (
    .pin1(ZERO), .pin2(pull_resistor_1_node), .pin3(NE), .pin4(CARRY), .pin5(pull_resistor_2_node),
    .pin6(CC), .pin13(NEGATIVE), .pin12(n7436_1_pin12), .pin11(PL), .pin10(OVERFLOW), .pin9(n7436_1_pin9),
    .pin8(VC));
  _74138 #(.ShowInternalStructure("true")) u_74138_1 (
    .pin1(A0), .pin2(A1), .pin3(A2), .pin4(A3), .pin5(n74138_1_pin5), .pin6(n74138_1_pin6), .pin7(MUL_7),
    .pin15(MUL_0), .pin14(MUL_1), .pin13(MUL_2), .pin12(MUL_3), .pin11(MUL_4), .pin10(MUL_5), .pin9(MUL_6));
  Pull_Resistor pull_resistor_3 (.node(n74138_1_pin5));
  _74138 #(.ShowInternalStructure("true")) u_74138_2 (
    .pin1(A0), .pin2(A1), .pin3(A2), .pin4(n_A3), .pin5(n74138_2_pin5), .pin6(n74138_1_pin6), .pin7(MUL_15),
    .pin15(MUL_8), .pin14(MUL_9), .pin13(MUL_10), .pin12(MUL_11), .pin11(MUL_12), .pin10(MUL_13),
    .pin9(MUL_14));
  Pull_Resistor pull_resistor_4 (.node(n74138_2_pin5));
  _7404 #(.ShowInternalStructure("true")) u_7404_1 (
    .pin1(A3), .pin2(n_A3), .pin3(MUL_0), .pin4(n_MUL_0), .pin5(MUL_1), .pin6(n_MUL_1), .pin13(MUL_2),
    .pin12(n_MUL_2), .pin11(MUL_3), .pin10(n_MUL_3), .pin9(MUL_4), .pin8(n_MUL_4));
  _7404 #(.ShowInternalStructure("true")) u_7404_2 (
    .pin1(MUL_5), .pin2(n_MUL_5), .pin3(MUL_6), .pin4(n_MUL_6), .pin5(MUL_7), .pin6(n_MUL_7), .pin13(MUL_8),
    .pin12(n_MUL_8), .pin11(MUL_9), .pin10(n_MUL_9), .pin9(MUL_10), .pin8(n_MUL_10));
  _7404 #(.ShowInternalStructure("true")) u_7404_3 (
    .pin1(MUL_11), .pin2(n_MUL_11), .pin3(MUL_12), .pin4(n_MUL_12), .pin5(MUL_13), .pin6(n_MUL_13),
    .pin13(MUL_14), .pin12(n_MUL_14), .pin11(MUL_15), .pin10(n_MUL_15), .pin9(n_GE), .pin8(GE));
  _7436 #(.ShowInternalStructure("true")) u_7436_2 (
    .pin1(EN_USER_ADDRESS_LOADING), .pin2(ControlSignals_1[2]), .pin3(ENUAL_NOR_UAREO),
    .pin4(EN_USER_ADDRESS_LOADING), .pin5(CommandsCounter_n_Enable_Load_t), .pin6(ENUAL_NOR_CCEL),
    .pin13(n7436_2_pin13), .pin12(n7436_2_pin12), .pin11(n7436_2_pin11), .pin10(n7436_2_pin10),
    .pin9(n7436_2_pin9), .pin8(n7436_2_pin8));
  _7432 #(.ShowInternalStructure("true")) u_7432_1 (
    .pin1(ControlSignals_1[2]), .pin2(ENUAL_NOR_UAREO), .pin3(UserAddressRegister_n_EN_Out),
    .pin4(CommandsCounter_n_Enable_Load_t), .pin5(ENUAL_NOR_CCEL), .pin6(CommandsCounter_n_Enable_Load),
    .pin13(n7432_1_pin13), .pin12(n7432_1_pin12), .pin11(n7432_1_pin11), .pin10(n7432_1_pin10),
    .pin9(n7432_1_pin9), .pin8(n7432_1_pin8));
  Pull_Resistor pull_resistor_5 (.node(n7436_1_pin12));
  Pull_Resistor pull_resistor_6 (.node(n7436_1_pin9));
  Pull_Resistor pull_resistor_7 (.node(n7436_2_pin13));
  Pull_Resistor pull_resistor_8 (.node(n7436_2_pin12));
  Pull_Resistor pull_resistor_9 (.node(n7436_2_pin10));
  Pull_Resistor pull_resistor_10 (.node(n7436_2_pin9));
  Pull_Resistor pull_resistor_11 (.node(n7432_1_pin13));
  Pull_Resistor pull_resistor_12 (.node(n7432_1_pin12));
  Pull_Resistor pull_resistor_13 (.node(n7432_1_pin10));
  Pull_Resistor pull_resistor_14 (.node(n7432_1_pin9));
  // NoConnect on n7436_2_pin11
  // NoConnect on n7436_2_pin8
  // NoConnect on n7432_1_pin11
  // NoConnect on n7432_1_pin8
  _7424 #(.ShowInternalStructure("true")) u_7424_1 (
    .pin1(ZERO), .pin2(n7424_1_pin2), .pin3(HI_1), .pin4(n7424_1_pin4), .pin5(n7424_1_pin5),
    .pin6(n7424_1_pin6), .pin13(n7424_1_pin13), .pin12(n7424_1_pin12), .pin11(n7424_1_pin11),
    .pin10(n7424_1_pin10), .pin9(n7424_1_pin9), .pin8(n7424_1_pin8));
  Pull_Resistor pull_resistor_15 (.node(n7424_1_pin2));
  Pull_Resistor pull_resistor_16 (.node(n7424_1_pin4));
  Pull_Resistor pull_resistor_17 (.node(n7424_1_pin5));
  // NoConnect on n7424_1_pin6
  _7408 #(.ShowInternalStructure("true")) u_7408_2 (
    .pin1(CARRY), .pin2(n7408_2_pin2), .pin3(HI_2), .pin4(HI_1), .pin5(HI_2), .pin6(HI), .pin13(NE),
    .pin12(GE), .pin11(GT), .pin10(EQ), .pin9(LT), .pin8(LE));
  _7486 #(.ShowInternalStructure("true")) u_7486_1 (
    .pin1(OVERFLOW), .pin2(NEGATIVE), .pin3(n_GE), .pin4(OVERFLOW), .pin5(NEGATIVE), .pin6(LT),
    .pin13(n7486_1_pin13), .pin12(n7486_1_pin12), .pin11(n7486_1_pin11), .pin10(n7486_1_pin10),
    .pin9(n7486_1_pin9), .pin8(n7486_1_pin8));
  Pull_Resistor pull_resistor_18 (.node(n7424_1_pin13));
  Pull_Resistor pull_resistor_19 (.node(n7424_1_pin12));
  // NoConnect on n7424_1_pin11
  Pull_Resistor pull_resistor_20 (.node(n7424_1_pin10));
  Pull_Resistor pull_resistor_21 (.node(n7424_1_pin9));
  // NoConnect on n7424_1_pin8
  Pull_Resistor pull_resistor_22 (.node(n7486_1_pin13));
  Pull_Resistor pull_resistor_23 (.node(n7486_1_pin12));
  // NoConnect on n7486_1_pin11
  Pull_Resistor pull_resistor_24 (.node(n7486_1_pin10));
  Pull_Resistor pull_resistor_25 (.node(n7486_1_pin9));
  // NoConnect on n7486_1_pin8
  _7408 #(.ShowInternalStructure("true")) u_7408_3 (
    .pin1(n7408_3_pin1), .pin2(n_MUL_0), .pin3(MUL_DEF_OUT), .pin4(EQ), .pin5(n_MUL_1), .pin6(MUL_EQ_OUT),
    .pin13(NE), .pin12(n_MUL_2), .pin11(MUL_NE_OUT), .pin10(CS), .pin9(n_MUL_3), .pin8(MUL_CS_OUT));
  _7408 #(.ShowInternalStructure("true")) u_7408_4 (
    .pin1(CC), .pin2(n_MUL_4), .pin3(MUL_CC_OUT), .pin4(MI), .pin5(n_MUL_5), .pin6(MUL_MI_OUT), .pin13(PL),
    .pin12(n_MUL_6), .pin11(MUL_PL_OUT), .pin10(VS), .pin9(n_MUL_7), .pin8(MUL_VS_OUT));
  _7408 #(.ShowInternalStructure("true")) u_7408_5 (
    .pin1(VC), .pin2(n_MUL_8), .pin3(MUL_VC_OUT), .pin4(HI), .pin5(n_MUL_9), .pin6(MUL_HI_OUT), .pin13(LS),
    .pin12(n_MUL_10), .pin11(MUL_LS_OUT), .pin10(GE), .pin9(n_MUL_11), .pin8(MUL_GE_OUT));
  _7408 #(.ShowInternalStructure("true")) u_7408_6 (
    .pin1(LT), .pin2(n_MUL_12), .pin3(MUL_LT_OUT), .pin4(GT), .pin5(n_MUL_13), .pin6(MUL_GT_OUT), .pin13(LE),
    .pin12(n_MUL_14), .pin11(MUL_LE_OUT), .pin10(n7408_6_pin10), .pin9(n7408_6_pin9), .pin8(n7408_6_pin8));
  Pull_Resistor pull_resistor_26 (.node(n7408_6_pin10));
  Pull_Resistor pull_resistor_27 (.node(n7408_6_pin9));
  // NoConnect on n7408_6_pin8
  ROM #(.addrWidth(16)) ROM_1 (
    .addr(MicroCommandAddress),
    .data({OpcodeRegister_n_EN1, OpcodeRegister_n_EN2, OpcodeRegister_n_EN_Out, UserAddressRegister_n_EN1, UserAddressRegister_n_EN2, ControlSignals_1[2], CurrentAddressRegister_n_EN1, CurrentAddressRegister_n_EN2}));
  ROM #(.addrWidth(16)) ROM_2 (
    .addr(MicroCommandAddress),
    .data({CurrentAddressRegister_n_EN_Out, MicroCommandsCounter_n_Enable_Counter, MicroCommandsCounter_n_Clear, MicroCommandsCounter_n_Enable_Load, CommandsCounter_n_Enable_Counter, CommandsCounter_n_Clear, CommandsCounter_n_Enable_Load_t, UserRegistersBlock_READ}));
  ROM #(.addrWidth(16)) ROM_3 (
    .addr(MicroCommandAddress),
    .data({UserRegistersBlock_WRITE, W_UREG_0, W_UREG_1, W_UREG_2, R_UREG_0, R_UREG_1, R_UREG_2, W_INNER_REG}));
  ROM #(.addrWidth(16)) ROM_4 (
    .addr(MicroCommandAddress),
    .data({R_INNER_REG, MEMORY_WE, MEMORY_OE, MEMORY_CE, FLASH_WE, FLASH_OE, FLASH_CE, FM_ADDRESS_REGISTER_SELECT_0}));
  ROM #(.addrWidth(16)) ROM_5 (
    .addr(MicroCommandAddress), .data({FM_ADDRESS_REGISTER_SELECT_1, REG_A_EN, REG_B_EN, ALU_MODE, A3, A2}));
  ROM #(.addrWidth(16)) ROM_6 (.addr(MicroCommandAddress), .data({A1, A0, ControlSignals_6}));
  _7432 #(.ShowInternalStructure("true")) u_7432_2 (
    .pin1(LT_GE_LS_HI_VC_PL_MI_CC_CS_NE_DEF_EQ), .pin2(MUL_GT_OUT),
    .pin3(GT_LT_GE_LS_HI_VC_PL_MI_CC_CS_NE_DEF_EQ), .pin4(GT_LT_GE_LS_HI_VC_PL_MI_CC_CS_NE_DEF_EQ),
    .pin5(MUL_LE_OUT), .pin6(EN_USER_ADDRESS_LOADING), .pin13(EQ), .pin12(CC), .pin11(LS),
    .pin10(n7432_2_pin10), .pin9(n7432_2_pin9));  // open: pin8
  _7432 #(.ShowInternalStructure("true")) u_7432_3 (
    .pin1(MUL_DEF_OUT), .pin2(MUL_EQ_OUT), .pin3(DEF_EQ), .pin4(DEF_EQ), .pin5(MUL_NE_OUT), .pin6(NE_DEF_EQ),
    .pin13(NE_DEF_EQ), .pin12(MUL_CS_OUT), .pin11(CS_NE_DEF_EQ), .pin10(CS_NE_DEF_EQ), .pin9(MUL_CC_OUT),
    .pin8(CC_CS_NE_DEF_EQ));
  _7432 #(.ShowInternalStructure("true")) u_7432_4 (
    .pin1(CC_CS_NE_DEF_EQ), .pin2(MUL_MI_OUT), .pin3(MI_CC_CS_NE_DEF_EQ), .pin4(MI_CC_CS_NE_DEF_EQ),
    .pin5(MUL_PL_OUT), .pin6(PL_MI_CC_CS_NE_DEF_EQ), .pin13(PL_MI_CC_CS_NE_DEF_EQ), .pin12(MUL_VS_OUT),
    .pin11(VS_PL_MI_CC_CS_NE_DEF_EQ), .pin10(VS_PL_MI_CC_CS_NE_DEF_EQ), .pin9(MUL_VC_OUT),
    .pin8(VC_PL_MI_CC_CS_NE_DEF_EQ));
  _7432 #(.ShowInternalStructure("true")) u_7432_5 (
    .pin1(VC_PL_MI_CC_CS_NE_DEF_EQ), .pin2(MUL_HI_OUT), .pin3(HI_VC_PL_MI_CC_CS_NE_DEF_EQ),
    .pin4(HI_VC_PL_MI_CC_CS_NE_DEF_EQ), .pin5(MUL_LS_OUT), .pin6(LS_HI_VC_PL_MI_CC_CS_NE_DEF_EQ),
    .pin13(LS_HI_VC_PL_MI_CC_CS_NE_DEF_EQ), .pin12(MUL_GE_OUT), .pin11(GE_LS_HI_VC_PL_MI_CC_CS_NE_DEF_EQ),
    .pin10(GE_LS_HI_VC_PL_MI_CC_CS_NE_DEF_EQ), .pin9(MUL_LT_OUT), .pin8(LT_GE_LS_HI_VC_PL_MI_CC_CS_NE_DEF_EQ));
  Pull_Resistor pull_resistor_28 (.node(n7432_2_pin10));
  Pull_Resistor pull_resistor_29 (.node(n7432_2_pin9));
  // also tied to VCC on the sheet: {n7408_1_pin2, n74138_1_pin6, n7408_1_pin12, n7408_2_pin2, n7408_3_pin1}

  // Other names for the same wires on the sheet: ALU_MODE_1 = ALU_MODE[0];
  //   ControlSignals_5[7:0] = {FM_ADDRESS_REGISTER_SELECT_1, REG_A_EN, REG_B_EN, ALU_MODE, A3, A2};
  //   ALU_MODE_2 = ALU_MODE[1]; ALU_MODE_3 = ALU_MODE[2];
  //   ControlSignals_1 (some bits) = {OpcodeRegister_n_EN1, OpcodeRegister_n_EN2, OpcodeRegister_n_EN_Out, UserAddressRegister_n_EN1, UserAddressRegister_n_EN2, CurrentAddressRegister_n_EN1, CurrentAddressRegister_n_EN2};
  //   UserAddressRegister_n_EN_Out_t = ControlSignals_1[2];
  //   ControlSignals_2[7:0] = {CurrentAddressRegister_n_EN_Out, MicroCommandsCounter_n_Enable_Counter, MicroCommandsCounter_n_Clear, MicroCommandsCounter_n_Enable_Load, CommandsCounter_n_Enable_Counter, CommandsCounter_n_Clear, CommandsCounter_n_Enable_Load_t, UserRegistersBlock_READ};
  //   ControlSignals_3[7:0] = {UserRegistersBlock_WRITE, W_UREG_0, W_UREG_1, W_UREG_2, R_UREG_0, R_UREG_1, R_UREG_2, W_INNER_REG};
  //   ControlSignals_4[7:0] = {R_INNER_REG, MEMORY_WE, MEMORY_OE, MEMORY_CE, FLASH_WE, FLASH_OE, FLASH_CE, FM_ADDRESS_REGISTER_SELECT_0};
  //   ControlSignals_6[7:6] = {A1, A0}; in_CommandsCounter_n_Enable_Load = CommandsCounter_n_Enable_Load;
  //   in_UserAddressRegister_n_EN_Out = UserAddressRegister_n_EN_Out

  // Notes on the sheet:
  //   contents of ROM_1 (hex, n*v repeats v):
  //   fc bc fc 7c dc fc   fc fc fc fc fc fc   fc fc fc fc fc fc   fc fc f4 fc ec fc   fc fb ff ff fc fc
  //   fc f4 fc ec fc fc   fb ff ff fc fc fc   fc fc fc fc fc fc   fc fc fc fc fc fc   fc fc fc fc fc fc
  //   fc fc fc fc fc fc   fc fc fc fc fc fc   fc fc fc fc fc fc   fc fc fc fc fc fc   fc fc fc fc fc fc
  //   fc fc fc fc fc fc   fc fc fc fc fc fc   fc fc fc fc fc fc   fc fc f4 fc ec fb   fc fc f4 fc ec fc
  //   fb fc fc f4 fc ec   fc fb fc fc f4 fc   ec fc fb fc fc f4   fc ec fc fb fc fc   f4 fc ec fc fb fc
  //   fc f4 fc ec fc fb   fc fc f4 fc ec fc   fb fc fc f4 fc ec   fc fb fc fc f4 fc   ec fc fb fc fc f4
  //   fc ec fc fb fc fc   f4 fc ec fc fb fc   fc f4 fc ec fc fb   fc fc f4 fc ec fc   fb fc fc f4 fc ec
  //   fc fb fc
  //   contents of ROM_2 (hex, n*v repeats v):
  //   f6 f6 fe f6 a6 fe   f6 fe f6 fe d6 fe   f6 fe f6 f7 f6 fe   d6 fe f6 fe f6 fe   f6 f4 f6 74 fe d6
  //   fe f6 fe f6 fe f6   f4 f7 74 fe d6 fe   f6 fe f6 fe f6 f7   f7 f6 fe d6 fe f6   fe f6 fe f6 f7 f7
  //   f6 fe d6 fe f6 fe   f6 fe f6 f7 f7 f6   fe d6 fe f6 fe f6   f7 f6 fe d6 fe f6   fe f6 fe f6 f7 f7
  //   f6 fe d6 fe f6 fe   f6 f7 f6 fe d6 fe   f6 fe f6 f7 f6 fe   d6 fe f6 fe f6 f4   d6 fe f6 fe f6 fe
  //   f4 d6 fe f6 fe f6   fe f4 d6 fe f6 fe   f6 fe f4 d6 fe f6   fe f6 fe f4 d6 fe   f6 fe f6 fe f4 d6
  //   fe f6 fe f6 fe f4   d6 fe f6 fe f6 fe   f4 d6 fe f6 fe f6   fe f4 d6 fe f6 fe   f6 fe f4 d6 fe f6
  //   fe f6 fe f4 d6 fe   f6 fe f6 fe f4 d6   fe f6 fe f6 fe f4   d6 fe f6 fe f6 fe   f4 d6 fe f6 fe f6
  //   fe f4 d6
  //   contents of ROM_3 (hex, n*v repeats v):
  //   0 0 0 0 0 0   40 0 88 0 0 0   40 0 20 9 84 0   0 0 0 0 0 0   40 0 88 0 0 0   0 0 0 0 0 40   0 8 0 0
  //   0 0   40 0 20 0 10 8   4 82 0 0 0 40   0 20 0 10 8 4   82 0 0 0 40 0   20 0 10 8 4 82   0 0 0 40 0
  //   20   8 84 0 0 0 40   0 20 0 10 8 4   82 0 0 0 40 0   20 8 84 0 0 0   40 0 20 8 84 0   0 0 0 0 0 0
  //   0 0 0 0 0 0   0 0 0 0 0 0   0 0 0 0 0 0   0 0 0 0 0 0   0 0 0 0 0 0   0 0 0 0 0 0   0 0 0 0 0 0   0
  //   0 0 0 0 0   0 0 0 0 0 0   0 0 0 0 0 0   0 0 0 0 0 0   0 0 0 0 0 0   0 0 0 0 0 0   0 0 0 0 0 0   0 0
  //   0 0 0 0   0 0 0 0 0 0   0 0 0
  //   contents of ROM_4 (hex, n*v repeats v):
  //   0 30 0 30 0 0   30 0 30 0 0 0   30 0 30 0 80 0   0 0 30 0 30 0   30 0 30 0 0 0   0 30 0 30 0 30   0
  //   50 0 0 0 0   30 0 30 0 30 0   0 0 0 0 0 30   0 30 0 30 0 0   0 0 0 0 30 0   30 0 30 0 0 0   0 0 0 30
  //   0 30   0 0 0 0 0 30   0 30 0 30 0 0   0 0 0 0 30 0   30 0 0 0 0 0   30 0 30 0 0 0   0 0 30 0 30 0
  //   0 0 30 0 30 0   0 0 0 30 0 30   0 0 0 0 30 0   30 0 0 0 0 30   0 30 0 0 0 0   30 0 30 0 0 0   0 30 0
  //   30 0 0   0 0 30 0 30 0   0 0 0 30 0 30   0 0 0 0 30 0   30 0 0 0 0 30   0 30 0 0 0 0   30 0 30 0 0 0
  //   0 30 0 30 0 0   0 0 30 0 30 0   0 0 0 30 0 30   0 0 0
  //   contents of ROM_5 (hex, n*v repeats v):
  //   0 0 0 0 0 0   0 0 0 0 0 0   0 0 0 0 0 0   0 0 0 0 0 0   0 0 0 0 0 0   0 0 0 0 0 0   0 0 0 0 0 0   0
  //   0 0 0 0 40   20 4 0 0 0 0   0 0 0 0 40 20   8 0 0 0 0 0   0 0 0 40 20 c   0 0 0 0 0 0   40 10 0 0 0
  //   0   0 0 0 0 40 20   14 0 0 0 0 0   0 40 18 0 0 0   0 0 0 40 1c 0   0 0 0 0 0 0   0 0 0 0 0 0   0 0 0
  //   0 0 0   0 0 0 0 0 0   0 0 0 0 0 0   0 0 0 1 0 0   0 0 0 0 1 0   0 0 0 0 0 1   0 0 0 0 0 0   1 0 0 0
  //   0 0   0 2 0 0 0 0   0 0 2 0 0 0   0 0 0 2 0 0   0 0 0 0 2 0   0 0 0 0 0 3   0 0 0 0 0 0   3 0 0 0 0
  //   0   0 3 0
  //   contents of ROM_6 (hex, n*v repeats v):
  //   0 0 0 0 0 0   0 0 0 0 0 0   0 0 0 0 0 0   0 0 0 0 0 0   0 0 0 0 0 0   0 0 0 0 0 0   0 0 0 0 0 0   0
  //   0 0 0 0 0   0 0 0 0 0 0   0 0 0 0 0 0   0 0 0 0 0 0   0 0 0 0 0 0   0 0 0 0 0 0   0 0 0 0 0 0   0 0
  //   0 0 0 0   0 0 0 0 0 0   0 0 0 0 0 0   0 0 0 0 0 0   0 0 0 0 0 0   0 0 0 0 0 0   40 0 0 0 0 0   0 80
  //   0 0 0 0   0 0 c0 0 0 0   0 0 0 0 0 0   0 0 0 0 40 0   0 0 0 0 0 80   0 0 0 0 0 0   c0 0 0 0 0 0   0
  //   0 0 0 0 0   0 0 40 0 0 0   0 0 0 80 0 0   0 0 0 0 c0 0   0 0 0 0 0 0   0 0 0 0 0 0   40 0 0 0 0 0
  //   0 80 0
endmodule

module Counter16bits (
  input  n_Enable_Count,
  input  n_Clear,
  input  C_Clock,
  input  n_Enable_Load,
  input  [15:0] DI,
  output [15:0] Counter_Output
);

  wire n74163_4_pin15, Power, RCO_1, RCO_2, RCO_3;

  _74163 #(.ShowInternalStructure("true")) u_74163_1 (
    .pin1(n_Clear), .pin2(C_Clock), .pin3(DI[0]), .pin4(DI[1]), .pin5(DI[2]), .pin6(DI[3]),
    .pin7(n_Enable_Count), .pin15(RCO_1), .pin14(Counter_Output[0]), .pin13(Counter_Output[1]),
    .pin12(Counter_Output[2]), .pin11(Counter_Output[3]), .pin10(Power), .pin9(n_Enable_Load));
  _74163 #(.ShowInternalStructure("true")) u_74163_2 (
    .pin1(n_Clear), .pin2(C_Clock), .pin3(DI[4]), .pin4(DI[5]), .pin5(DI[6]), .pin6(DI[7]),
    .pin7(n_Enable_Count), .pin15(RCO_2), .pin14(Counter_Output[4]), .pin13(Counter_Output[5]),
    .pin12(Counter_Output[6]), .pin11(Counter_Output[7]), .pin10(RCO_1), .pin9(n_Enable_Load));
  _74163 #(.ShowInternalStructure("true")) u_74163_3 (
    .pin1(n_Clear), .pin2(C_Clock), .pin3(DI[8]), .pin4(DI[9]), .pin5(DI[10]), .pin6(DI[11]),
    .pin7(n_Enable_Count), .pin15(RCO_3), .pin14(Counter_Output[8]), .pin13(Counter_Output[9]),
    .pin12(Counter_Output[10]), .pin11(Counter_Output[11]), .pin10(RCO_2), .pin9(n_Enable_Load));
  _74163 #(.ShowInternalStructure("true")) u_74163_4 (
    .pin1(n_Clear), .pin2(C_Clock), .pin3(DI[12]), .pin4(DI[13]), .pin5(DI[14]), .pin6(DI[15]),
    .pin7(n_Enable_Count), .pin15(n74163_4_pin15), .pin14(Counter_Output[12]), .pin13(Counter_Output[13]),
    .pin12(Counter_Output[14]), .pin11(Counter_Output[15]), .pin10(RCO_3), .pin9(n_Enable_Load));
  // NoConnect on n74163_4_pin15
  // also tied to VCC on the sheet: Power

  // Other names for the same wires on the sheet: CLK = C_Clock; CLR = n_Clear; EN_P = n_Enable_Count; IN_1[15:0] = DI;
  //   NLD_1 = n_Enable_Load; OUT_1[15:0] = Counter_Output
endmodule

module Register16bits (
  input  Clock,
  input  n_EN_1,
  input  n_EN_2,
  input  n_EN_Out,
  input  [7:0] IN2,
  input  [7:0] IN1,
  output [15:0] OUT1
);

  wire O_1, O_2, O_3, O_4, O_5, O_6, O_7, O_8, O_9, O_10, O_11, O_12, O_13, O_14, O_15, O_16;

  _74377 #(.ShowInternalStructure("true")) u_74377_1 (
    .pin1(n_EN_1), .pin2(O_1), .pin3(IN1[0]), .pin4(IN1[1]), .pin5(O_2), .pin6(O_3), .pin7(IN1[2]),
    .pin8(IN1[3]), .pin9(O_4), .pin19(O_8), .pin18(IN1[7]), .pin17(IN1[6]), .pin16(O_7), .pin15(O_6),
    .pin14(IN1[5]), .pin13(IN1[4]), .pin12(O_5), .pin11(Clock));
  _74377 #(.ShowInternalStructure("true")) u_74377_2 (
    .pin1(n_EN_2), .pin2(O_9), .pin3(IN2[0]), .pin4(IN2[1]), .pin5(O_10), .pin6(O_11), .pin7(IN2[2]),
    .pin8(IN2[3]), .pin9(O_12), .pin19(O_16), .pin18(IN2[7]), .pin17(IN2[6]), .pin16(O_15), .pin15(O_14),
    .pin14(IN2[5]), .pin13(IN2[4]), .pin12(O_13), .pin11(Clock));
  _74244 #(.ShowInternalStructure("true")) u_74244_1 (
    .pin1(n_EN_Out), .pin2(O_5), .pin3(OUT1[0]), .pin4(O_6), .pin5(OUT1[1]), .pin6(O_7), .pin7(OUT1[2]),
    .pin8(O_8), .pin9(OUT1[3]), .pin19(n_EN_Out), .pin18(OUT1[4]), .pin17(O_1), .pin16(OUT1[5]), .pin15(O_2),
    .pin14(OUT1[6]), .pin13(O_3), .pin12(OUT1[7]), .pin11(O_4));
  _74244 #(.ShowInternalStructure("true")) u_74244_2 (
    .pin1(n_EN_Out), .pin2(O_13), .pin3(OUT1[8]), .pin4(O_14), .pin5(OUT1[9]), .pin6(O_15), .pin7(OUT1[10]),
    .pin8(O_16), .pin9(OUT1[11]), .pin19(n_EN_Out), .pin18(OUT1[12]), .pin17(O_9), .pin16(OUT1[13]),
    .pin15(O_10), .pin14(OUT1[14]), .pin13(O_11), .pin12(OUT1[15]), .pin11(O_12));

  // Other names for the same wires on the sheet: EN_1 = n_EN_1; EN_2 = n_EN_2; EN_Output = n_EN_Out; IN_1[7:0] = IN1;
  //   IN_11 = IN1[0]; IN_12 = IN1[1]; IN_13 = IN1[2]; IN_14 = IN1[3]; IN_15 = IN1[4]; IN_16 = IN1[5]; IN_17 = IN1[6];
  //   IN_18 = IN1[7]; IN_2[7:0] = IN2; IN_21 = IN2[0]; IN_22 = IN2[1]; IN_23 = IN2[2]; IN_24 = IN2[3]; IN_25 = IN2[4];
  //   IN_26 = IN2[5]; IN_27 = IN2[6]; IN_28 = IN2[7]; O1 = OUT1[0]; O2 = OUT1[1]; O3 = OUT1[2]; O4 = OUT1[3];
  //   O5 = OUT1[4]; O6 = OUT1[5]; O7 = OUT1[6]; O8 = OUT1[7]; O9 = OUT1[8]; O10 = OUT1[9]; O11 = OUT1[10];
  //   O12 = OUT1[11]; O13 = OUT1[12]; O14 = OUT1[13]; O15 = OUT1[14]; O16 = OUT1[15]
endmodule

module UserRegistersBlock (
  input  CLOCK,
  input  [7:0] DATA_BUS_IN,
  input  READ,
  input  WRITE,
  input  [1:0] REG_NUMBER,
  output [7:0] DATA_BUS_OUT
);

  wire n7414_1_pin10, n7414_1_pin11, n7414_1_pin12, n7414_1_pin13, n74139_1_pin9, n74139_1_pin10,
       n74139_1_pin11, n74139_1_pin12, n74139_1_pin13, n74139_1_pin14, n74139_1_pin15, n_REG_0, n_REG_1,
       n_REG_2, n_REG_3, pull_resistor_1_node, R_REG_0, R_REG_1, R_REG_2, R_REG_3, REG_0, REG_0_O0, REG_0_O1,
       REG_0_O2, REG_0_O3, REG_0_O4, REG_0_O5, REG_0_O6, REG_0_O7, REG_1, REG_1_O0, REG_1_O1, REG_1_O2,
       REG_1_O3, REG_1_O4, REG_1_O5, REG_1_O6, REG_1_O7, REG_2, REG_2_O0, REG_2_O1, REG_2_O2, REG_2_O3,
       REG_2_O4, REG_2_O5, REG_2_O6, REG_2_O7, REG_3, REG_3_O0, REG_3_O1, REG_3_O2, REG_3_O3, REG_3_O4,
       REG_3_O5, REG_3_O6, REG_3_O7, W_REG_0, W_REG_1, W_REG_2, W_REG_3;

  Pull_Resistor pull_resistor_1 (.node(pull_resistor_1_node));
  _74139 #(.ShowInternalStructure("true")) u_74139_1 (
    .pin1(pull_resistor_1_node), .pin2(REG_NUMBER[0]), .pin3(REG_NUMBER[1]), .pin4(REG_0), .pin5(REG_1),
    .pin6(REG_2), .pin7(REG_3), .pin15(n74139_1_pin15), .pin14(n74139_1_pin14), .pin13(n74139_1_pin13),
    .pin12(n74139_1_pin12), .pin11(n74139_1_pin11), .pin10(n74139_1_pin10), .pin9(n74139_1_pin9));
  _74377 #(.ShowInternalStructure("true")) u_74377_1 (
    .pin1(W_REG_0), .pin2(REG_0_O0), .pin3(DATA_BUS_IN[0]), .pin4(DATA_BUS_IN[1]), .pin5(REG_0_O1),
    .pin6(REG_0_O2), .pin7(DATA_BUS_IN[2]), .pin8(DATA_BUS_IN[3]), .pin9(REG_0_O3), .pin19(REG_0_O7),
    .pin18(DATA_BUS_IN[7]), .pin17(DATA_BUS_IN[6]), .pin16(REG_0_O6), .pin15(REG_0_O5),
    .pin14(DATA_BUS_IN[5]), .pin13(DATA_BUS_IN[4]), .pin12(REG_0_O4), .pin11(CLOCK));
  _74244 #(.ShowInternalStructure("true")) u_74244_1 (
    .pin1(R_REG_0), .pin2(REG_0_O0), .pin3(DATA_BUS_IN[7]), .pin4(REG_0_O1), .pin5(DATA_BUS_IN[6]),
    .pin6(REG_0_O2), .pin7(DATA_BUS_IN[5]), .pin8(REG_0_O3), .pin9(DATA_BUS_IN[4]), .pin19(R_REG_0),
    .pin18(DATA_BUS_IN[0]), .pin17(REG_0_O7), .pin16(DATA_BUS_IN[1]), .pin15(REG_0_O6),
    .pin14(DATA_BUS_IN[2]), .pin13(REG_0_O5), .pin12(DATA_BUS_IN[3]), .pin11(REG_0_O4));
  Pull_Resistor pull_resistor_2 (.node(n74139_1_pin15));
  Pull_Resistor pull_resistor_3 (.node(n74139_1_pin14));
  Pull_Resistor pull_resistor_4 (.node(n74139_1_pin13));
  // NoConnect on n74139_1_pin12
  // NoConnect on n74139_1_pin11
  // NoConnect on n74139_1_pin10
  // NoConnect on n74139_1_pin9
  _7414 #(.ShowInternalStructure("true")) u_7414_1 (
    .pin1(REG_0), .pin2(n_REG_0), .pin3(REG_1), .pin4(n_REG_1), .pin5(REG_2), .pin6(n_REG_2),
    .pin13(n7414_1_pin13), .pin12(n7414_1_pin12), .pin11(n7414_1_pin11), .pin10(n7414_1_pin10), .pin9(REG_3),
    .pin8(n_REG_3));
  Pull_Resistor pull_resistor_5 (.node(n7414_1_pin13));
  // NoConnect on n7414_1_pin12
  Pull_Resistor pull_resistor_6 (.node(n7414_1_pin11));
  // NoConnect on n7414_1_pin10
  _74377 #(.ShowInternalStructure("true")) u_74377_2 (
    .pin1(W_REG_1), .pin2(REG_1_O0), .pin3(DATA_BUS_IN[0]), .pin4(DATA_BUS_IN[1]), .pin5(REG_1_O1),
    .pin6(REG_1_O2), .pin7(DATA_BUS_IN[2]), .pin8(DATA_BUS_IN[3]), .pin9(REG_1_O3), .pin19(REG_1_O7),
    .pin18(DATA_BUS_IN[7]), .pin17(DATA_BUS_IN[6]), .pin16(REG_1_O6), .pin15(REG_1_O5),
    .pin14(DATA_BUS_IN[5]), .pin13(DATA_BUS_IN[4]), .pin12(REG_1_O4), .pin11(CLOCK));
  _74244 #(.ShowInternalStructure("true")) u_74244_2 (
    .pin1(R_REG_1), .pin2(REG_1_O0), .pin3(DATA_BUS_IN[7]), .pin4(REG_1_O1), .pin5(DATA_BUS_IN[6]),
    .pin6(REG_1_O2), .pin7(DATA_BUS_IN[5]), .pin8(REG_1_O3), .pin9(DATA_BUS_IN[4]), .pin19(R_REG_1),
    .pin18(DATA_BUS_IN[0]), .pin17(REG_1_O7), .pin16(DATA_BUS_IN[1]), .pin15(REG_1_O6),
    .pin14(DATA_BUS_IN[2]), .pin13(REG_1_O5), .pin12(DATA_BUS_IN[3]), .pin11(REG_1_O4));
  _7424 #(.ShowInternalStructure("true")) u_7424_1 (
    .pin1(WRITE), .pin2(n_REG_0), .pin3(W_REG_0), .pin4(WRITE), .pin5(n_REG_1), .pin6(W_REG_1),
    .pin13(WRITE), .pin12(n_REG_3), .pin11(W_REG_3), .pin10(WRITE), .pin9(n_REG_2), .pin8(W_REG_2));
  _74377 #(.ShowInternalStructure("true")) u_74377_3 (
    .pin1(W_REG_2), .pin2(REG_2_O0), .pin3(DATA_BUS_IN[0]), .pin4(DATA_BUS_IN[1]), .pin5(REG_2_O1),
    .pin6(REG_2_O2), .pin7(DATA_BUS_IN[2]), .pin8(DATA_BUS_IN[3]), .pin9(REG_2_O3), .pin19(REG_2_O7),
    .pin18(DATA_BUS_IN[7]), .pin17(DATA_BUS_IN[6]), .pin16(REG_2_O6), .pin15(REG_2_O5),
    .pin14(DATA_BUS_IN[5]), .pin13(DATA_BUS_IN[4]), .pin12(REG_2_O4), .pin11(CLOCK));
  _74244 #(.ShowInternalStructure("true")) u_74244_3 (
    .pin1(R_REG_2), .pin2(REG_2_O0), .pin3(DATA_BUS_IN[7]), .pin4(REG_2_O1), .pin5(DATA_BUS_IN[6]),
    .pin6(REG_2_O2), .pin7(DATA_BUS_IN[5]), .pin8(REG_2_O3), .pin9(DATA_BUS_IN[4]), .pin19(R_REG_2),
    .pin18(DATA_BUS_IN[0]), .pin17(REG_2_O7), .pin16(DATA_BUS_IN[1]), .pin15(REG_2_O6),
    .pin14(DATA_BUS_IN[2]), .pin13(REG_2_O5), .pin12(DATA_BUS_IN[3]), .pin11(REG_2_O4));
  _7424 #(.ShowInternalStructure("true")) u_7424_2 (
    .pin1(READ), .pin2(n_REG_0), .pin3(R_REG_0), .pin4(READ), .pin5(n_REG_1), .pin6(R_REG_1), .pin13(READ),
    .pin12(n_REG_3), .pin11(R_REG_3), .pin10(READ), .pin9(n_REG_2), .pin8(R_REG_2));
  _74377 #(.ShowInternalStructure("true")) u_74377_4 (
    .pin1(W_REG_3), .pin2(REG_3_O0), .pin3(DATA_BUS_IN[0]), .pin4(DATA_BUS_IN[1]), .pin5(REG_3_O1),
    .pin6(REG_3_O2), .pin7(DATA_BUS_IN[2]), .pin8(DATA_BUS_IN[3]), .pin9(REG_3_O3), .pin19(REG_3_O7),
    .pin18(DATA_BUS_IN[7]), .pin17(DATA_BUS_IN[6]), .pin16(REG_3_O6), .pin15(REG_3_O5),
    .pin14(DATA_BUS_IN[5]), .pin13(DATA_BUS_IN[4]), .pin12(REG_3_O4), .pin11(CLOCK));
  _74244 #(.ShowInternalStructure("true")) u_74244_4 (
    .pin1(R_REG_3), .pin2(REG_3_O0), .pin3(DATA_BUS_IN[7]), .pin4(REG_3_O1), .pin5(DATA_BUS_IN[6]),
    .pin6(REG_3_O2), .pin7(DATA_BUS_IN[5]), .pin8(REG_3_O3), .pin9(DATA_BUS_IN[4]), .pin19(R_REG_3),
    .pin18(DATA_BUS_IN[0]), .pin17(REG_3_O7), .pin16(DATA_BUS_IN[1]), .pin15(REG_3_O6),
    .pin14(DATA_BUS_IN[2]), .pin13(REG_3_O5), .pin12(DATA_BUS_IN[3]), .pin11(REG_3_O4));

  assign DATA_BUS_OUT = DATA_BUS_IN;

  // Other names for the same wires on the sheet: DATA_BUS[7:0] = DATA_BUS_IN; IQ0 = DATA_BUS_IN[0];
  //   IQ1 = DATA_BUS_IN[1]; IQ2 = DATA_BUS_IN[2]; IQ3 = DATA_BUS_IN[3]; IQ4 = DATA_BUS_IN[4]; IQ5 = DATA_BUS_IN[5];
  //   IQ6 = DATA_BUS_IN[6]; IQ7 = DATA_BUS_IN[7]; RN0 = REG_NUMBER[0]; RN1 = REG_NUMBER[1]
endmodule
