// Logisim project PC_with_ROM_CU_test_USER_REGISTERS.circ as structural Verilog
module CPU (
  output O_Clock,
  output [15:0] AddressMemory
);

  wire ALU_SUM_CARRY_FLAG, CARRY, CommandsCounter_n_Clear, CommandsCounter_n_Enable_Counter,
       CommandsCounter_n_Enable_Load, CurrentAddressRegister_n_EN1, CurrentAddressRegister_n_EN2,
       CurrentAddressRegister_n_EN_Out, FLASH_CE, FLASH_OE, FLASH_WE, FM_ADDRESS_REGISTER_SELECT_0,
       FM_ADDRESS_REGISTER_SELECT_1, FM_REG_1, FM_REG_2, FM_REG_3, IN_REG_0_O0, IN_REG_0_O1, IN_REG_0_O2,
       IN_REG_0_O3, IN_REG_0_O4, IN_REG_0_O5, IN_REG_0_O6, IN_REG_0_O7, MCA1, MCA2, MCA3, MCA4, MCA5, MCA6,
       MCA7, MCA8, MCA9, MCA10, MCA11, MCA12, MCA13, MCA14, MCA15, MCA16, MEMORY_CE, MEMORY_OE, MEMORY_WE,
       MicroCommandsCounter_n_Clear, MicroCommandsCounter_n_Enable_Counter,
       MicroCommandsCounter_n_Enable_Load, n7427_1_pin8, n7427_1_pin9, n7427_1_pin10, n7427_1_pin11,
       n74139_1_pin4, n74139_1_pin9, n74139_1_pin10, n74139_1_pin11, n74139_1_pin12, n74139_1_pin13,
       n74139_1_pin14, n74139_1_pin15, n74377_4_pin9, n74377_4_pin12, n74377_4_pin13, n74377_4_pin14,
       n74377_4_pin15, n74377_4_pin16, n74377_4_pin17, n74377_4_pin18, n74377_4_pin19, n_ALU_AND_EN,
       n_ALU_NOT_EN, n_ALU_OR_EN, n_ALU_SHL_EN, n_ALU_SHR_EN, n_ALU_SUM_EN, n_ALU_XOR_EN, n_B13,
       n_R_INNER_REG, n_REG_A_EN, n_REG_B_EN, n_W_INNER_REG, NEGATIVE, not_1_out, not_2_out, not_3_out,
       not_4_out, OpcodeRegister_n_EN1, OpcodeRegister_n_EN2, OpcodeRegister_n_EN_Out, OVERFLOW,
       pull_resistor_4_node, pull_resistor_5_node, pull_resistor_6_node, pull_resistor_7_node, R_INNER_REG,
       R_UREG_0, R_UREG_1, R_UREG_2, RAM_CE, RAM_EN, RAM_OE, RAM_WE, REG_A_EN, REG_B_EN, ROM_EN, ROM_OE,
       UserAddressRegister_n_EN1, UserAddressRegister_n_EN2, UserAddressRegister_n_EN_Out,
       UserRegistersBlock_READ, UserRegistersBlock_WRITE, W_INNER_REG, W_UREG_0, W_UREG_1, W_UREG_2, ZERO;
  wire [2:0] ALU_MODE;
  wire [7:0] DATA_BUS;
  wire [18:0] FLASH_MEMORY_ADDRESS_BUS;

  // Probe on DATA_BUS
  Clock clock_1 (.out(O_Clock));
  CU cu_1 (
    .MicroCommandAddress({MCA16, MCA15, MCA14, MCA13, MCA12, MCA11, MCA10, MCA9, MCA8, MCA7, MCA6, MCA5, MCA4, MCA3, MCA2, MCA1}),
    .ZERO(ZERO), .OVERFLOW(OVERFLOW), .NEGATIVE(NEGATIVE), .CARRY(CARRY),
    .OpcodeRegister_n_EN1(OpcodeRegister_n_EN1), .OpcodeRegister_n_EN2(OpcodeRegister_n_EN2),
    .OpcodeRegister_n_EN_Out(OpcodeRegister_n_EN_Out), .UserAddressRegister_n_EN1(UserAddressRegister_n_EN1),
    .UserAddressRegister_n_EN2(UserAddressRegister_n_EN2),
    .UserAddressRegister_n_EN_Out(UserAddressRegister_n_EN_Out),
    .CurrentAddressRegister_n_EN1(CurrentAddressRegister_n_EN1),
    .CurrentAddressRegister_n_EN2(CurrentAddressRegister_n_EN2),
    .CurrentAddressRegister_n_EN_Out(CurrentAddressRegister_n_EN_Out),
    .MicroCommandsCounter_n_Enable_Counter(MicroCommandsCounter_n_Enable_Counter),
    .MicroCommandsCounter_n_Clear(MicroCommandsCounter_n_Clear),
    .MicroCommandsCounter_n_Enable_Load(MicroCommandsCounter_n_Enable_Load),
    .CommandsCounter_n_Enable_Counter(CommandsCounter_n_Enable_Counter),
    .CommandsCounter_n_Clear(CommandsCounter_n_Clear),
    .CommandsCounter_n_Enable_Load(CommandsCounter_n_Enable_Load),
    .UserRegistersBlock_READ(UserRegistersBlock_READ), .UserRegistersBlock_WRITE(UserRegistersBlock_WRITE),
    .W_UREG_0(W_UREG_0), .W_UREG_1(W_UREG_1), .W_UREG_2(W_UREG_2), .R_UREG_0(R_UREG_0), .R_UREG_1(R_UREG_1),
    .R_UREG_2(R_UREG_2), .W_INNER_REG(W_INNER_REG), .R_INNER_REG(R_INNER_REG), .MEMORY_WE(MEMORY_WE),
    .MEMORY_OE(MEMORY_OE), .MEMORY_CE(MEMORY_CE), .FLASH_WE(FLASH_WE), .FLASH_OE(FLASH_OE),
    .FLASH_CE(FLASH_CE), .FM_ADDRESS_REGISTER_SELECT_0(FM_ADDRESS_REGISTER_SELECT_0),
    .FM_ADDRESS_REGISTER_SELECT_1(FM_ADDRESS_REGISTER_SELECT_1), .REG_A_EN(REG_A_EN), .REG_B_EN(REG_B_EN),
    .ALU_MODE(ALU_MODE));
  _7419 #(.ShowInternalStructure("true")) u_7419_1 (
    .pin1(W_INNER_REG), .pin2(n_W_INNER_REG), .pin3(R_INNER_REG), .pin4(n_R_INNER_REG),
    .pin5(AddressMemory[13]), .pin6(n_B13));  // open: pin13, pin12, pin11, pin10, pin9, pin8
  _7427 #(.ShowInternalStructure("true")) u_7427_1 (
    .pin1(AddressMemory[14]), .pin2(AddressMemory[13]), .pin3(n_B13), .pin4(AddressMemory[14]),
    .pin5(AddressMemory[15]), .pin6(RAM_EN), .pin13(AddressMemory[15]), .pin12(ROM_EN),
    .pin11(n7427_1_pin11), .pin10(n7427_1_pin10), .pin9(n7427_1_pin9), .pin8(n7427_1_pin8));
  _7400 #(.ShowInternalStructure("true")) u_7400_1 (
    .pin1(ROM_EN), .pin2(MEMORY_OE), .pin3(ROM_OE), .pin4(RAM_EN), .pin5(MEMORY_OE), .pin6(RAM_OE),
    .pin13(RAM_EN), .pin12(MEMORY_WE), .pin11(RAM_WE), .pin10(RAM_EN), .pin9(MEMORY_CE), .pin8(RAM_CE));
  Pull_Resistor pull_resistor_1 (.node(n7427_1_pin11));
  Pull_Resistor pull_resistor_2 (.node(n7427_1_pin10));
  Pull_Resistor pull_resistor_3 (.node(n7427_1_pin9));
  // NoConnect on n7427_1_pin8
  ALU_V2_test alu_v2_test_1 (
    .B1(DATA_BUS[0]), .B2(DATA_BUS[1]), .B3(DATA_BUS[2]), .B4(DATA_BUS[3]), .B5(DATA_BUS[4]),
    .B6(DATA_BUS[5]), .B7(DATA_BUS[6]), .B8(DATA_BUS[7]), .EN_A(n_REG_A_EN), .EN_B(n_REG_B_EN),
    .CLK(O_Clock), .SL1(ALU_MODE[0]), .SL2(ALU_MODE[1]), .SL3(ALU_MODE[2]), .O1(DATA_BUS[0]),
    .O2(DATA_BUS[1]), .O3(DATA_BUS[2]), .O4(DATA_BUS[3]), .O5(DATA_BUS[4]), .O6(DATA_BUS[5]),
    .O7(DATA_BUS[6]), .O8(DATA_BUS[7]), .n_SUM_EN(n_ALU_SUM_EN), .n_AND_EN(n_ALU_AND_EN),
    .n_OR_EN(n_ALU_OR_EN), .n_NOT_EN(n_ALU_NOT_EN), .n_XOR_EN(n_ALU_XOR_EN), .n_SHL_EN(n_ALU_SHL_EN),
    .n_SHR_EN(n_ALU_SHR_EN), .F_CARRY(ALU_SUM_CARRY_FLAG));
  USER_REGISTER_BLOCK user_register_block_1 (
    .CLK(O_Clock), .B_1(DATA_BUS[0]), .B_2(DATA_BUS[1]), .B_3(DATA_BUS[2]), .B_4(DATA_BUS[3]),
    .B_5(DATA_BUS[4]), .B_6(DATA_BUS[5]), .B_7(DATA_BUS[6]), .B_8(DATA_BUS[7]), .W_UREG_0(W_UREG_0),
    .W_UREG_1(W_UREG_1), .W_UREG_2(W_UREG_2), .R_UREG_0(R_UREG_0), .R_UREG_1(R_UREG_1), .R_UREG_2(R_UREG_2),
    .URB_READ(UserRegistersBlock_READ), .URB_WRITE(UserRegistersBlock_WRITE), .OB_1(DATA_BUS[0]),
    .OB_2(DATA_BUS[1]), .OB_3(DATA_BUS[2]), .OB_4(DATA_BUS[3]), .OB_5(DATA_BUS[4]), .OB_6(DATA_BUS[5]),
    .OB_7(DATA_BUS[6]), .OB_8(DATA_BUS[7]));
  Pull_Resistor pull_resistor_4 (.node(pull_resistor_4_node));
  not not_1 (not_1_out, ROM_OE);
  not not_2 (not_2_out, 1'b1);
  RAM #(.addrWidth(13), .databus("bidir"), .enables("line"), .trigger("low")) ROM_AT28C64B (
    .addr(AddressMemory[12:0]), .we(not_2_out), .oe(not_1_out), .clk(pull_resistor_4_node), .data(DATA_BUS));
  _74377 #(.ShowInternalStructure("true")) u_74377_1 (
    .pin1(n_W_INNER_REG), .pin2(IN_REG_0_O0), .pin3(DATA_BUS[0]), .pin4(DATA_BUS[1]), .pin5(IN_REG_0_O1),
    .pin6(IN_REG_0_O2), .pin7(DATA_BUS[2]), .pin8(DATA_BUS[3]), .pin9(IN_REG_0_O3), .pin19(IN_REG_0_O7),
    .pin18(DATA_BUS[7]), .pin17(DATA_BUS[6]), .pin16(IN_REG_0_O6), .pin15(IN_REG_0_O5), .pin14(DATA_BUS[5]),
    .pin13(DATA_BUS[4]), .pin12(IN_REG_0_O4), .pin11(O_Clock));
  _74244 #(.ShowInternalStructure("true")) u_74244_1 (
    .pin1(n_R_INNER_REG), .pin2(IN_REG_0_O0), .pin3(DATA_BUS[7]), .pin4(IN_REG_0_O1), .pin5(DATA_BUS[6]),
    .pin6(IN_REG_0_O2), .pin7(DATA_BUS[5]), .pin8(IN_REG_0_O3), .pin9(DATA_BUS[4]), .pin19(n_R_INNER_REG),
    .pin18(DATA_BUS[0]), .pin17(IN_REG_0_O7), .pin16(DATA_BUS[1]), .pin15(IN_REG_0_O6), .pin14(DATA_BUS[2]),
    .pin13(IN_REG_0_O5), .pin12(DATA_BUS[3]), .pin11(IN_REG_0_O4));
  FLAGS_test flags_test_1 (
    .F_CARRY(ALU_SUM_CARRY_FLAG), .n_SUM_EN(n_ALU_SUM_EN), .n_AND_EN(n_ALU_AND_EN), .n_OR_EN(n_ALU_OR_EN),
    .n_NOT_EN(n_ALU_NOT_EN), .n_XOR_EN(n_ALU_XOR_EN), .n_SHL_EN(n_ALU_SHL_EN), .n_SHR_EN(n_ALU_SHR_EN),
    .B1(DATA_BUS[0]), .B2(DATA_BUS[1]), .B3(DATA_BUS[2]), .B4(DATA_BUS[3]), .B5(DATA_BUS[4]),
    .B6(DATA_BUS[5]), .B7(DATA_BUS[6]), .B8(DATA_BUS[7]), .CLK(O_Clock), .ZERO(ZERO), .NEGATIVE(NEGATIVE),
    .CARRY(CARRY), .OVERFLOW(OVERFLOW));
  not not_3 (not_3_out, RAM_OE);
  not not_4 (not_4_out, RAM_WE);
  RAM #(.addrWidth(15), .databus("bidir"), .enables("line"), .trigger("low")) SRAM_AS6C62256 (
    .addr(AddressMemory[14:0]), .we(not_4_out), .oe(not_3_out), .clk(RAM_CE), .data(DATA_BUS));
  COUNTERS_test counters_test_1 (
    .CLK(O_Clock), .B1(DATA_BUS[0]), .B2(DATA_BUS[1]), .B3(DATA_BUS[2]), .B4(DATA_BUS[3]), .B5(DATA_BUS[4]),
    .B6(DATA_BUS[5]), .B7(DATA_BUS[6]), .B8(DATA_BUS[7]),
    .MC_n_Enable_Counter(MicroCommandsCounter_n_Enable_Counter), .MC_c_Clear(MicroCommandsCounter_n_Clear),
    .MC_n_Enable_Load(MicroCommandsCounter_n_Enable_Load),
    .C_n_Enable_Counter(CommandsCounter_n_Enable_Counter), .C_n_Clear(CommandsCounter_n_Clear),
    .C_n_Enable_Load(CommandsCounter_n_Enable_Load), .OR_n_EN1(OpcodeRegister_n_EN1),
    .OR_n_EN2(OpcodeRegister_n_EN2), .OR_n_EN_Out(OpcodeRegister_n_EN_Out),
    .UAR_n_EN1(UserAddressRegister_n_EN1), .UAR_n_EN2(UserAddressRegister_n_EN2),
    .UAR_n_EN_Out(UserAddressRegister_n_EN_Out), .CAR_n_EN1(CurrentAddressRegister_n_EN1),
    .CAR_n_EN2(CurrentAddressRegister_n_EN2), .CAR_n_EN_Out(CurrentAddressRegister_n_EN_Out), .MCA1(MCA1),
    .AB1(AddressMemory[0]), .MCA2(MCA2), .AB2(AddressMemory[1]), .MCA3(MCA3), .AB3(AddressMemory[2]),
    .MCA4(MCA4), .AB4(AddressMemory[3]), .MCA5(MCA5), .AB5(AddressMemory[4]), .MCA6(MCA6),
    .AB6(AddressMemory[5]), .MCA7(MCA7), .AB7(AddressMemory[6]), .MCA8(MCA8), .AB8(AddressMemory[7]),
    .MCA9(MCA9), .AB9(AddressMemory[8]), .MCA10(MCA10), .AB10(AddressMemory[9]), .MCA11(MCA11),
    .AB11(AddressMemory[10]), .MCA12(MCA12), .AB12(AddressMemory[11]), .MCA13(MCA13),
    .AB13(AddressMemory[12]), .MCA14(MCA14), .AB14(AddressMemory[13]), .MCA15(MCA15),
    .AB15(AddressMemory[14]), .MCA16(MCA16), .AB16(AddressMemory[15]));
  RAM #(.addrWidth(19), .databus("bidir"), .enables("line"), .trigger("low")) FLASH (
    .addr(FLASH_MEMORY_ADDRESS_BUS), .we(FLASH_WE), .oe(FLASH_OE), .clk(FLASH_CE), .data(DATA_BUS));
  _74377 #(.ShowInternalStructure("true")) u_74377_2 (
    .pin1(FM_REG_1), .pin2(FLASH_MEMORY_ADDRESS_BUS[0]), .pin3(DATA_BUS[0]), .pin4(DATA_BUS[1]),
    .pin5(FLASH_MEMORY_ADDRESS_BUS[1]), .pin6(FLASH_MEMORY_ADDRESS_BUS[2]), .pin7(DATA_BUS[2]),
    .pin8(DATA_BUS[3]), .pin9(FLASH_MEMORY_ADDRESS_BUS[3]), .pin19(FLASH_MEMORY_ADDRESS_BUS[7]),
    .pin18(DATA_BUS[7]), .pin17(DATA_BUS[6]), .pin16(FLASH_MEMORY_ADDRESS_BUS[6]),
    .pin15(FLASH_MEMORY_ADDRESS_BUS[5]), .pin14(DATA_BUS[5]), .pin13(DATA_BUS[4]),
    .pin12(FLASH_MEMORY_ADDRESS_BUS[4]), .pin11(O_Clock));
  _74377 #(.ShowInternalStructure("true")) u_74377_3 (
    .pin1(FM_REG_2), .pin2(FLASH_MEMORY_ADDRESS_BUS[8]), .pin3(DATA_BUS[0]), .pin4(DATA_BUS[1]),
    .pin5(FLASH_MEMORY_ADDRESS_BUS[9]), .pin6(FLASH_MEMORY_ADDRESS_BUS[10]), .pin7(DATA_BUS[2]),
    .pin8(DATA_BUS[3]), .pin9(FLASH_MEMORY_ADDRESS_BUS[11]), .pin19(FLASH_MEMORY_ADDRESS_BUS[15]),
    .pin18(DATA_BUS[7]), .pin17(DATA_BUS[6]), .pin16(FLASH_MEMORY_ADDRESS_BUS[14]),
    .pin15(FLASH_MEMORY_ADDRESS_BUS[13]), .pin14(DATA_BUS[5]), .pin13(DATA_BUS[4]),
    .pin12(FLASH_MEMORY_ADDRESS_BUS[12]), .pin11(O_Clock));
  Pull_Resistor pull_resistor_5 (.node(pull_resistor_5_node));
  // NoConnect on n74139_1_pin4
  Pull_Resistor pull_resistor_6 (.node(pull_resistor_6_node));
  Pull_Resistor pull_resistor_7 (.node(pull_resistor_7_node));
  // NoConnect on n74377_4_pin9
  _74139 #(.ShowInternalStructure("true")) u_74139_1 (
    .pin1(pull_resistor_5_node), .pin2(FM_ADDRESS_REGISTER_SELECT_0), .pin3(FM_ADDRESS_REGISTER_SELECT_1),
    .pin4(n74139_1_pin4), .pin5(FM_REG_1), .pin6(FM_REG_2), .pin7(FM_REG_3), .pin15(n74139_1_pin15),
    .pin14(n74139_1_pin14), .pin13(n74139_1_pin13), .pin12(n74139_1_pin12), .pin11(n74139_1_pin11),
    .pin10(n74139_1_pin10), .pin9(n74139_1_pin9));
  Pull_Resistor pull_resistor_8 (.node(n74139_1_pin15));
  Pull_Resistor pull_resistor_9 (.node(n74139_1_pin14));
  Pull_Resistor pull_resistor_10 (.node(n74139_1_pin13));
  // NoConnect on n74139_1_pin12
  // NoConnect on n74139_1_pin11
  // NoConnect on n74139_1_pin10
  // NoConnect on n74139_1_pin9
  _74377 #(.ShowInternalStructure("true")) u_74377_4 (
    .pin1(FM_REG_3), .pin2(FLASH_MEMORY_ADDRESS_BUS[16]), .pin3(DATA_BUS[0]), .pin4(DATA_BUS[1]),
    .pin5(FLASH_MEMORY_ADDRESS_BUS[17]), .pin6(FLASH_MEMORY_ADDRESS_BUS[18]), .pin7(pull_resistor_6_node),
    .pin8(pull_resistor_7_node), .pin9(n74377_4_pin9), .pin19(n74377_4_pin19), .pin18(n74377_4_pin18),
    .pin17(n74377_4_pin17), .pin16(n74377_4_pin16), .pin15(n74377_4_pin15), .pin14(n74377_4_pin14),
    .pin13(n74377_4_pin13), .pin12(n74377_4_pin12), .pin11(O_Clock));
  // NoConnect on n74377_4_pin19
  Pull_Resistor pull_resistor_11 (.node(n74377_4_pin18));
  Pull_Resistor pull_resistor_12 (.node(n74377_4_pin17));
  // NoConnect on n74377_4_pin16
  // NoConnect on n74377_4_pin15
  Pull_Resistor pull_resistor_13 (.node(n74377_4_pin14));
  Pull_Resistor pull_resistor_14 (.node(n74377_4_pin13));
  // NoConnect on n74377_4_pin12

  // Other names for the same wires on the sheet: AB16 = AddressMemory[15]; ADDRESS_BUS[15:0] = AddressMemory;
  //   B15 = AddressMemory[15]; AB1 = AddressMemory[0]; ADDRESS_BUS_RAM[14:0] = AddressMemory[14:0];
  //   ADDRESS_BUS_ROM[12:0] = AddressMemory[12:0]; B0 = AddressMemory[0]; AB2 = AddressMemory[1];
  //   B1 = AddressMemory[1]; AB3 = AddressMemory[2]; B2 = AddressMemory[2]; AB4 = AddressMemory[3];
  //   B3 = AddressMemory[3]; AB5 = AddressMemory[4]; B4 = AddressMemory[4]; AB6 = AddressMemory[5];
  //   B5 = AddressMemory[5]; AB7 = AddressMemory[6]; B6 = AddressMemory[6]; AB8 = AddressMemory[7];
  //   B7 = AddressMemory[7]; AB9 = AddressMemory[8]; B8 = AddressMemory[8]; AB10 = AddressMemory[9];
  //   B9 = AddressMemory[9]; AB11 = AddressMemory[10]; B10 = AddressMemory[10]; AB12 = AddressMemory[11];
  //   B11 = AddressMemory[11]; AB13 = AddressMemory[12]; B12 = AddressMemory[12]; AB14 = AddressMemory[13];
  //   B13 = AddressMemory[13]; AB15 = AddressMemory[14]; B14 = AddressMemory[14]; AMA = ALU_MODE[0];
  //   AMB = ALU_MODE[1]; AMC = ALU_MODE[2]; CPU_Clock = O_Clock; IQ0 = DATA_BUS[0]; IQ1 = DATA_BUS[1];
  //   IQ2 = DATA_BUS[2]; IQ3 = DATA_BUS[3]; IQ4 = DATA_BUS[4]; IQ5 = DATA_BUS[5]; IQ6 = DATA_BUS[6];
  //   IQ7 = DATA_BUS[7]; FM0 = FLASH_MEMORY_ADDRESS_BUS[0]; FM1 = FLASH_MEMORY_ADDRESS_BUS[1];
  //   FM2 = FLASH_MEMORY_ADDRESS_BUS[2]; FM3 = FLASH_MEMORY_ADDRESS_BUS[3]; FM4 = FLASH_MEMORY_ADDRESS_BUS[4];
  //   FM5 = FLASH_MEMORY_ADDRESS_BUS[5]; FM6 = FLASH_MEMORY_ADDRESS_BUS[6]; FM7 = FLASH_MEMORY_ADDRESS_BUS[7];
  //   FM8 = FLASH_MEMORY_ADDRESS_BUS[8]; FM9 = FLASH_MEMORY_ADDRESS_BUS[9]; FM10 = FLASH_MEMORY_ADDRESS_BUS[10];
  //   FM11 = FLASH_MEMORY_ADDRESS_BUS[11]; FM12 = FLASH_MEMORY_ADDRESS_BUS[12]; FM13 = FLASH_MEMORY_ADDRESS_BUS[13];
  //   FM14 = FLASH_MEMORY_ADDRESS_BUS[14]; FM15 = FLASH_MEMORY_ADDRESS_BUS[15]; FM16 = FLASH_MEMORY_ADDRESS_BUS[16];
  //   FM17 = FLASH_MEMORY_ADDRESS_BUS[17]; FM18 = FLASH_MEMORY_ADDRESS_BUS[18];
  //   MicroCommandAddress[15:0] = {MCA16, MCA15, MCA14, MCA13, MCA12, MCA11, MCA10, MCA9, MCA8, MCA7, MCA6, MCA5, MCA4, MCA3, MCA2, MCA1}

  // Notes on the sheet:
  //   ALU Device
  //   ROM/RAM ENABLING
  //   USER REGISTER BLOCK
  //   FLAGS REGISTER
  //   INNER REGISTER
  //   COUNTERS
endmodule

module CU (
  input  [15:0] MicroCommandAddress,
  input  ZERO,
  input  OVERFLOW,
  input  NEGATIVE,
  input  CARRY,
  output OpcodeRegister_n_EN1,
  output OpcodeRegister_n_EN2,
  output OpcodeRegister_n_EN_Out,
  output UserAddressRegister_n_EN1,
  output UserAddressRegister_n_EN2,
  output UserAddressRegister_n_EN_Out,
  output CurrentAddressRegister_n_EN1,
  output CurrentAddressRegister_n_EN2,
  output CurrentAddressRegister_n_EN_Out,
  output MicroCommandsCounter_n_Enable_Counter,
  output MicroCommandsCounter_n_Clear,
  output MicroCommandsCounter_n_Enable_Load,
  output CommandsCounter_n_Enable_Counter,
  output CommandsCounter_n_Clear,
  output CommandsCounter_n_Enable_Load,
  output UserRegistersBlock_READ,
  output UserRegistersBlock_WRITE,
  output W_UREG_0,
  output W_UREG_1,
  output W_UREG_2,
  output R_UREG_0,
  output R_UREG_1,
  output R_UREG_2,
  output W_INNER_REG,
  output R_INNER_REG,
  output MEMORY_WE,
  output MEMORY_OE,
  output MEMORY_CE,
  output FLASH_WE,
  output FLASH_OE,
  output FLASH_CE,
  output FM_ADDRESS_REGISTER_SELECT_0,
  output FM_ADDRESS_REGISTER_SELECT_1,
  output REG_A_EN,
  output REG_B_EN,
  output [2:0] ALU_MODE
);

  wire A0, A1, A2, A3, CC, CC_CS_NE_DEF_EQ, CommandsCounter_n_Enable_Load_t, CS, CS_NE_DEF_EQ, DEF_EQ,
       EN_USER_ADDRESS_LOADING, ENUAL_NOR_CCEL, ENUAL_NOR_UAREO, EQ, GE, GE_LS_HI_VC_PL_MI_CC_CS_NE_DEF_EQ,
       GT, GT_LT_GE_LS_HI_VC_PL_MI_CC_CS_NE_DEF_EQ, HI, HI_1, HI_2, HI_VC_PL_MI_CC_CS_NE_DEF_EQ, LE, LS,
       LS_HI_VC_PL_MI_CC_CS_NE_DEF_EQ, LT, LT_GE_LS_HI_VC_PL_MI_CC_CS_NE_DEF_EQ, MI, MI_CC_CS_NE_DEF_EQ,
       MUL_0, MUL_1, MUL_2, MUL_3, MUL_4, MUL_5, MUL_6, MUL_7, MUL_8, MUL_9, MUL_10, MUL_11, MUL_12, MUL_13,
       MUL_14, MUL_15, MUL_CC_OUT, MUL_CS_OUT, MUL_DEF_OUT, MUL_EQ_OUT, MUL_GE_OUT, MUL_GT_OUT, MUL_HI_OUT,
       MUL_LE_OUT, MUL_LS_OUT, MUL_LT_OUT, MUL_MI_OUT, MUL_NE_OUT, MUL_PL_OUT, MUL_VC_OUT, MUL_VS_OUT,
       n7408_1_pin2, n7408_1_pin12, n7408_2_pin2, n7408_3_pin1, n7408_6_pin8, n7408_6_pin9, n7408_6_pin10,
       n7424_1_pin2, n7424_1_pin4, n7424_1_pin5, n7424_1_pin6, n7424_1_pin8, n7424_1_pin9, n7424_1_pin10,
       n7424_1_pin11, n7424_1_pin12, n7424_1_pin13, n7432_1_pin8, n7432_1_pin9, n7432_1_pin10, n7432_1_pin11,
       n7432_1_pin12, n7432_1_pin13, n7432_2_pin9, n7432_2_pin10, n7436_1_pin9, n7436_1_pin12, n7436_2_pin8,
       n7436_2_pin9, n7436_2_pin10, n7436_2_pin11, n7436_2_pin12, n7436_2_pin13, n7486_1_pin8, n7486_1_pin9,
       n7486_1_pin10, n7486_1_pin11, n7486_1_pin12, n7486_1_pin13, n74138_1_pin5, n74138_1_pin6,
       n74138_2_pin5, n_A3, n_GE, n_MUL_0, n_MUL_1, n_MUL_2, n_MUL_3, n_MUL_4, n_MUL_5, n_MUL_6, n_MUL_7,
       n_MUL_8, n_MUL_9, n_MUL_10, n_MUL_11, n_MUL_12, n_MUL_13, n_MUL_14, n_MUL_15, NE, NE_DEF_EQ, PL,
       PL_MI_CC_CS_NE_DEF_EQ, pull_resistor_1_node, pull_resistor_2_node, VC, VC_PL_MI_CC_CS_NE_DEF_EQ, VS,
       VS_PL_MI_CC_CS_NE_DEF_EQ;
  wire [2:2] ControlSignals_1;
  wire [5:0] ControlSignals_6;

  Pull_Resistor pull_resistor_1 (.node(pull_resistor_1_node));
  Pull_Resistor pull_resistor_2 (.node(pull_resistor_2_node));
  _7408 #(.ShowInternalStructure("true")) u_7408_1 (
    .pin1(ZERO), .pin2(n7408_1_pin2), .pin3(EQ), .pin4(CARRY), .pin5(n7408_1_pin2), .pin6(CS),
    .pin13(NEGATIVE), .pin12(n7408_1_pin12), .pin11(MI), .pin10(OVERFLOW), .pin9(n7408_1_pin12), .pin8(VS));
  _7436 #(.ShowInternalStructure("true")) u_7436_1 (
    .pin1(ZERO), .pin2(pull_resistor_1_node), .pin3(NE), .pin4(CARRY), .pin5(pull_resistor_2_node),
    .pin6(CC), .pin13(NEGATIVE), .pin12(n7436_1_pin12), .pin11(PL), .pin10(OVERFLOW), .pin9(n7436_1_pin9),
    .pin8(VC));
  _74138 #(.ShowInternalStructure("true")) u_74138_1 (
    .pin1(A0), .pin2(A1), .pin3(A2), .pin4(A3), .pin5(n74138_1_pin5), .pin6(n74138_1_pin6), .pin7(MUL_7),
    .pin15(MUL_0), .pin14(MUL_1), .pin13(MUL_2), .pin12(MUL_3), .pin11(MUL_4), .pin10(MUL_5), .pin9(MUL_6));
  Pull_Resistor pull_resistor_3 (.node(n74138_1_pin5));
  _74138 #(.ShowInternalStructure("true")) u_74138_2 (
    .pin1(A0), .pin2(A1), .pin3(A2), .pin4(n_A3), .pin5(n74138_2_pin5), .pin6(n74138_1_pin6), .pin7(MUL_15),
    .pin15(MUL_8), .pin14(MUL_9), .pin13(MUL_10), .pin12(MUL_11), .pin11(MUL_12), .pin10(MUL_13),
    .pin9(MUL_14));
  Pull_Resistor pull_resistor_4 (.node(n74138_2_pin5));
  _7404 #(.ShowInternalStructure("true")) u_7404_1 (
    .pin1(A3), .pin2(n_A3), .pin3(MUL_0), .pin4(n_MUL_0), .pin5(MUL_1), .pin6(n_MUL_1), .pin13(MUL_2),
    .pin12(n_MUL_2), .pin11(MUL_3), .pin10(n_MUL_3), .pin9(MUL_4), .pin8(n_MUL_4));
  _7404 #(.ShowInternalStructure("true")) u_7404_2 (
    .pin1(MUL_5), .pin2(n_MUL_5), .pin3(MUL_6), .pin4(n_MUL_6), .pin5(MUL_7), .pin6(n_MUL_7), .pin13(MUL_8),
    .pin12(n_MUL_8), .pin11(MUL_9), .pin10(n_MUL_9), .pin9(MUL_10), .pin8(n_MUL_10));
  _7404 #(.ShowInternalStructure("true")) u_7404_3 (
    .pin1(MUL_11), .pin2(n_MUL_11), .pin3(MUL_12), .pin4(n_MUL_12), .pin5(MUL_13), .pin6(n_MUL_13),
    .pin13(MUL_14), .pin12(n_MUL_14), .pin11(MUL_15), .pin10(n_MUL_15), .pin9(n_GE), .pin8(GE));
  _7436 #(.ShowInternalStructure("true")) u_7436_2 (
    .pin1(EN_USER_ADDRESS_LOADING), .pin2(ControlSignals_1[2]), .pin3(ENUAL_NOR_UAREO),
    .pin4(EN_USER_ADDRESS_LOADING), .pin5(CommandsCounter_n_Enable_Load_t), .pin6(ENUAL_NOR_CCEL),
    .pin13(n7436_2_pin13), .pin12(n7436_2_pin12), .pin11(n7436_2_pin11), .pin10(n7436_2_pin10),
    .pin9(n7436_2_pin9), .pin8(n7436_2_pin8));
  _7432 #(.ShowInternalStructure("true")) u_7432_1 (
    .pin1(ControlSignals_1[2]), .pin2(ENUAL_NOR_UAREO), .pin3(UserAddressRegister_n_EN_Out),
    .pin4(CommandsCounter_n_Enable_Load_t), .pin5(ENUAL_NOR_CCEL), .pin6(CommandsCounter_n_Enable_Load),
    .pin13(n7432_1_pin13), .pin12(n7432_1_pin12), .pin11(n7432_1_pin11), .pin10(n7432_1_pin10),
    .pin9(n7432_1_pin9), .pin8(n7432_1_pin8));
  Pull_Resistor pull_resistor_5 (.node(n7436_1_pin12));
  Pull_Resistor pull_resistor_6 (.node(n7436_1_pin9));
  Pull_Resistor pull_resistor_7 (.node(n7436_2_pin13));
  Pull_Resistor pull_resistor_8 (.node(n7436_2_pin12));
  Pull_Resistor pull_resistor_9 (.node(n7436_2_pin10));
  Pull_Resistor pull_resistor_10 (.node(n7436_2_pin9));
  Pull_Resistor pull_resistor_11 (.node(n7432_1_pin13));
  Pull_Resistor pull_resistor_12 (.node(n7432_1_pin12));
  Pull_Resistor pull_resistor_13 (.node(n7432_1_pin10));
  Pull_Resistor pull_resistor_14 (.node(n7432_1_pin9));
  // NoConnect on n7436_2_pin11
  // NoConnect on n7436_2_pin8
  // NoConnect on n7432_1_pin11
  // NoConnect on n7432_1_pin8
  _7424 #(.ShowInternalStructure("true")) u_7424_1 (
    .pin1(ZERO), .pin2(n7424_1_pin2), .pin3(HI_1), .pin4(n7424_1_pin4), .pin5(n7424_1_pin5),
    .pin6(n7424_1_pin6), .pin13(n7424_1_pin13), .pin12(n7424_1_pin12), .pin11(n7424_1_pin11),
    .pin10(n7424_1_pin10), .pin9(n7424_1_pin9), .pin8(n7424_1_pin8));
  Pull_Resistor pull_resistor_15 (.node(n7424_1_pin2));
  Pull_Resistor pull_resistor_16 (.node(n7424_1_pin4));
  Pull_Resistor pull_resistor_17 (.node(n7424_1_pin5));
  // NoConnect on n7424_1_pin6
  _7408 #(.ShowInternalStructure("true")) u_7408_2 (
    .pin1(CARRY), .pin2(n7408_2_pin2), .pin3(HI_2), .pin4(HI_1), .pin5(HI_2), .pin6(HI), .pin13(NE),
    .pin12(GE), .pin11(GT), .pin10(EQ), .pin9(LT), .pin8(LE));
  _7486 #(.ShowInternalStructure("true")) u_7486_1 (
    .pin1(OVERFLOW), .pin2(NEGATIVE), .pin3(n_GE), .pin4(OVERFLOW), .pin5(NEGATIVE), .pin6(LT),
    .pin13(n7486_1_pin13), .pin12(n7486_1_pin12), .pin11(n7486_1_pin11), .pin10(n7486_1_pin10),
    .pin9(n7486_1_pin9), .pin8(n7486_1_pin8));
  Pull_Resistor pull_resistor_18 (.node(n7424_1_pin13));
  Pull_Resistor pull_resistor_19 (.node(n7424_1_pin12));
  // NoConnect on n7424_1_pin11
  Pull_Resistor pull_resistor_20 (.node(n7424_1_pin10));
  Pull_Resistor pull_resistor_21 (.node(n7424_1_pin9));
  // NoConnect on n7424_1_pin8
  Pull_Resistor pull_resistor_22 (.node(n7486_1_pin13));
  Pull_Resistor pull_resistor_23 (.node(n7486_1_pin12));
  // NoConnect on n7486_1_pin11
  Pull_Resistor pull_resistor_24 (.node(n7486_1_pin10));
  Pull_Resistor pull_resistor_25 (.node(n7486_1_pin9));
  // NoConnect on n7486_1_pin8
  _7408 #(.ShowInternalStructure("true")) u_7408_3 (
    .pin1(n7408_3_pin1), .pin2(n_MUL_0), .pin3(MUL_DEF_OUT), .pin4(EQ), .pin5(n_MUL_1), .pin6(MUL_EQ_OUT),
    .pin13(NE), .pin12(n_MUL_2), .pin11(MUL_NE_OUT), .pin10(CS), .pin9(n_MUL_3), .pin8(MUL_CS_OUT));
  _7408 #(.ShowInternalStructure("true")) u_7408_4 (
    .pin1(CC), .pin2(n_MUL_4), .pin3(MUL_CC_OUT), .pin4(MI), .pin5(n_MUL_5), .pin6(MUL_MI_OUT), .pin13(PL),
    .pin12(n_MUL_6), .pin11(MUL_PL_OUT), .pin10(VS), .pin9(n_MUL_7), .pin8(MUL_VS_OUT));
  _7408 #(.ShowInternalStructure("true")) u_7408_5 (
    .pin1(VC), .pin2(n_MUL_8), .pin3(MUL_VC_OUT), .pin4(HI), .pin5(n_MUL_9), .pin6(MUL_HI_OUT), .pin13(LS),
    .pin12(n_MUL_10), .pin11(MUL_LS_OUT), .pin10(GE), .pin9(n_MUL_11), .pin8(MUL_GE_OUT));
  _7408 #(.ShowInternalStructure("true")) u_7408_6 (
    .pin1(LT), .pin2(n_MUL_12), .pin3(MUL_LT_OUT), .pin4(GT), .pin5(n_MUL_13), .pin6(MUL_GT_OUT), .pin13(LE),
    .pin12(n_MUL_14), .pin11(MUL_LE_OUT), .pin10(n7408_6_pin10), .pin9(n7408_6_pin9), .pin8(n7408_6_pin8));
  Pull_Resistor pull_resistor_26 (.node(n7408_6_pin10));
  Pull_Resistor pull_resistor_27 (.node(n7408_6_pin9));
  // NoConnect on n7408_6_pin8
  ROM #(.addrWidth(16)) ROM_1 (
    .addr(MicroCommandAddress),
    .data({OpcodeRegister_n_EN1, OpcodeRegister_n_EN2, OpcodeRegister_n_EN_Out, UserAddressRegister_n_EN1, UserAddressRegister_n_EN2, ControlSignals_1[2], CurrentAddressRegister_n_EN1, CurrentAddressRegister_n_EN2}));
  ROM #(.addrWidth(16)) ROM_2 (
    .addr(MicroCommandAddress),
    .data({CurrentAddressRegister_n_EN_Out, MicroCommandsCounter_n_Enable_Counter, MicroCommandsCounter_n_Clear, MicroCommandsCounter_n_Enable_Load, CommandsCounter_n_Enable_Counter, CommandsCounter_n_Clear, CommandsCounter_n_Enable_Load_t, UserRegistersBlock_READ}));
  ROM #(.addrWidth(16)) ROM_3 (
    .addr(MicroCommandAddress),
    .data({UserRegistersBlock_WRITE, W_UREG_0, W_UREG_1, W_UREG_2, R_UREG_0, R_UREG_1, R_UREG_2, W_INNER_REG}));
  ROM #(.addrWidth(16)) ROM_4 (
    .addr(MicroCommandAddress),
    .data({R_INNER_REG, MEMORY_WE, MEMORY_OE, MEMORY_CE, FLASH_WE, FLASH_OE, FLASH_CE, FM_ADDRESS_REGISTER_SELECT_0}));
  ROM #(.addrWidth(16)) ROM_5 (
    .addr(MicroCommandAddress), .data({FM_ADDRESS_REGISTER_SELECT_1, REG_A_EN, REG_B_EN, ALU_MODE, A3, A2}));
  ROM #(.addrWidth(16)) ROM_6 (.addr(MicroCommandAddress), .data({A1, A0, ControlSignals_6}));
  _7432 #(.ShowInternalStructure("true")) u_7432_2 (
    .pin1(LT_GE_LS_HI_VC_PL_MI_CC_CS_NE_DEF_EQ), .pin2(MUL_GT_OUT),
    .pin3(GT_LT_GE_LS_HI_VC_PL_MI_CC_CS_NE_DEF_EQ), .pin4(GT_LT_GE_LS_HI_VC_PL_MI_CC_CS_NE_DEF_EQ),
    .pin5(MUL_LE_OUT), .pin6(EN_USER_ADDRESS_LOADING), .pin13(EQ), .pin12(CC), .pin11(LS),
    .pin10(n7432_2_pin10), .pin9(n7432_2_pin9));  // open: pin8
  _7432 #(.ShowInternalStructure("true")) u_7432_3 (
    .pin1(MUL_DEF_OUT), .pin2(MUL_EQ_OUT), .pin3(DEF_EQ), .pin4(DEF_EQ), .pin5(MUL_NE_OUT), .pin6(NE_DEF_EQ),
    .pin13(NE_DEF_EQ), .pin12(MUL_CS_OUT), .pin11(CS_NE_DEF_EQ), .pin10(CS_NE_DEF_EQ), .pin9(MUL_CC_OUT),
    .pin8(CC_CS_NE_DEF_EQ));
  _7432 #(.ShowInternalStructure("true")) u_7432_4 (
    .pin1(CC_CS_NE_DEF_EQ), .pin2(MUL_MI_OUT), .pin3(MI_CC_CS_NE_DEF_EQ), .pin4(MI_CC_CS_NE_DEF_EQ),
    .pin5(MUL_PL_OUT), .pin6(PL_MI_CC_CS_NE_DEF_EQ), .pin13(PL_MI_CC_CS_NE_DEF_EQ), .pin12(MUL_VS_OUT),
    .pin11(VS_PL_MI_CC_CS_NE_DEF_EQ), .pin10(VS_PL_MI_CC_CS_NE_DEF_EQ), .pin9(MUL_VC_OUT),
    .pin8(VC_PL_MI_CC_CS_NE_DEF_EQ));
  _7432 #(.ShowInternalStructure("true")) u_7432_5 (
    .pin1(VC_PL_MI_CC_CS_NE_DEF_EQ), .pin2(MUL_HI_OUT), .pin3(HI_VC_PL_MI_CC_CS_NE_DEF_EQ),
    .pin4(HI_VC_PL_MI_CC_CS_NE_DEF_EQ), .pin5(MUL_LS_OUT), .pin6(LS_HI_VC_PL_MI_CC_CS_NE_DEF_EQ),
    .pin13(LS_HI_VC_PL_MI_CC_CS_NE_DEF_EQ), .pin12(MUL_GE_OUT), .pin11(GE_LS_HI_VC_PL_MI_CC_CS_NE_DEF_EQ),
    .pin10(GE_LS_HI_VC_PL_MI_CC_CS_NE_DEF_EQ), .pin9(MUL_LT_OUT), .pin8(LT_GE_LS_HI_VC_PL_MI_CC_CS_NE_DEF_EQ));
  Pull_Resistor pull_resistor_28 (.node(n7432_2_pin10));
  Pull_Resistor pull_resistor_29 (.node(n7432_2_pin9));
  // also tied to VCC on the sheet: {n7408_1_pin2, n74138_1_pin6, n7408_1_pin12, n7408_2_pin2, n7408_3_pin1}

  // Other names for the same wires on the sheet: ALU_MODE_1 = ALU_MODE[0];
  //   ControlSignals_5[7:0] = {FM_ADDRESS_REGISTER_SELECT_1, REG_A_EN, REG_B_EN, ALU_MODE, A3, A2};
  //   ALU_MODE_2 = ALU_MODE[1]; ALU_MODE_3 = ALU_MODE[2];
  //   ControlSignals_1 (some bits) = {OpcodeRegister_n_EN1, OpcodeRegister_n_EN2, OpcodeRegister_n_EN_Out, UserAddressRegister_n_EN1, UserAddressRegister_n_EN2, CurrentAddressRegister_n_EN1, CurrentAddressRegister_n_EN2};
  //   UserAddressRegister_n_EN_Out_t = ControlSignals_1[2];
  //   ControlSignals_2[7:0] = {CurrentAddressRegister_n_EN_Out, MicroCommandsCounter_n_Enable_Counter, MicroCommandsCounter_n_Clear, MicroCommandsCounter_n_Enable_Load, CommandsCounter_n_Enable_Counter, CommandsCounter_n_Clear, CommandsCounter_n_Enable_Load_t, UserRegistersBlock_READ};
  //   ControlSignals_3[7:0] = {UserRegistersBlock_WRITE, W_UREG_0, W_UREG_1, W_UREG_2, R_UREG_0, R_UREG_1, R_UREG_2, W_INNER_REG};
  //   ControlSignals_4[7:0] = {R_INNER_REG, MEMORY_WE, MEMORY_OE, MEMORY_CE, FLASH_WE, FLASH_OE, FLASH_CE, FM_ADDRESS_REGISTER_SELECT_0};
  //   ControlSignals_6[7:6] = {A1, A0}; in_CommandsCounter_n_Enable_Load = CommandsCounter_n_Enable_Load;
  //   in_UserAddressRegister_n_EN_Out = UserAddressRegister_n_EN_Out

  // Notes on the sheet:
  //   contents of ROM_1 (hex, n*v repeats v):
  //   fc bc fc 7c dc 15*fc f4 fc ec fc fc fb ff ff fc fc fc f4 fc ec fc fc fb ff ff 71*fc f4 fc ec fb fc
  //   fc f4 fc ec fc fb fc fc f4 fc ec fc fb fc fc f4 fc ec fc fb fc fc f4 fc ec fc fb fc fc f4 fc ec fc
  //   fb fc fc f4 fc ec fc fb fc fc f4 fc ec fc fb fc fc f4 fc ec fc fb fc fc f4 fc ec fc fb fc fc f4 fc
  //   ec fc fb fc fc f4 fc ec fc fb fc fc f4 fc ec fc fb fc fc f4 fc ec fc fb fc fc f4 fc ec fc fb fc
  //   contents of ROM_2 (hex, n*v repeats v):
  //   f6 f6 fe f6 a6 fe f6 fe f6 fe d6 fe f6 fe f6 f7 f6 fe d6 fe f6 fe f6 fe f6 f4 f6 74 fe d6 fe f6 fe
  //   f6 fe f6 f4 f7 74 fe d6 fe f6 fe f6 fe f6 f7 f7 f6 fe d6 fe f6 fe f6 fe f6 f7 f7 f6 fe d6 fe f6 fe
  //   f6 fe f6 f7 f7 f6 fe d6 fe f6 fe f6 f7 f6 fe d6 fe f6 fe f6 fe f6 f7 f7 f6 fe d6 fe f6 fe f6 f7 f6
  //   fe d6 fe f6 fe f6 f7 f6 fe d6 fe f6 fe f6 f4 d6 fe f6 fe f6 fe f4 d6 fe f6 fe f6 fe f4 d6 fe f6 fe
  //   f6 fe f4 d6 fe f6 fe f6 fe f4 d6 fe f6 fe f6 fe f4 d6 fe f6 fe f6 fe f4 d6 fe f6 fe f6 fe f4 d6 fe
  //   f6 fe f6 fe f4 d6 fe f6 fe f6 fe f4 d6 fe f6 fe f6 fe f4 d6 fe f6 fe f6 fe f4 d6 fe f6 fe f6 fe f4
  //   d6 fe f6 fe f6 fe f4 d6 fe f6 fe f6 fe f4 d6
  //   contents of ROM_3 (hex, n*v repeats v):
  //   6*0 40 0 88 0 0 0 40 0 20 9 84 7*0 40 0 88 8*0 40 0 8 4*0 40 0 20 0 10 8 4 82 0 0 0 40 0 20 0 10 8 4
  //   82 0 0 0 40 0 20 0 10 8 4 82 0 0 0 40 0 20 8 84 0 0 0 40 0 20 0 10 8 4 82 0 0 0 40 0 20 8 84 0 0 0
  //   40 0 20 8 84
  //   contents of ROM_4 (hex, n*v repeats v):
  //   0 30 0 30 0 0 30 0 30 0 0 0 30 0 30 0 80 0 0 0 30 0 30 0 30 0 30 4*0 30 0 30 0 30 0 50 4*0 30 0 30 0
  //   30 6*0 30 0 30 0 30 6*0 30 0 30 0 30 6*0 30 0 30 5*0 30 0 30 0 30 6*0 30 0 30 5*0 30 0 30 5*0 30 0
  //   30 0 0 0 30 0 30 4*0 30 0 30 4*0 30 0 30 4*0 30 0 30 4*0 30 0 30 4*0 30 0 30 4*0 30 0 30 4*0 30 0 30
  //   4*0 30 0 30 4*0 30 0 30 4*0 30 0 30 4*0 30 0 30 4*0 30 0 30 4*0 30 0 30
  //   contents of ROM_5 (hex, n*v repeats v):
  //   47*0 40 20 4 8*0 40 20 8 8*0 40 20 c 6*0 40 10 8*0 40 20 14 6*0 40 18 6*0 40 1c 34*0 1 6*0 1 6*0 1
  //   6*0 1 6*0 2 6*0 2 6*0 2 6*0 2 6*0 3 6*0 3 6*0 3
  //   contents of ROM_6 (hex, n*v repeats v):
  //   120*0 40 6*0 80 6*0 c0 13*0 40 6*0 80 6*0 c0 13*0 40 6*0 80 6*0 c0 13*0 40 6*0 80
endmodule

module Counter16bits (
  input  n_Enable_Count,
  input  n_Clear,
  input  C_Clock,
  input  n_Enable_Load,
  input  [15:0] DI,
  output [15:0] Counter_Output
);

  wire n74163_4_pin15, Power, RCO_1, RCO_2, RCO_3;

  _74163 #(.ShowInternalStructure("true")) u_74163_1 (
    .pin1(n_Clear), .pin2(C_Clock), .pin3(DI[0]), .pin4(DI[1]), .pin5(DI[2]), .pin6(DI[3]),
    .pin7(n_Enable_Count), .pin15(RCO_1), .pin14(Counter_Output[0]), .pin13(Counter_Output[1]),
    .pin12(Counter_Output[2]), .pin11(Counter_Output[3]), .pin10(Power), .pin9(n_Enable_Load));
  _74163 #(.ShowInternalStructure("true")) u_74163_2 (
    .pin1(n_Clear), .pin2(C_Clock), .pin3(DI[4]), .pin4(DI[5]), .pin5(DI[6]), .pin6(DI[7]),
    .pin7(n_Enable_Count), .pin15(RCO_2), .pin14(Counter_Output[4]), .pin13(Counter_Output[5]),
    .pin12(Counter_Output[6]), .pin11(Counter_Output[7]), .pin10(RCO_1), .pin9(n_Enable_Load));
  _74163 #(.ShowInternalStructure("true")) u_74163_3 (
    .pin1(n_Clear), .pin2(C_Clock), .pin3(DI[8]), .pin4(DI[9]), .pin5(DI[10]), .pin6(DI[11]),
    .pin7(n_Enable_Count), .pin15(RCO_3), .pin14(Counter_Output[8]), .pin13(Counter_Output[9]),
    .pin12(Counter_Output[10]), .pin11(Counter_Output[11]), .pin10(RCO_2), .pin9(n_Enable_Load));
  _74163 #(.ShowInternalStructure("true")) u_74163_4 (
    .pin1(n_Clear), .pin2(C_Clock), .pin3(DI[12]), .pin4(DI[13]), .pin5(DI[14]), .pin6(DI[15]),
    .pin7(n_Enable_Count), .pin15(n74163_4_pin15), .pin14(Counter_Output[12]), .pin13(Counter_Output[13]),
    .pin12(Counter_Output[14]), .pin11(Counter_Output[15]), .pin10(RCO_3), .pin9(n_Enable_Load));
  // NoConnect on n74163_4_pin15
  // also tied to VCC on the sheet: Power

  // Other names for the same wires on the sheet: CLK = C_Clock; CLR = n_Clear; EN_P = n_Enable_Count; IN_1[15:0] = DI;
  //   NLD_1 = n_Enable_Load; OUT_1[15:0] = Counter_Output
endmodule

module Register16bits (
  input  Clock,
  input  n_EN_1,
  input  n_EN_2,
  input  n_EN_Out,
  input  [7:0] IN2,
  input  [7:0] IN1,
  output [15:0] OUT1
);

  wire O_1, O_2, O_3, O_4, O_5, O_6, O_7, O_8, O_9, O_10, O_11, O_12, O_13, O_14, O_15, O_16;

  _74377 #(.ShowInternalStructure("true")) u_74377_1 (
    .pin1(n_EN_1), .pin2(O_1), .pin3(IN1[0]), .pin4(IN1[1]), .pin5(O_2), .pin6(O_3), .pin7(IN1[2]),
    .pin8(IN1[3]), .pin9(O_4), .pin19(O_8), .pin18(IN1[7]), .pin17(IN1[6]), .pin16(O_7), .pin15(O_6),
    .pin14(IN1[5]), .pin13(IN1[4]), .pin12(O_5), .pin11(Clock));
  _74377 #(.ShowInternalStructure("true")) u_74377_2 (
    .pin1(n_EN_2), .pin2(O_9), .pin3(IN2[0]), .pin4(IN2[1]), .pin5(O_10), .pin6(O_11), .pin7(IN2[2]),
    .pin8(IN2[3]), .pin9(O_12), .pin19(O_16), .pin18(IN2[7]), .pin17(IN2[6]), .pin16(O_15), .pin15(O_14),
    .pin14(IN2[5]), .pin13(IN2[4]), .pin12(O_13), .pin11(Clock));
  _74244 #(.ShowInternalStructure("true")) u_74244_1 (
    .pin1(n_EN_Out), .pin2(O_5), .pin3(OUT1[0]), .pin4(O_6), .pin5(OUT1[1]), .pin6(O_7), .pin7(OUT1[2]),
    .pin8(O_8), .pin9(OUT1[3]), .pin19(n_EN_Out), .pin18(OUT1[4]), .pin17(O_1), .pin16(OUT1[5]), .pin15(O_2),
    .pin14(OUT1[6]), .pin13(O_3), .pin12(OUT1[7]), .pin11(O_4));
  _74244 #(.ShowInternalStructure("true")) u_74244_2 (
    .pin1(n_EN_Out), .pin2(O_13), .pin3(OUT1[8]), .pin4(O_14), .pin5(OUT1[9]), .pin6(O_15), .pin7(OUT1[10]),
    .pin8(O_16), .pin9(OUT1[11]), .pin19(n_EN_Out), .pin18(OUT1[12]), .pin17(O_9), .pin16(OUT1[13]),
    .pin15(O_10), .pin14(OUT1[14]), .pin13(O_11), .pin12(OUT1[15]), .pin11(O_12));

  // Other names for the same wires on the sheet: EN_1 = n_EN_1; EN_2 = n_EN_2; EN_Output = n_EN_Out; IN_1[7:0] = IN1;
  //   IN_11 = IN1[0]; IN_12 = IN1[1]; IN_13 = IN1[2]; IN_14 = IN1[3]; IN_15 = IN1[4]; IN_16 = IN1[5]; IN_17 = IN1[6];
  //   IN_18 = IN1[7]; IN_2[7:0] = IN2; IN_21 = IN2[0]; IN_22 = IN2[1]; IN_23 = IN2[2]; IN_24 = IN2[3]; IN_25 = IN2[4];
  //   IN_26 = IN2[5]; IN_27 = IN2[6]; IN_28 = IN2[7]; O1 = OUT1[0]; O2 = OUT1[1]; O3 = OUT1[2]; O4 = OUT1[3];
  //   O5 = OUT1[4]; O6 = OUT1[5]; O7 = OUT1[6]; O8 = OUT1[7]; O9 = OUT1[8]; O10 = OUT1[9]; O11 = OUT1[10];
  //   O12 = OUT1[11]; O13 = OUT1[12]; O14 = OUT1[13]; O15 = OUT1[14]; O16 = OUT1[15]
endmodule

module UserRegistersBlock (
  input  CLOCK,
  input  [7:0] DATA_BUS_IN,
  input  READ,
  input  WRITE,
  input  [1:0] REG_NUMBER,
  output [7:0] DATA_BUS_OUT
);

  wire n7414_1_pin10, n7414_1_pin11, n7414_1_pin12, n7414_1_pin13, n74139_1_pin9, n74139_1_pin10,
       n74139_1_pin11, n74139_1_pin12, n74139_1_pin13, n74139_1_pin14, n74139_1_pin15, n_REG_0, n_REG_1,
       n_REG_2, n_REG_3, pull_resistor_1_node, R_REG_0, R_REG_1, R_REG_2, R_REG_3, REG_0, REG_0_O0, REG_0_O1,
       REG_0_O2, REG_0_O3, REG_0_O4, REG_0_O5, REG_0_O6, REG_0_O7, REG_1, REG_1_O0, REG_1_O1, REG_1_O2,
       REG_1_O3, REG_1_O4, REG_1_O5, REG_1_O6, REG_1_O7, REG_2, REG_2_O0, REG_2_O1, REG_2_O2, REG_2_O3,
       REG_2_O4, REG_2_O5, REG_2_O6, REG_2_O7, REG_3, REG_3_O0, REG_3_O1, REG_3_O2, REG_3_O3, REG_3_O4,
       REG_3_O5, REG_3_O6, REG_3_O7, W_REG_0, W_REG_1, W_REG_2, W_REG_3;

  Pull_Resistor pull_resistor_1 (.node(pull_resistor_1_node));
  _74139 #(.ShowInternalStructure("true")) u_74139_1 (
    .pin1(pull_resistor_1_node), .pin2(REG_NUMBER[0]), .pin3(REG_NUMBER[1]), .pin4(REG_0), .pin5(REG_1),
    .pin6(REG_2), .pin7(REG_3), .pin15(n74139_1_pin15), .pin14(n74139_1_pin14), .pin13(n74139_1_pin13),
    .pin12(n74139_1_pin12), .pin11(n74139_1_pin11), .pin10(n74139_1_pin10), .pin9(n74139_1_pin9));
  _74377 #(.ShowInternalStructure("true")) u_74377_1 (
    .pin1(W_REG_0), .pin2(REG_0_O0), .pin3(DATA_BUS_IN[0]), .pin4(DATA_BUS_IN[1]), .pin5(REG_0_O1),
    .pin6(REG_0_O2), .pin7(DATA_BUS_IN[2]), .pin8(DATA_BUS_IN[3]), .pin9(REG_0_O3), .pin19(REG_0_O7),
    .pin18(DATA_BUS_IN[7]), .pin17(DATA_BUS_IN[6]), .pin16(REG_0_O6), .pin15(REG_0_O5),
    .pin14(DATA_BUS_IN[5]), .pin13(DATA_BUS_IN[4]), .pin12(REG_0_O4), .pin11(CLOCK));
  _74244 #(.ShowInternalStructure("true")) u_74244_1 (
    .pin1(R_REG_0), .pin2(REG_0_O0), .pin3(DATA_BUS_IN[7]), .pin4(REG_0_O1), .pin5(DATA_BUS_IN[6]),
    .pin6(REG_0_O2), .pin7(DATA_BUS_IN[5]), .pin8(REG_0_O3), .pin9(DATA_BUS_IN[4]), .pin19(R_REG_0),
    .pin18(DATA_BUS_IN[0]), .pin17(REG_0_O7), .pin16(DATA_BUS_IN[1]), .pin15(REG_0_O6),
    .pin14(DATA_BUS_IN[2]), .pin13(REG_0_O5), .pin12(DATA_BUS_IN[3]), .pin11(REG_0_O4));
  Pull_Resistor pull_resistor_2 (.node(n74139_1_pin15));
  Pull_Resistor pull_resistor_3 (.node(n74139_1_pin14));
  Pull_Resistor pull_resistor_4 (.node(n74139_1_pin13));
  // NoConnect on n74139_1_pin12
  // NoConnect on n74139_1_pin11
  // NoConnect on n74139_1_pin10
  // NoConnect on n74139_1_pin9
  _7414 #(.ShowInternalStructure("true")) u_7414_1 (
    .pin1(REG_0), .pin2(n_REG_0), .pin3(REG_1), .pin4(n_REG_1), .pin5(REG_2), .pin6(n_REG_2),
    .pin13(n7414_1_pin13), .pin12(n7414_1_pin12), .pin11(n7414_1_pin11), .pin10(n7414_1_pin10), .pin9(REG_3),
    .pin8(n_REG_3));
  Pull_Resistor pull_resistor_5 (.node(n7414_1_pin13));
  // NoConnect on n7414_1_pin12
  Pull_Resistor pull_resistor_6 (.node(n7414_1_pin11));
  // NoConnect on n7414_1_pin10
  _74377 #(.ShowInternalStructure("true")) u_74377_2 (
    .pin1(W_REG_1), .pin2(REG_1_O0), .pin3(DATA_BUS_IN[0]), .pin4(DATA_BUS_IN[1]), .pin5(REG_1_O1),
    .pin6(REG_1_O2), .pin7(DATA_BUS_IN[2]), .pin8(DATA_BUS_IN[3]), .pin9(REG_1_O3), .pin19(REG_1_O7),
    .pin18(DATA_BUS_IN[7]), .pin17(DATA_BUS_IN[6]), .pin16(REG_1_O6), .pin15(REG_1_O5),
    .pin14(DATA_BUS_IN[5]), .pin13(DATA_BUS_IN[4]), .pin12(REG_1_O4), .pin11(CLOCK));
  _74244 #(.ShowInternalStructure("true")) u_74244_2 (
    .pin1(R_REG_1), .pin2(REG_1_O0), .pin3(DATA_BUS_IN[7]), .pin4(REG_1_O1), .pin5(DATA_BUS_IN[6]),
    .pin6(REG_1_O2), .pin7(DATA_BUS_IN[5]), .pin8(REG_1_O3), .pin9(DATA_BUS_IN[4]), .pin19(R_REG_1),
    .pin18(DATA_BUS_IN[0]), .pin17(REG_1_O7), .pin16(DATA_BUS_IN[1]), .pin15(REG_1_O6),
    .pin14(DATA_BUS_IN[2]), .pin13(REG_1_O5), .pin12(DATA_BUS_IN[3]), .pin11(REG_1_O4));
  _7424 #(.ShowInternalStructure("true")) u_7424_1 (
    .pin1(WRITE), .pin2(n_REG_0), .pin3(W_REG_0), .pin4(WRITE), .pin5(n_REG_1), .pin6(W_REG_1),
    .pin13(WRITE), .pin12(n_REG_3), .pin11(W_REG_3), .pin10(WRITE), .pin9(n_REG_2), .pin8(W_REG_2));
  _74377 #(.ShowInternalStructure("true")) u_74377_3 (
    .pin1(W_REG_2), .pin2(REG_2_O0), .pin3(DATA_BUS_IN[0]), .pin4(DATA_BUS_IN[1]), .pin5(REG_2_O1),
    .pin6(REG_2_O2), .pin7(DATA_BUS_IN[2]), .pin8(DATA_BUS_IN[3]), .pin9(REG_2_O3), .pin19(REG_2_O7),
    .pin18(DATA_BUS_IN[7]), .pin17(DATA_BUS_IN[6]), .pin16(REG_2_O6), .pin15(REG_2_O5),
    .pin14(DATA_BUS_IN[5]), .pin13(DATA_BUS_IN[4]), .pin12(REG_2_O4), .pin11(CLOCK));
  _74244 #(.ShowInternalStructure("true")) u_74244_3 (
    .pin1(R_REG_2), .pin2(REG_2_O0), .pin3(DATA_BUS_IN[7]), .pin4(REG_2_O1), .pin5(DATA_BUS_IN[6]),
    .pin6(REG_2_O2), .pin7(DATA_BUS_IN[5]), .pin8(REG_2_O3), .pin9(DATA_BUS_IN[4]), .pin19(R_REG_2),
    .pin18(DATA_BUS_IN[0]), .pin17(REG_2_O7), .pin16(DATA_BUS_IN[1]), .pin15(REG_2_O6),
    .pin14(DATA_BUS_IN[2]), .pin13(REG_2_O5), .pin12(DATA_BUS_IN[3]), .pin11(REG_2_O4));
  _7424 #(.ShowInternalStructure("true")) u_7424_2 (
    .pin1(READ), .pin2(n_REG_0), .pin3(R_REG_0), .pin4(READ), .pin5(n_REG_1), .pin6(R_REG_1), .pin13(READ),
    .pin12(n_REG_3), .pin11(R_REG_3), .pin10(READ), .pin9(n_REG_2), .pin8(R_REG_2));
  _74377 #(.ShowInternalStructure("true")) u_74377_4 (
    .pin1(W_REG_3), .pin2(REG_3_O0), .pin3(DATA_BUS_IN[0]), .pin4(DATA_BUS_IN[1]), .pin5(REG_3_O1),
    .pin6(REG_3_O2), .pin7(DATA_BUS_IN[2]), .pin8(DATA_BUS_IN[3]), .pin9(REG_3_O3), .pin19(REG_3_O7),
    .pin18(DATA_BUS_IN[7]), .pin17(DATA_BUS_IN[6]), .pin16(REG_3_O6), .pin15(REG_3_O5),
    .pin14(DATA_BUS_IN[5]), .pin13(DATA_BUS_IN[4]), .pin12(REG_3_O4), .pin11(CLOCK));
  _74244 #(.ShowInternalStructure("true")) u_74244_4 (
    .pin1(R_REG_3), .pin2(REG_3_O0), .pin3(DATA_BUS_IN[7]), .pin4(REG_3_O1), .pin5(DATA_BUS_IN[6]),
    .pin6(REG_3_O2), .pin7(DATA_BUS_IN[5]), .pin8(REG_3_O3), .pin9(DATA_BUS_IN[4]), .pin19(R_REG_3),
    .pin18(DATA_BUS_IN[0]), .pin17(REG_3_O7), .pin16(DATA_BUS_IN[1]), .pin15(REG_3_O6),
    .pin14(DATA_BUS_IN[2]), .pin13(REG_3_O5), .pin12(DATA_BUS_IN[3]), .pin11(REG_3_O4));

  assign DATA_BUS_OUT = DATA_BUS_IN;

  // Other names for the same wires on the sheet: DATA_BUS[7:0] = DATA_BUS_IN; IQ0 = DATA_BUS_IN[0];
  //   IQ1 = DATA_BUS_IN[1]; IQ2 = DATA_BUS_IN[2]; IQ3 = DATA_BUS_IN[3]; IQ4 = DATA_BUS_IN[4]; IQ5 = DATA_BUS_IN[5];
  //   IQ6 = DATA_BUS_IN[6]; IQ7 = DATA_BUS_IN[7]; RN0 = REG_NUMBER[0]; RN1 = REG_NUMBER[1]
endmodule

module ALU (
  input  in_1,
  input  in_2,
  input  in_3,
  input  in_4,
  input  in_5,
  input  in_6,
  input  in_7,
  input  in_8,
  input  in_9,
  input  in_10,
  input  in_11,
  input  in_12,
  input  in_13,
  input  in_14,
  output out_15,
  output out_16,
  output out_17,
  output out_18,
  output out_19,
  output out_20,
  output out_21,
  output out_22,
  output out_23,
  output out_24,
  output out_25,
  output out_26,
  output out_27,
  output out_28,
  output out_29,
  output out_30
);

  wire AND_EN, AND_O_1, AND_O_2, AND_O_3, AND_O_4, AND_O_5, AND_O_6, AND_O_7, AND_O_8, n7414_2_pin3,
       n7414_2_pin4, n7414_2_pin5, n7414_2_pin6, n7414_2_pin8, n7414_2_pin9, n7414_2_pin10, n7414_2_pin11,
       n7414_2_pin12, n7414_2_pin13, n74138_1_pin6, n74138_1_pin15, n74244_3_pin17, n74244_6_pin15,
       n74283_1_pin9, NOT_EN, OR_EN, OR_O_1, OR_O_2, OR_O_3, OR_O_4, OR_O_5, OR_O_6, OR_O_7, OR_O_8,
       pull_resistor_2_node, pull_resistor_3_node, pull_resistor_4_node, RA_O_1, RA_O_2, RA_O_3, RA_O_4,
       RA_O_5, RA_O_6, RA_O_7, RA_O_8, RB_O_1, RB_O_2, RB_O_3, RB_O_4, RB_O_5, RB_O_6, RB_O_7, RB_O_8,
       SHL_EN, SHR_EN, SUM_EN, SUM_O_1, SUM_O_2, SUM_O_3, SUM_O_4, SUM_O_5, SUM_O_6, SUM_O_7, SUM_O_8,
       XOR_EN, XOR_O_1, XOR_O_2, XOR_O_3, XOR_O_4, XOR_O_5, XOR_O_6, XOR_O_7, XOR_O_8;

  _74377 #(.ShowInternalStructure("true")) REGISTER_A (
    .pin1(in_9), .pin2(RA_O_4), .pin3(in_4), .pin4(in_3), .pin5(RA_O_3), .pin6(RA_O_2), .pin7(in_2),
    .pin8(in_1), .pin9(RA_O_1), .pin19(RA_O_5), .pin18(in_5), .pin17(in_6), .pin16(RA_O_6), .pin15(RA_O_7),
    .pin14(in_7), .pin13(in_8), .pin12(RA_O_8), .pin11(in_11));
  _7408 #(.ShowInternalStructure("true")) u_7408_1 (
    .pin1(RB_O_1), .pin2(RA_O_1), .pin3(AND_O_1), .pin4(RB_O_2), .pin5(RA_O_2), .pin6(AND_O_2),
    .pin13(RB_O_4), .pin12(RA_O_4), .pin11(AND_O_4), .pin10(RB_O_3), .pin9(RA_O_3), .pin8(AND_O_3));
  _74244 #(.ShowInternalStructure("true")) u_74244_1 (
    .pin1(AND_EN), .pin2(AND_O_2), .pin3(out_21), .pin4(AND_O_1), .pin5(out_22), .pin6(AND_O_4),
    .pin7(out_19), .pin8(AND_O_3), .pin9(out_20), .pin19(AND_EN), .pin18(out_16), .pin17(AND_O_7),
    .pin16(out_15), .pin15(AND_O_8), .pin14(out_18), .pin13(AND_O_5), .pin12(out_17), .pin11(AND_O_6));
  _7432 #(.ShowInternalStructure("true")) u_7432_1 (
    .pin1(RB_O_1), .pin2(RA_O_1), .pin3(OR_O_1), .pin4(RB_O_2), .pin5(RA_O_2), .pin6(OR_O_2), .pin13(RB_O_4),
    .pin12(RA_O_4), .pin11(OR_O_4), .pin10(RB_O_3), .pin9(RA_O_3), .pin8(OR_O_3));
  _74244 #(.ShowInternalStructure("true")) u_74244_2 (
    .pin1(OR_EN), .pin2(OR_O_2), .pin3(out_21), .pin4(OR_O_1), .pin5(out_22), .pin6(OR_O_4), .pin7(out_19),
    .pin8(OR_O_3), .pin9(out_20), .pin19(OR_EN), .pin18(out_16), .pin17(OR_O_7), .pin16(out_15),
    .pin15(OR_O_8), .pin14(out_18), .pin13(OR_O_5), .pin12(out_17), .pin11(OR_O_6));
  _74240 #(.ShowInternalStructure("true")) u_74240_1 (
    .pin1(NOT_EN), .pin2(RA_O_5), .pin3(out_15), .pin4(RA_O_4), .pin5(out_22), .pin6(RA_O_6), .pin7(out_16),
    .pin8(RA_O_7), .pin9(out_17), .pin19(NOT_EN), .pin18(out_19), .pin17(RA_O_1), .pin16(out_18),
    .pin15(RA_O_8), .pin14(out_20), .pin13(RA_O_2), .pin12(out_21), .pin11(RA_O_3));
  _74244 #(.ShowInternalStructure("true")) u_74244_3 (
    .pin1(SHR_EN), .pin2(RA_O_5), .pin3(out_22), .pin4(RA_O_4), .pin5(out_21), .pin6(RA_O_6), .pin7(out_15),
    .pin8(RA_O_7), .pin9(out_16), .pin19(SHR_EN), .pin18(out_18), .pin17(n74244_3_pin17), .pin16(out_17),
    .pin15(RA_O_8), .pin14(out_19), .pin13(RA_O_2), .pin12(out_20), .pin11(RA_O_3));
  Pull_Resistor pull_resistor_1 (.node(n74244_3_pin17));
  _7408 #(.ShowInternalStructure("true")) u_7408_2 (
    .pin1(RB_O_5), .pin2(RA_O_5), .pin3(AND_O_5), .pin4(RB_O_6), .pin5(RA_O_6), .pin6(AND_O_6),
    .pin13(RB_O_8), .pin12(RA_O_8), .pin11(AND_O_8), .pin10(RB_O_7), .pin9(RA_O_7), .pin8(AND_O_7));
  _7432 #(.ShowInternalStructure("true")) u_7432_2 (
    .pin1(RB_O_5), .pin2(RA_O_5), .pin3(OR_O_5), .pin4(RB_O_6), .pin5(RA_O_6), .pin6(OR_O_6), .pin13(RB_O_8),
    .pin12(RA_O_8), .pin11(OR_O_8), .pin10(RB_O_7), .pin9(RA_O_7), .pin8(OR_O_7));
  _74377 #(.ShowInternalStructure("true")) REGISTER_B (
    .pin1(in_10), .pin2(RB_O_4), .pin3(in_4), .pin4(in_3), .pin5(RB_O_3), .pin6(RB_O_2), .pin7(in_2),
    .pin8(in_1), .pin9(RB_O_1), .pin19(RB_O_5), .pin18(in_5), .pin17(in_6), .pin16(RB_O_6), .pin15(RB_O_7),
    .pin14(in_7), .pin13(in_8), .pin12(RB_O_8), .pin11(in_11));
  LED led_1 (.in(RA_O_8));
  LED led_2 (.in(RA_O_7));
  LED led_3 (.in(RA_O_6));
  LED led_4 (.in(RA_O_5));
  Pull_Resistor pull_resistor_2 (.node(pull_resistor_2_node));
  LED led_5 (.in(RA_O_4));
  LED led_6 (.in(RA_O_3));
  LED led_7 (.in(RA_O_2));
  LED led_8 (.in(RA_O_1));
  Pull_Resistor pull_resistor_3 (.node(pull_resistor_3_node));
  Pull_Resistor pull_resistor_4 (.node(pull_resistor_4_node));
  _74283 #(.ShowInternalStructure("true")) u_74283_1 (
    .pin1(SUM_O_2), .pin2(RA_O_2), .pin3(RB_O_2), .pin4(SUM_O_1), .pin5(RA_O_1), .pin6(RB_O_1),
    .pin7(pull_resistor_2_node), .pin15(RA_O_3), .pin14(RB_O_3), .pin13(SUM_O_3), .pin12(RA_O_4),
    .pin11(RB_O_4), .pin10(SUM_O_4), .pin9(n74283_1_pin9));
  _74244 #(.ShowInternalStructure("true")) u_74244_4 (
    .pin1(SUM_EN), .pin2(SUM_O_1), .pin3(out_22), .pin4(SUM_O_2), .pin5(out_21), .pin6(SUM_O_3),
    .pin7(out_20), .pin8(SUM_O_4), .pin9(out_19), .pin19(SUM_EN), .pin18(out_15), .pin17(SUM_O_8),
    .pin16(out_16), .pin15(SUM_O_7), .pin14(out_17), .pin13(SUM_O_6), .pin12(out_18), .pin11(SUM_O_5));
  _7486 #(.ShowInternalStructure("true")) u_7486_1 (
    .pin1(RB_O_1), .pin2(RA_O_1), .pin3(XOR_O_1), .pin4(RB_O_2), .pin5(RA_O_2), .pin6(XOR_O_2),
    .pin13(RB_O_4), .pin12(RA_O_4), .pin11(XOR_O_4), .pin10(RB_O_3), .pin9(RA_O_3), .pin8(XOR_O_3));
  _74244 #(.ShowInternalStructure("true")) u_74244_5 (
    .pin1(XOR_EN), .pin2(XOR_O_2), .pin3(out_21), .pin4(XOR_O_1), .pin5(out_22), .pin6(XOR_O_4),
    .pin7(out_19), .pin8(XOR_O_3), .pin9(out_20), .pin19(XOR_EN), .pin18(out_16), .pin17(XOR_O_7),
    .pin16(out_15), .pin15(XOR_O_8), .pin14(out_18), .pin13(XOR_O_5), .pin12(out_17), .pin11(XOR_O_6));
  _74244 #(.ShowInternalStructure("true")) u_74244_6 (
    .pin1(SHL_EN), .pin2(RA_O_5), .pin3(out_16), .pin4(RA_O_4), .pin5(out_15), .pin6(RA_O_6), .pin7(out_17),
    .pin8(RA_O_7), .pin9(out_18), .pin19(SHL_EN), .pin18(out_20), .pin17(RA_O_1), .pin16(out_19),
    .pin15(n74244_6_pin15), .pin14(out_21), .pin13(RA_O_2), .pin12(out_22), .pin11(RA_O_3));
  LED led_9 (.in(RB_O_8));
  _74138 #(.ShowInternalStructure("true")) u_74138_1 (
    .pin1(in_12), .pin2(in_13), .pin3(in_14), .pin4(pull_resistor_3_node), .pin5(pull_resistor_4_node),
    .pin6(n74138_1_pin6), .pin7(SHR_EN), .pin15(n74138_1_pin15), .pin14(SUM_EN), .pin13(AND_EN),
    .pin12(OR_EN), .pin11(NOT_EN), .pin10(XOR_EN), .pin9(SHL_EN));
  Pull_Resistor pull_resistor_5 (.node(n74244_6_pin15));
  LED led_10 (.in(RB_O_7));
  LED led_11 (.in(RB_O_6));
  LED led_12 (.in(RB_O_5));
  LED led_13 (.in(RB_O_4));
  // NoConnect on n74138_1_pin15
  LED led_14 (.in(RB_O_1));
  LED led_15 (.in(RB_O_3));
  LED led_16 (.in(RB_O_2));
  _7486 #(.ShowInternalStructure("true")) u_7486_2 (
    .pin1(RB_O_5), .pin2(RA_O_5), .pin3(XOR_O_5), .pin4(RB_O_6), .pin5(RA_O_6), .pin6(XOR_O_6),
    .pin13(RB_O_8), .pin12(RA_O_8), .pin11(XOR_O_8), .pin10(RB_O_7), .pin9(RA_O_7), .pin8(XOR_O_7));
  // NoConnect on n7414_2_pin4
  // NoConnect on n7414_2_pin6
  _74283 #(.ShowInternalStructure("true")) u_74283_2 (
    .pin1(SUM_O_6), .pin2(RA_O_6), .pin3(RB_O_6), .pin4(SUM_O_5), .pin5(RA_O_5), .pin6(RB_O_5),
    .pin7(n74283_1_pin9), .pin15(RA_O_7), .pin14(RB_O_7), .pin13(SUM_O_7), .pin12(RA_O_8), .pin11(RB_O_8),
    .pin10(SUM_O_8), .pin9(out_30));
  _7414 #(.ShowInternalStructure("true")) u_7414_1 (
    .pin1(SUM_EN), .pin2(out_23), .pin3(AND_EN), .pin4(out_24), .pin5(OR_EN), .pin6(out_25), .pin13(NOT_EN),
    .pin12(out_26), .pin11(XOR_EN), .pin10(out_27), .pin9(SHL_EN), .pin8(out_28));
  _7414 #(.ShowInternalStructure("true")) u_7414_2 (
    .pin1(SHR_EN), .pin2(out_29), .pin3(n7414_2_pin3), .pin4(n7414_2_pin4), .pin5(n7414_2_pin5),
    .pin6(n7414_2_pin6), .pin13(n7414_2_pin13), .pin12(n7414_2_pin12), .pin11(n7414_2_pin11),
    .pin10(n7414_2_pin10), .pin9(n7414_2_pin9), .pin8(n7414_2_pin8));
  Pull_Resistor pull_resistor_6 (.node(n7414_2_pin3));
  Pull_Resistor pull_resistor_7 (.node(n7414_2_pin5));
  LED led_17 (.in(out_23));
  LED led_18 (.in(out_24));
  LED led_19 (.in(out_25));
  LED led_20 (.in(out_26));
  LED led_21 (.in(out_27));
  LED led_22 (.in(out_28));
  LED led_23 (.in(out_29));
  Pull_Resistor pull_resistor_8 (.node(n7414_2_pin13));
  // NoConnect on n7414_2_pin12
  Pull_Resistor pull_resistor_9 (.node(n7414_2_pin11));
  // NoConnect on n7414_2_pin10
  Pull_Resistor pull_resistor_10 (.node(n7414_2_pin9));
  // NoConnect on n7414_2_pin8
  // also tied to VCC on the sheet: n74138_1_pin6

  // Other names for the same wires on the sheet: B_1 = in_1; B_2 = in_2; B_3 = in_3; B_4 = in_4; B_5 = in_5;
  //   B_6 = in_6; B_7 = in_7; B_8 = in_8; CLOCK = in_11; EN_A = in_9; EN_B = in_10; F_CARRY = out_30;
  //   n_AND_EN = out_24; n_NOT_EN = out_26; n_OR_EN = out_25; n_SHL_EN = out_28; n_SHR_EN = out_29; n_SUM_EN = out_23;
  //   n_XOR_EN = out_27; OUT_1 = out_15; OUT_2 = out_16; OUT_3 = out_17; OUT_4 = out_18; OUT_5 = out_19;
  //   OUT_6 = out_20; OUT_7 = out_21; OUT_8 = out_22; SI_1 = in_12; SI_2 = in_13; SI_3 = in_14

  // Notes on the sheet:
  //   OR OPERATION
  //   REGISTERS "A" , "B"
  //   AND OPERATION
  //   NOT OPERATION
  //   SHR OPERATION
  //   OUT REG "A"
  //   SUM OPERATION
  //   XOR OPERATION
  //   SHL OPERATION
  //   MODE SELECTOR
  //   OUT REG "B"
  //   OUT MODE
  //   OUT nMODES
endmodule

module FLAGS_test (
  input  F_CARRY,
  input  n_SUM_EN,
  input  n_AND_EN,
  input  n_OR_EN,
  input  n_NOT_EN,
  input  n_XOR_EN,
  input  n_SHL_EN,
  input  n_SHR_EN,
  input  B1,
  input  B2,
  input  B3,
  input  B4,
  input  B5,
  input  B6,
  input  B7,
  input  B8,
  input  CLK,
  output ZERO,
  output NEGATIVE,
  output CARRY,
  output OVERFLOW
);

  wire CLK_Flags, EN_WRITE_FLAGS, F_OVERFLOW, F_ZERO, n7408_1_pin6, n7408_1_pin8, n7408_1_pin9,
       n7408_1_pin10, n7408_1_pin11, n7408_1_pin12, n7408_1_pin13, n7414_1_pin5, n7414_1_pin6, n7414_1_pin8,
       n7414_1_pin9, n7414_1_pin10, n7414_1_pin11, n7414_1_pin12, n7414_1_pin13, n7432_2_pin8, n7432_2_pin9,
       n7432_2_pin10, n7486_1_pin6, n7486_1_pin8, n7486_1_pin9, n7486_1_pin10, n7486_1_pin11, n7486_1_pin12,
       n7486_1_pin13, n74175_1_pin1, n74175_1_pin3, n74175_1_pin6, n74175_1_pin11, n74175_1_pin14,
       n_O1_O2_O3, n_O4_O5_O6, n_O7_O8, NOT_OR_OR, O1_O2_O3, O4_O5_O6, pull_resistor_5_node,
       pull_resistor_6_node, pull_resistor_11_node, pull_resistor_12_node, SUM_OR_AND,
       SUM_OR_AND_OR_NOT_OR_OR, XOR_OR_SHL, XOR_OR_SHL_OR_SHR;

  _7427 #(.ShowInternalStructure("true")) u_7427_1 (
    .pin1(B6), .pin2(B5), .pin3(B3), .pin4(B2), .pin5(B1), .pin6(O1_O2_O3), .pin13(B4), .pin12(O4_O5_O6),
    .pin11(n_O7_O8), .pin10(n_O4_O5_O6), .pin9(n_O1_O2_O3), .pin8(F_ZERO));
  _7414 #(.ShowInternalStructure("true")) u_7414_1 (
    .pin1(O1_O2_O3), .pin2(n_O1_O2_O3), .pin3(O4_O5_O6), .pin4(n_O4_O5_O6), .pin5(n7414_1_pin5),
    .pin6(n7414_1_pin6), .pin13(n7414_1_pin13), .pin12(n7414_1_pin12), .pin11(n7414_1_pin11),
    .pin10(n7414_1_pin10), .pin9(n7414_1_pin9), .pin8(n7414_1_pin8));
  Pull_Resistor pull_resistor_1 (.node(n7414_1_pin5));
  // NoConnect on n7414_1_pin6
  Pull_Resistor pull_resistor_2 (.node(n7414_1_pin13));
  // NoConnect on n7414_1_pin12
  Pull_Resistor pull_resistor_3 (.node(n7414_1_pin11));
  // NoConnect on n7414_1_pin10
  Pull_Resistor pull_resistor_4 (.node(n7414_1_pin9));
  // NoConnect on n7414_1_pin8
  // NoConnect on n74175_1_pin3
  // NoConnect on n74175_1_pin6
  Pull_Resistor pull_resistor_5 (.node(pull_resistor_5_node));
  Pull_Resistor pull_resistor_6 (.node(pull_resistor_6_node));
  // NoConnect on n7486_1_pin6
  _74175 #(.ShowInternalStructure("true")) u_74175_1 (
    .pin1(n74175_1_pin1), .pin2(ZERO), .pin3(n74175_1_pin3), .pin4(F_ZERO), .pin5(F_CARRY),
    .pin6(n74175_1_pin6), .pin7(CARRY), .pin15(OVERFLOW), .pin14(n74175_1_pin14), .pin13(F_OVERFLOW),
    .pin12(B8), .pin11(n74175_1_pin11), .pin10(NEGATIVE), .pin9(CLK_Flags));
  _7432 #(.ShowInternalStructure("true")) u_7432_1 (
    .pin1(B7), .pin2(B8), .pin3(n_O7_O8), .pin4(n_SUM_EN), .pin5(n_AND_EN), .pin6(SUM_OR_AND),
    .pin13(n_OR_EN), .pin12(n_NOT_EN), .pin11(NOT_OR_OR), .pin10(n_XOR_EN), .pin9(n_SHL_EN), .pin8(XOR_OR_SHL));
  _7486 #(.ShowInternalStructure("true")) u_7486_1 (
    .pin1(F_CARRY), .pin2(B8), .pin3(F_OVERFLOW), .pin4(pull_resistor_5_node), .pin5(pull_resistor_6_node),
    .pin6(n7486_1_pin6), .pin13(n7486_1_pin13), .pin12(n7486_1_pin12), .pin11(n7486_1_pin11),
    .pin10(n7486_1_pin10), .pin9(n7486_1_pin9), .pin8(n7486_1_pin8));
  // NoConnect on n74175_1_pin14
  // NoConnect on n74175_1_pin11
  Pull_Resistor pull_resistor_7 (.node(n7486_1_pin13));
  Pull_Resistor pull_resistor_8 (.node(n7486_1_pin12));
  // NoConnect on n7486_1_pin11
  Pull_Resistor pull_resistor_9 (.node(n7486_1_pin10));
  Pull_Resistor pull_resistor_10 (.node(n7486_1_pin9));
  // NoConnect on n7486_1_pin8
  LED led_1 (.in(ZERO));
  LED led_2 (.in(NEGATIVE));
  LED led_3 (.in(CARRY));
  LED led_4 (.in(OVERFLOW));
  Pull_Resistor pull_resistor_11 (.node(pull_resistor_11_node));
  Pull_Resistor pull_resistor_12 (.node(pull_resistor_12_node));
  // NoConnect on n7408_1_pin6
  _7432 #(.ShowInternalStructure("true")) u_7432_2 (
    .pin1(SUM_OR_AND), .pin2(NOT_OR_OR), .pin3(SUM_OR_AND_OR_NOT_OR_OR), .pin4(XOR_OR_SHL), .pin5(n_SHR_EN),
    .pin6(XOR_OR_SHL_OR_SHR), .pin13(SUM_OR_AND_OR_NOT_OR_OR), .pin12(XOR_OR_SHL_OR_SHR),
    .pin11(EN_WRITE_FLAGS), .pin10(n7432_2_pin10), .pin9(n7432_2_pin9), .pin8(n7432_2_pin8));
  Pull_Resistor pull_resistor_13 (.node(n7432_2_pin10));
  Pull_Resistor pull_resistor_14 (.node(n7432_2_pin9));
  // NoConnect on n7432_2_pin8
  _7408 #(.ShowInternalStructure("true")) u_7408_1 (
    .pin1(EN_WRITE_FLAGS), .pin2(CLK), .pin3(CLK_Flags), .pin4(pull_resistor_11_node),
    .pin5(pull_resistor_12_node), .pin6(n7408_1_pin6), .pin13(n7408_1_pin13), .pin12(n7408_1_pin12),
    .pin11(n7408_1_pin11), .pin10(n7408_1_pin10), .pin9(n7408_1_pin9), .pin8(n7408_1_pin8));
  Pull_Resistor pull_resistor_15 (.node(n7408_1_pin13));
  Pull_Resistor pull_resistor_16 (.node(n7408_1_pin12));
  // NoConnect on n7408_1_pin11
  Pull_Resistor pull_resistor_17 (.node(n7408_1_pin10));
  Pull_Resistor pull_resistor_18 (.node(n7408_1_pin9));
  // NoConnect on n7408_1_pin8
  // also tied to VCC on the sheet: n74175_1_pin1

  // Other names for the same wires on the sheet: B_1 = B1; B_2 = B2; B_3 = B3; B_4 = B4; B_5 = B5; B_6 = B6; B_7 = B7;
  //   B_8 = B8

  // Notes on the sheet:
  //   FLAGS OUT
endmodule

module ALU_V2_test (
  input  B1,
  input  B2,
  input  B3,
  input  B4,
  input  B5,
  input  B6,
  input  B7,
  input  B8,
  input  EN_A,
  input  EN_B,
  input  CLK,
  input  SL1,
  input  SL2,
  input  SL3,
  output O1,
  output O2,
  output O3,
  output O4,
  output O5,
  output O6,
  output O7,
  output O8,
  output n_SUM_EN,
  output n_AND_EN,
  output n_OR_EN,
  output n_NOT_EN,
  output n_XOR_EN,
  output n_SHL_EN,
  output n_SHR_EN,
  output F_CARRY
);

  wire AND_EN, AND_O_1, AND_O_2, AND_O_3, AND_O_4, AND_O_5, AND_O_6, AND_O_7, AND_O_8, n7414_2_pin4,
       n7414_2_pin6, n7414_2_pin8, n7414_2_pin9, n7414_2_pin10, n7414_2_pin11, n7414_2_pin12, n7414_2_pin13,
       n74138_1_pin4, n74138_1_pin5, n74138_1_pin6, n74138_1_pin15, n74244_5_pin11, n74283_1_pin7,
       n74283_1_pin9, NOT_EN, OR_EN, OR_O_1, OR_O_2, OR_O_3, OR_O_4, OR_O_5, OR_O_6, OR_O_7, OR_O_8,
       pull_resistor_4_node, pull_resistor_5_node, pull_resistor_10_node, RA_O_1, RA_O_2, RA_O_3, RA_O_4,
       RA_O_5, RA_O_6, RA_O_7, RA_O_8, RB_O_1, RB_O_2, RB_O_3, RB_O_4, RB_O_5, RB_O_6, RB_O_7, RB_O_8,
       SHL_EN, SHR_EN, SUM_EN, SUM_O_1, SUM_O_2, SUM_O_3, SUM_O_4, SUM_O_5, SUM_O_6, SUM_O_7, SUM_O_8,
       XOR_EN, XOR_O_1, XOR_O_2, XOR_O_3, XOR_O_4, XOR_O_5, XOR_O_6, XOR_O_7, XOR_O_8;

  _74283 #(.ShowInternalStructure("true")) u_74283_1 (
    .pin1(SUM_O_2), .pin2(RB_O_2), .pin3(RA_O_2), .pin4(SUM_O_1), .pin5(RB_O_1), .pin6(RA_O_1),
    .pin7(n74283_1_pin7), .pin15(RB_O_3), .pin14(RA_O_3), .pin13(SUM_O_3), .pin12(RB_O_4), .pin11(RA_O_4),
    .pin10(SUM_O_4), .pin9(n74283_1_pin9));
  Pull_Resistor pull_resistor_1 (.node(n74283_1_pin7));
  _74283 #(.ShowInternalStructure("true")) u_74283_2 (
    .pin1(SUM_O_6), .pin2(RB_O_6), .pin3(RA_O_6), .pin4(SUM_O_5), .pin5(RB_O_5), .pin6(RA_O_5),
    .pin7(n74283_1_pin9), .pin15(RB_O_7), .pin14(RA_O_7), .pin13(SUM_O_7), .pin12(RB_O_8), .pin11(RA_O_8),
    .pin10(SUM_O_8), .pin9(F_CARRY));
  _74244 #(.ShowInternalStructure("true")) u_74244_1 (
    .pin1(SUM_EN), .pin2(SUM_O_5), .pin3(O8), .pin4(SUM_O_6), .pin5(O7), .pin6(SUM_O_1), .pin7(O4),
    .pin8(SUM_O_2), .pin9(O3), .pin19(SUM_EN), .pin18(O5), .pin17(SUM_O_8), .pin16(O6), .pin15(SUM_O_7),
    .pin14(O1), .pin13(SUM_O_4), .pin12(O2), .pin11(SUM_O_3));
  _74377 #(.ShowInternalStructure("true")) REGISTER_A (
    .pin1(EN_A), .pin2(RA_O_4), .pin3(B4), .pin4(B3), .pin5(RA_O_3), .pin6(RA_O_2), .pin7(B2), .pin8(B1),
    .pin9(RA_O_1), .pin19(RA_O_5), .pin18(B5), .pin17(B6), .pin16(RA_O_6), .pin15(RA_O_7), .pin14(B7),
    .pin13(B8), .pin12(RA_O_8), .pin11(CLK));
  _74377 #(.ShowInternalStructure("true")) REGISTER_B (
    .pin1(EN_B), .pin2(RB_O_4), .pin3(B4), .pin4(B3), .pin5(RB_O_3), .pin6(RB_O_2), .pin7(B2), .pin8(B1),
    .pin9(RB_O_1), .pin19(RB_O_5), .pin18(B5), .pin17(B6), .pin16(RB_O_6), .pin15(RB_O_7), .pin14(B7),
    .pin13(B8), .pin12(RB_O_8), .pin11(CLK));
  _7408 #(.ShowInternalStructure("true")) u_7408_1 (
    .pin1(RB_O_2), .pin2(RA_O_2), .pin3(AND_O_2), .pin4(RB_O_1), .pin5(RA_O_1), .pin6(AND_O_1),
    .pin13(RA_O_3), .pin12(RB_O_3), .pin11(AND_O_3), .pin10(RA_O_4), .pin9(RB_O_4), .pin8(AND_O_4));
  _7408 #(.ShowInternalStructure("true")) u_7408_2 (
    .pin1(RB_O_6), .pin2(RA_O_6), .pin3(AND_O_6), .pin4(RB_O_5), .pin5(RA_O_5), .pin6(AND_O_5),
    .pin13(RA_O_7), .pin12(RB_O_7), .pin11(AND_O_7), .pin10(RA_O_8), .pin9(RB_O_8), .pin8(AND_O_8));
  _74244 #(.ShowInternalStructure("true")) u_74244_2 (
    .pin1(AND_EN), .pin2(AND_O_5), .pin3(O8), .pin4(AND_O_6), .pin5(O7), .pin6(AND_O_1), .pin7(O4),
    .pin8(AND_O_2), .pin9(O3), .pin19(AND_EN), .pin18(O5), .pin17(AND_O_8), .pin16(O6), .pin15(AND_O_7),
    .pin14(O1), .pin13(AND_O_4), .pin12(O2), .pin11(AND_O_3));
  LED led_1 (.in(RA_O_8));
  LED led_2 (.in(RA_O_7));
  LED led_3 (.in(RA_O_6));
  LED led_4 (.in(RA_O_5));
  LED led_5 (.in(RA_O_4));
  LED led_6 (.in(RA_O_3));
  LED led_7 (.in(RA_O_2));
  LED led_8 (.in(RA_O_1));
  _7432 #(.ShowInternalStructure("true")) u_7432_1 (
    .pin1(RB_O_2), .pin2(RA_O_2), .pin3(OR_O_2), .pin4(RB_O_1), .pin5(RA_O_1), .pin6(OR_O_1), .pin13(RA_O_3),
    .pin12(RB_O_3), .pin11(OR_O_3), .pin10(RA_O_4), .pin9(RB_O_4), .pin8(OR_O_4));
  _7432 #(.ShowInternalStructure("true")) u_7432_2 (
    .pin1(RB_O_6), .pin2(RA_O_6), .pin3(OR_O_6), .pin4(RB_O_5), .pin5(RA_O_5), .pin6(OR_O_5), .pin13(RA_O_7),
    .pin12(RB_O_7), .pin11(OR_O_7), .pin10(RA_O_8), .pin9(RB_O_8), .pin8(OR_O_8));
  _74244 #(.ShowInternalStructure("true")) u_74244_3 (
    .pin1(OR_EN), .pin2(OR_O_5), .pin3(O8), .pin4(OR_O_6), .pin5(O7), .pin6(OR_O_1), .pin7(O4),
    .pin8(OR_O_2), .pin9(O3), .pin19(OR_EN), .pin18(O5), .pin17(OR_O_8), .pin16(O6), .pin15(OR_O_7),
    .pin14(O1), .pin13(OR_O_4), .pin12(O2), .pin11(OR_O_3));
  LED led_9 (.in(RB_O_8));
  LED led_10 (.in(RB_O_7));
  LED led_11 (.in(RB_O_6));
  LED led_12 (.in(RB_O_5));
  _74138 #(.ShowInternalStructure("true")) u_74138_1 (
    .pin1(SL1), .pin2(SL2), .pin3(SL3), .pin4(n74138_1_pin4), .pin5(n74138_1_pin5), .pin6(n74138_1_pin6),
    .pin7(SHR_EN), .pin15(n74138_1_pin15), .pin14(SUM_EN), .pin13(AND_EN), .pin12(OR_EN), .pin11(NOT_EN),
    .pin10(XOR_EN), .pin9(SHL_EN));
  Pull_Resistor pull_resistor_2 (.node(n74138_1_pin4));
  Pull_Resistor pull_resistor_3 (.node(n74138_1_pin5));
  LED led_13 (.in(RB_O_4));
  LED led_14 (.in(RB_O_3));
  LED led_15 (.in(RB_O_2));
  LED led_16 (.in(RB_O_1));
  // NoConnect on n74138_1_pin15
  _7486 #(.ShowInternalStructure("true")) u_7486_1 (
    .pin1(RB_O_2), .pin2(RA_O_2), .pin3(XOR_O_2), .pin4(RB_O_1), .pin5(RA_O_1), .pin6(XOR_O_1),
    .pin13(RA_O_3), .pin12(RB_O_3), .pin11(XOR_O_3), .pin10(RA_O_4), .pin9(RB_O_4), .pin8(XOR_O_4));
  _7486 #(.ShowInternalStructure("true")) u_7486_2 (
    .pin1(RB_O_6), .pin2(RA_O_6), .pin3(XOR_O_6), .pin4(RB_O_5), .pin5(RA_O_5), .pin6(XOR_O_5),
    .pin13(RA_O_7), .pin12(RB_O_7), .pin11(XOR_O_7), .pin10(RA_O_8), .pin9(RB_O_8), .pin8(XOR_O_8));
  _74244 #(.ShowInternalStructure("true")) u_74244_4 (
    .pin1(XOR_EN), .pin2(XOR_O_5), .pin3(O8), .pin4(XOR_O_6), .pin5(O7), .pin6(XOR_O_1), .pin7(O4),
    .pin8(XOR_O_2), .pin9(O3), .pin19(XOR_EN), .pin18(O5), .pin17(XOR_O_8), .pin16(O6), .pin15(XOR_O_7),
    .pin14(O1), .pin13(XOR_O_4), .pin12(O2), .pin11(XOR_O_3));
  LED led_17 (.in(n_SUM_EN));
  LED led_18 (.in(n_AND_EN));
  LED led_19 (.in(n_OR_EN));
  LED led_20 (.in(n_NOT_EN));
  LED led_21 (.in(n_XOR_EN));
  LED led_22 (.in(n_SHL_EN));
  LED led_23 (.in(n_SHR_EN));
  Pull_Resistor pull_resistor_4 (.node(pull_resistor_4_node));
  // NoConnect on n7414_2_pin4
  Pull_Resistor pull_resistor_5 (.node(pull_resistor_5_node));
  // NoConnect on n7414_2_pin6
  _7414 #(.ShowInternalStructure("true")) u_7414_1 (
    .pin1(SUM_EN), .pin2(n_SUM_EN), .pin3(AND_EN), .pin4(n_AND_EN), .pin5(OR_EN), .pin6(n_OR_EN),
    .pin13(NOT_EN), .pin12(n_NOT_EN), .pin11(XOR_EN), .pin10(n_XOR_EN), .pin9(SHL_EN), .pin8(n_SHL_EN));
  _7414 #(.ShowInternalStructure("true")) u_7414_2 (
    .pin1(SHR_EN), .pin2(n_SHR_EN), .pin3(pull_resistor_4_node), .pin4(n7414_2_pin4),
    .pin5(pull_resistor_5_node), .pin6(n7414_2_pin6), .pin13(n7414_2_pin13), .pin12(n7414_2_pin12),
    .pin11(n7414_2_pin11), .pin10(n7414_2_pin10), .pin9(n7414_2_pin9), .pin8(n7414_2_pin8));
  Pull_Resistor pull_resistor_6 (.node(n7414_2_pin13));
  // NoConnect on n7414_2_pin12
  Pull_Resistor pull_resistor_7 (.node(n7414_2_pin11));
  // NoConnect on n7414_2_pin10
  Pull_Resistor pull_resistor_8 (.node(n7414_2_pin9));
  // NoConnect on n7414_2_pin8
  _74240 #(.ShowInternalStructure("true")) u_74240_1 (
    .pin1(NOT_EN), .pin2(RA_O_2), .pin3(O3), .pin4(RA_O_1), .pin5(O4), .pin6(RA_O_6), .pin7(O7),
    .pin8(RA_O_5), .pin9(O8), .pin19(NOT_EN), .pin18(O2), .pin17(RA_O_3), .pin16(O1), .pin15(RA_O_4),
    .pin14(O6), .pin13(RA_O_7), .pin12(O5), .pin11(RA_O_8));
  _74244 #(.ShowInternalStructure("true")) u_74244_5 (
    .pin1(SHL_EN), .pin2(RA_O_2), .pin3(O4), .pin4(RA_O_1), .pin5(O5), .pin6(RA_O_6), .pin7(O8),
    .pin8(RA_O_5), .pin9(O1), .pin19(SHL_EN), .pin18(O3), .pin17(RA_O_3), .pin16(O2), .pin15(RA_O_4),
    .pin14(O7), .pin13(RA_O_7), .pin12(O6), .pin11(n74244_5_pin11));
  Pull_Resistor pull_resistor_9 (.node(n74244_5_pin11));
  Pull_Resistor pull_resistor_10 (.node(pull_resistor_10_node));
  _74244 #(.ShowInternalStructure("true")) u_74244_6 (
    .pin1(SHR_EN), .pin2(RA_O_2), .pin3(O2), .pin4(pull_resistor_10_node), .pin5(O3), .pin6(RA_O_6),
    .pin7(O6), .pin8(RA_O_5), .pin9(O7), .pin19(SHR_EN), .pin18(O1), .pin17(RA_O_3), .pin16(O8),
    .pin15(RA_O_4), .pin14(O5), .pin13(RA_O_7), .pin12(O4), .pin11(RA_O_8));
  // also tied to VCC on the sheet: n74138_1_pin6

  // Other names for the same wires on the sheet: B_1 = B1; B_2 = B2; B_3 = B3; B_4 = B4; B_5 = B5; B_6 = B6; B_7 = B7;
  //   B_8 = B8; CLOCK = CLK; OUT_1 = O1; OUT_2 = O2; OUT_3 = O3; OUT_4 = O4; OUT_5 = O5; OUT_6 = O6; OUT_7 = O7;
  //   OUT_8 = O8; SI_1 = SL1; SI_2 = SL2; SI_3 = SL3

  // Notes on the sheet:
  //   SUM OPERATION
  //   REGISTERS "A" , "B"
  //   AND OPERATION
  //   OUT REG "A"
  //   OR OPERATION
  //   OUT REG "B"
  //   MODE SELECTOR
  //   OUT MODE
  //   XOR OPERATION
  //   OUT nMODES
  //   NOT OPERATION
  //   SHL OPERATION
  //   SHR OPERATION
endmodule

module COUNTERS_test (
  input  CLK,
  input  B1,
  input  B2,
  input  B3,
  input  B4,
  input  B5,
  input  B6,
  input  B7,
  input  B8,
  input  MC_n_Enable_Counter,
  input  MC_c_Clear,
  input  MC_n_Enable_Load,
  input  C_n_Enable_Counter,
  input  C_n_Clear,
  input  C_n_Enable_Load,
  input  OR_n_EN1,
  input  OR_n_EN2,
  input  OR_n_EN_Out,
  input  UAR_n_EN1,
  input  UAR_n_EN2,
  input  UAR_n_EN_Out,
  input  CAR_n_EN1,
  input  CAR_n_EN2,
  input  CAR_n_EN_Out,
  output MCA1,
  output AB1,
  output MCA2,
  output AB2,
  output MCA3,
  output AB3,
  output MCA4,
  output AB4,
  output MCA5,
  output AB5,
  output MCA6,
  output AB6,
  output MCA7,
  output AB7,
  output MCA8,
  output AB8,
  output MCA9,
  output AB9,
  output MCA10,
  output AB10,
  output MCA11,
  output AB11,
  output MCA12,
  output AB12,
  output MCA13,
  output AB13,
  output MCA14,
  output AB14,
  output MCA15,
  output AB15,
  output MCA16,
  output AB16
);

  MC_Counter mc_counter_1 (
    .CLK(CLK), .B1(B1), .B2(B2), .B3(B3), .B4(B4), .B5(B5), .B6(B6), .B7(B7), .B8(B8),
    .MC_n_Enable_Counter(MC_n_Enable_Counter), .MC_n_Clear(MC_c_Clear), .MC_n_Enable_Load(MC_n_Enable_Load),
    .OR_n_EN1(OR_n_EN1), .OR_n_EN2(OR_n_EN2), .OR_n_EN_Out(OR_n_EN_Out), .MCA1(MCA1), .MCA2(MCA2),
    .MCA3(MCA3), .MCA4(MCA4), .MCA5(MCA5), .MCA6(MCA6), .MCA7(MCA7), .MCA8(MCA8), .MCA9(MCA9), .MCA10(MCA10),
    .MCA11(MCA11), .MCA12(MCA12), .MCA13(MCA13), .MCA14(MCA14), .MCA15(MCA15), .MCA16(MCA16));
  C_Counter c_counter_1 (
    .CLK(CLK), .B1(B1), .B2(B2), .B3(B3), .B4(B4), .B5(B5), .B6(B6), .B7(B7), .B8(B8),
    .C_n_Enable_Counter(C_n_Enable_Counter), .C_n_Clear(C_n_Clear), .C_n_Enable_Load(C_n_Enable_Load),
    .UAR_n_EN1(UAR_n_EN1), .UAR_n_EN2(UAR_n_EN2), .UAR_n_EN_Out(UAR_n_EN_Out), .CAR_n_EN1(CAR_n_EN1),
    .CAR_n_EN2(CAR_n_EN2), .CAR_n_EN_Out(CAR_n_EN_Out), .AB1(AB1), .AB2(AB2), .AB3(AB3), .AB4(AB4),
    .AB5(AB5), .AB6(AB6), .AB7(AB7), .AB8(AB8), .AB9(AB9), .AB10(AB10), .AB11(AB11), .AB12(AB12),
    .AB13(AB13), .AB14(AB14), .AB15(AB15), .AB16(AB16));

  // Other names for the same wires on the sheet: AB_1 = AB1; AB_2 = AB2; AB_3 = AB3; AB_4 = AB4; AB_5 = AB5;
  //   AB_6 = AB6; AB_7 = AB7; AB_8 = AB8; AB_9 = AB9; AB_10 = AB10; AB_11 = AB11; AB_12 = AB12; AB_13 = AB13;
  //   AB_14 = AB14; AB_15 = AB15; AB_16 = AB16; C_Clock = CLK; DB_1 = B1; DB_2 = B2; DB_3 = B3; DB_4 = B4; DB_5 = B5;
  //   DB_6 = B6; DB_7 = B7; DB_8 = B8; MC_n_Clear = MC_c_Clear; MCA_1 = MCA1; MCA_2 = MCA2; MCA_3 = MCA3;
  //   MCA_4 = MCA4; MCA_5 = MCA5; MCA_6 = MCA6; MCA_7 = MCA7; MCA_8 = MCA8; MCA_9 = MCA9; MCA_10 = MCA10;
  //   MCA_11 = MCA11; MCA_12 = MCA12; MCA_13 = MCA13; MCA_14 = MCA14; MCA_15 = MCA15; MCA_16 = MCA16
endmodule

module MC_Counter (
  input  CLK,
  input  B1,
  input  B2,
  input  B3,
  input  B4,
  input  B5,
  input  B6,
  input  B7,
  input  B8,
  input  MC_n_Enable_Counter,
  input  MC_n_Clear,
  input  MC_n_Enable_Load,
  input  OR_n_EN1,
  input  OR_n_EN2,
  input  OR_n_EN_Out,
  output MCA1,
  output MCA2,
  output MCA3,
  output MCA4,
  output MCA5,
  output MCA6,
  output MCA7,
  output MCA8,
  output MCA9,
  output MCA10,
  output MCA11,
  output MCA12,
  output MCA13,
  output MCA14,
  output MCA15,
  output MCA16
);

  wire in_OR_O_1, in_OR_O_2, in_OR_O_3, in_OR_O_4, in_OR_O_5, in_OR_O_6, in_OR_O_7, in_OR_O_8, in_OR_O_9,
       in_OR_O_10, in_OR_O_11, in_OR_O_12, in_OR_O_13, in_OR_O_14, in_OR_O_15, in_OR_O_16, MC_RCO_1,
       MC_RCO_2, MC_RCO_3, n7404_1_pin4, n7404_1_pin6, n7404_1_pin8, n7404_1_pin9, n7404_1_pin10,
       n7404_1_pin11, n7404_1_pin12, n7404_1_pin13, n74163_4_pin15, n_C_Clock, OR_O_1, OR_O_2, OR_O_3,
       OR_O_4, OR_O_5, OR_O_6, OR_O_7, OR_O_8, OR_O_9, OR_O_10, OR_O_11, OR_O_12, OR_O_13, OR_O_14, OR_O_15,
       OR_O_16, Power, pull_resistor_1_node, pull_resistor_2_node;

  _74244 #(.ShowInternalStructure("true")) u_74244_1 (
    .pin1(OR_n_EN_Out), .pin2(in_OR_O_2), .pin3(OR_O_1), .pin4(in_OR_O_4), .pin5(OR_O_3), .pin6(in_OR_O_6),
    .pin7(OR_O_5), .pin8(in_OR_O_8), .pin9(OR_O_7), .pin19(OR_n_EN_Out), .pin18(OR_O_2), .pin17(in_OR_O_1),
    .pin16(OR_O_4), .pin15(in_OR_O_3), .pin14(OR_O_6), .pin13(in_OR_O_5), .pin12(OR_O_8), .pin11(in_OR_O_7));
  _74244 #(.ShowInternalStructure("true")) u_74244_2 (
    .pin1(OR_n_EN_Out), .pin2(in_OR_O_10), .pin3(OR_O_9), .pin4(in_OR_O_12), .pin5(OR_O_11),
    .pin6(in_OR_O_14), .pin7(OR_O_13), .pin8(in_OR_O_16), .pin9(OR_O_15), .pin19(OR_n_EN_Out),
    .pin18(OR_O_10), .pin17(in_OR_O_9), .pin16(OR_O_12), .pin15(in_OR_O_11), .pin14(OR_O_14),
    .pin13(in_OR_O_13), .pin12(OR_O_16), .pin11(in_OR_O_15));
  _74377 #(.ShowInternalStructure("true")) u_74377_1 (
    .pin1(OR_n_EN1), .pin2(in_OR_O_8), .pin3(B8), .pin4(B6), .pin5(in_OR_O_6), .pin6(in_OR_O_4), .pin7(B4),
    .pin8(B2), .pin9(in_OR_O_2), .pin19(in_OR_O_7), .pin18(B7), .pin17(B5), .pin16(in_OR_O_5),
    .pin15(in_OR_O_3), .pin14(B3), .pin13(B1), .pin12(in_OR_O_1), .pin11(CLK));
  _74377 #(.ShowInternalStructure("true")) u_74377_2 (
    .pin1(OR_n_EN2), .pin2(in_OR_O_16), .pin3(B8), .pin4(B6), .pin5(in_OR_O_14), .pin6(in_OR_O_12),
    .pin7(B4), .pin8(B2), .pin9(in_OR_O_10), .pin19(in_OR_O_15), .pin18(B7), .pin17(B5), .pin16(in_OR_O_13),
    .pin15(in_OR_O_11), .pin14(B3), .pin13(B1), .pin12(in_OR_O_9), .pin11(CLK));
  Pull_Resistor pull_resistor_1 (.node(pull_resistor_1_node));
  // NoConnect on n7404_1_pin4
  Pull_Resistor pull_resistor_2 (.node(pull_resistor_2_node));
  // NoConnect on n7404_1_pin6
  _74163 #(.ShowInternalStructure("true")) u_74163_1 (
    .pin1(MC_n_Clear), .pin2(n_C_Clock), .pin3(OR_O_1), .pin4(OR_O_2), .pin5(OR_O_3), .pin6(OR_O_4),
    .pin7(MC_n_Enable_Counter), .pin15(MC_RCO_1), .pin14(MCA1), .pin13(MCA2), .pin12(MCA3), .pin11(MCA4),
    .pin10(Power), .pin9(MC_n_Enable_Load));
  _74163 #(.ShowInternalStructure("true")) u_74163_2 (
    .pin1(MC_n_Clear), .pin2(n_C_Clock), .pin3(OR_O_5), .pin4(OR_O_6), .pin5(OR_O_7), .pin6(OR_O_8),
    .pin7(MC_n_Enable_Counter), .pin15(MC_RCO_2), .pin14(MCA5), .pin13(MCA6), .pin12(MCA7), .pin11(MCA8),
    .pin10(MC_RCO_1), .pin9(MC_n_Enable_Load));
  _74163 #(.ShowInternalStructure("true")) u_74163_3 (
    .pin1(MC_n_Clear), .pin2(n_C_Clock), .pin3(OR_O_9), .pin4(OR_O_10), .pin5(OR_O_11), .pin6(OR_O_12),
    .pin7(MC_n_Enable_Counter), .pin15(MC_RCO_3), .pin14(MCA9), .pin13(MCA10), .pin12(MCA11), .pin11(MCA12),
    .pin10(MC_RCO_2), .pin9(MC_n_Enable_Load));
  _74163 #(.ShowInternalStructure("true")) u_74163_4 (
    .pin1(MC_n_Clear), .pin2(n_C_Clock), .pin3(OR_O_13), .pin4(OR_O_14), .pin5(OR_O_15), .pin6(OR_O_16),
    .pin7(MC_n_Enable_Counter), .pin15(n74163_4_pin15), .pin14(MCA13), .pin13(MCA14), .pin12(MCA15),
    .pin11(MCA16), .pin10(MC_RCO_3), .pin9(MC_n_Enable_Load));
  // NoConnect on n74163_4_pin15
  _7404 #(.ShowInternalStructure("true")) u_7404_1 (
    .pin1(CLK), .pin2(n_C_Clock), .pin3(pull_resistor_1_node), .pin4(n7404_1_pin4),
    .pin5(pull_resistor_2_node), .pin6(n7404_1_pin6), .pin13(n7404_1_pin13), .pin12(n7404_1_pin12),
    .pin11(n7404_1_pin11), .pin10(n7404_1_pin10), .pin9(n7404_1_pin9), .pin8(n7404_1_pin8));
  Pull_Resistor pull_resistor_3 (.node(n7404_1_pin13));
  // NoConnect on n7404_1_pin12
  Pull_Resistor pull_resistor_4 (.node(n7404_1_pin11));
  // NoConnect on n7404_1_pin10
  Pull_Resistor pull_resistor_5 (.node(n7404_1_pin9));
  // NoConnect on n7404_1_pin8
  // also tied to VCC on the sheet: Power

  // Other names for the same wires on the sheet: C_Clock = CLK; DB_1 = B1; DB_2 = B2; DB_3 = B3; DB_4 = B4; DB_5 = B5;
  //   DB_6 = B6; DB_7 = B7; DB_8 = B8; MCA_1 = MCA1; MCA_2 = MCA2; MCA_3 = MCA3; MCA_4 = MCA4; MCA_5 = MCA5;
  //   MCA_6 = MCA6; MCA_7 = MCA7; MCA_8 = MCA8; MCA_9 = MCA9; MCA_10 = MCA10; MCA_11 = MCA11; MCA_12 = MCA12;
  //   MCA_13 = MCA13; MCA_14 = MCA14; MCA_15 = MCA15; MCA_16 = MCA16

  // Notes on the sheet:
  //   Opcode Register
  //   Microcommands Counter
endmodule

module C_Counter (
  input  CLK,
  input  B1,
  input  B2,
  input  B3,
  input  B4,
  input  B5,
  input  B6,
  input  B7,
  input  B8,
  input  C_n_Enable_Counter,
  input  C_n_Clear,
  input  C_n_Enable_Load,
  input  UAR_n_EN1,
  input  UAR_n_EN2,
  input  UAR_n_EN_Out,
  input  CAR_n_EN1,
  input  CAR_n_EN2,
  input  CAR_n_EN_Out,
  output AB1,
  output AB2,
  output AB3,
  output AB4,
  output AB5,
  output AB6,
  output AB7,
  output AB8,
  output AB9,
  output AB10,
  output AB11,
  output AB12,
  output AB13,
  output AB14,
  output AB15,
  output AB16
);

  wire C_RCO_1, C_RCO_2, C_RCO_3, CR_O_1, CR_O_2, CR_O_3, CR_O_4, CR_O_5, CR_O_6, CR_O_7, CR_O_8, CR_O_9,
       CR_O_10, CR_O_11, CR_O_12, CR_O_13, CR_O_14, CR_O_15, CR_O_16, in_CAR_O_1, in_CAR_O_2, in_CAR_O_3,
       in_CAR_O_4, in_CAR_O_5, in_CAR_O_6, in_CAR_O_7, in_CAR_O_8, in_CAR_O_9, in_CAR_O_10, in_CAR_O_11,
       in_CAR_O_12, in_CAR_O_13, in_CAR_O_14, in_CAR_O_15, in_CAR_O_16, in_UAR_O_1, in_UAR_O_2, in_UAR_O_3,
       in_UAR_O_4, in_UAR_O_5, in_UAR_O_6, in_UAR_O_7, in_UAR_O_8, in_UAR_O_9, in_UAR_O_10, in_UAR_O_11,
       in_UAR_O_12, in_UAR_O_13, in_UAR_O_14, in_UAR_O_15, in_UAR_O_16, n7404_1_pin4, n7404_1_pin6,
       n7404_1_pin8, n7404_1_pin9, n7404_1_pin10, n7404_1_pin11, n7404_1_pin12, n7404_1_pin13,
       n74163_4_pin15, n_C_Clock, Power, pull_resistor_1_node, pull_resistor_2_node;

  Pull_Resistor pull_resistor_1 (.node(pull_resistor_1_node));
  // NoConnect on n7404_1_pin4
  Pull_Resistor pull_resistor_2 (.node(pull_resistor_2_node));
  // NoConnect on n7404_1_pin6
  _7404 #(.ShowInternalStructure("true")) u_7404_1 (
    .pin1(CLK), .pin2(n_C_Clock), .pin3(pull_resistor_1_node), .pin4(n7404_1_pin4),
    .pin5(pull_resistor_2_node), .pin6(n7404_1_pin6), .pin13(n7404_1_pin13), .pin12(n7404_1_pin12),
    .pin11(n7404_1_pin11), .pin10(n7404_1_pin10), .pin9(n7404_1_pin9), .pin8(n7404_1_pin8));
  Pull_Resistor pull_resistor_3 (.node(n7404_1_pin13));
  // NoConnect on n7404_1_pin12
  Pull_Resistor pull_resistor_4 (.node(n7404_1_pin11));
  // NoConnect on n7404_1_pin10
  Pull_Resistor pull_resistor_5 (.node(n7404_1_pin9));
  // NoConnect on n7404_1_pin8
  _74377 #(.ShowInternalStructure("true")) u_74377_1 (
    .pin1(UAR_n_EN1), .pin2(in_UAR_O_8), .pin3(B8), .pin4(B6), .pin5(in_UAR_O_6), .pin6(in_UAR_O_4),
    .pin7(B4), .pin8(B2), .pin9(in_UAR_O_2), .pin19(in_UAR_O_7), .pin18(B7), .pin17(B5), .pin16(in_UAR_O_5),
    .pin15(in_UAR_O_3), .pin14(B3), .pin13(B1), .pin12(in_UAR_O_1), .pin11(CLK));
  _74244 #(.ShowInternalStructure("true")) u_74244_1 (
    .pin1(UAR_n_EN_Out), .pin2(in_UAR_O_2), .pin3(CR_O_1), .pin4(in_UAR_O_4), .pin5(CR_O_3),
    .pin6(in_UAR_O_6), .pin7(CR_O_5), .pin8(in_UAR_O_8), .pin9(CR_O_7), .pin19(UAR_n_EN_Out), .pin18(CR_O_2),
    .pin17(in_UAR_O_1), .pin16(CR_O_4), .pin15(in_UAR_O_3), .pin14(CR_O_6), .pin13(in_UAR_O_5),
    .pin12(CR_O_8), .pin11(in_UAR_O_7));
  _74377 #(.ShowInternalStructure("true")) u_74377_2 (
    .pin1(UAR_n_EN2), .pin2(in_UAR_O_16), .pin3(B8), .pin4(B6), .pin5(in_UAR_O_14), .pin6(in_UAR_O_12),
    .pin7(B4), .pin8(B2), .pin9(in_UAR_O_10), .pin19(in_UAR_O_15), .pin18(B7), .pin17(B5),
    .pin16(in_UAR_O_13), .pin15(in_UAR_O_11), .pin14(B3), .pin13(B1), .pin12(in_UAR_O_9), .pin11(CLK));
  _74244 #(.ShowInternalStructure("true")) u_74244_2 (
    .pin1(UAR_n_EN_Out), .pin2(in_UAR_O_10), .pin3(CR_O_9), .pin4(in_UAR_O_12), .pin5(CR_O_11),
    .pin6(in_UAR_O_14), .pin7(CR_O_13), .pin8(in_UAR_O_16), .pin9(CR_O_15), .pin19(UAR_n_EN_Out),
    .pin18(CR_O_10), .pin17(in_UAR_O_9), .pin16(CR_O_12), .pin15(in_UAR_O_11), .pin14(CR_O_14),
    .pin13(in_UAR_O_13), .pin12(CR_O_16), .pin11(in_UAR_O_15));
  _74163 #(.ShowInternalStructure("true")) u_74163_1 (
    .pin1(C_n_Clear), .pin2(CLK), .pin3(CR_O_1), .pin4(CR_O_2), .pin5(CR_O_3), .pin6(CR_O_4),
    .pin7(C_n_Enable_Counter), .pin15(C_RCO_1), .pin14(AB1), .pin13(AB2), .pin12(AB3), .pin11(AB4),
    .pin10(Power), .pin9(C_n_Enable_Load));
  _74163 #(.ShowInternalStructure("true")) u_74163_2 (
    .pin1(C_n_Clear), .pin2(CLK), .pin3(CR_O_5), .pin4(CR_O_6), .pin5(CR_O_7), .pin6(CR_O_8),
    .pin7(C_n_Enable_Counter), .pin15(C_RCO_2), .pin14(AB5), .pin13(AB6), .pin12(AB7), .pin11(AB8),
    .pin10(C_RCO_1), .pin9(C_n_Enable_Load));
  _74163 #(.ShowInternalStructure("true")) u_74163_3 (
    .pin1(C_n_Clear), .pin2(CLK), .pin3(CR_O_9), .pin4(CR_O_10), .pin5(CR_O_11), .pin6(CR_O_12),
    .pin7(C_n_Enable_Counter), .pin15(C_RCO_3), .pin14(AB9), .pin13(AB10), .pin12(AB11), .pin11(AB12),
    .pin10(C_RCO_2), .pin9(C_n_Enable_Load));
  _74163 #(.ShowInternalStructure("true")) u_74163_4 (
    .pin1(C_n_Clear), .pin2(CLK), .pin3(CR_O_13), .pin4(CR_O_14), .pin5(CR_O_15), .pin6(CR_O_16),
    .pin7(C_n_Enable_Counter), .pin15(n74163_4_pin15), .pin14(AB13), .pin13(AB14), .pin12(AB15),
    .pin11(AB16), .pin10(C_RCO_3), .pin9(C_n_Enable_Load));
  // NoConnect on n74163_4_pin15
  _74377 #(.ShowInternalStructure("true")) u_74377_3 (
    .pin1(CAR_n_EN1), .pin2(in_CAR_O_1), .pin3(AB1), .pin4(AB2), .pin5(in_CAR_O_2), .pin6(in_CAR_O_3),
    .pin7(AB3), .pin8(AB4), .pin9(in_CAR_O_4), .pin19(in_CAR_O_8), .pin18(AB8), .pin17(AB7),
    .pin16(in_CAR_O_7), .pin15(in_CAR_O_6), .pin14(AB6), .pin13(AB5), .pin12(in_CAR_O_5), .pin11(n_C_Clock));
  _74244 #(.ShowInternalStructure("true")) u_74244_3 (
    .pin1(CAR_n_EN_Out), .pin2(in_CAR_O_1), .pin3(CR_O_8), .pin4(in_CAR_O_2), .pin5(CR_O_7),
    .pin6(in_CAR_O_3), .pin7(CR_O_6), .pin8(in_CAR_O_4), .pin9(CR_O_5), .pin19(CAR_n_EN_Out), .pin18(CR_O_1),
    .pin17(in_CAR_O_8), .pin16(CR_O_2), .pin15(in_CAR_O_7), .pin14(CR_O_3), .pin13(in_CAR_O_6),
    .pin12(CR_O_4), .pin11(in_CAR_O_5));
  _74377 #(.ShowInternalStructure("true")) u_74377_4 (
    .pin1(CAR_n_EN2), .pin2(in_CAR_O_9), .pin3(AB9), .pin4(AB10), .pin5(in_CAR_O_10), .pin6(in_CAR_O_11),
    .pin7(AB11), .pin8(AB12), .pin9(in_CAR_O_12), .pin19(in_CAR_O_16), .pin18(AB16), .pin17(AB15),
    .pin16(in_CAR_O_15), .pin15(in_CAR_O_14), .pin14(AB14), .pin13(AB13), .pin12(in_CAR_O_13),
    .pin11(n_C_Clock));
  _74244 #(.ShowInternalStructure("true")) u_74244_4 (
    .pin1(CAR_n_EN_Out), .pin2(in_CAR_O_9), .pin3(CR_O_16), .pin4(in_CAR_O_10), .pin5(CR_O_15),
    .pin6(in_CAR_O_11), .pin7(CR_O_14), .pin8(in_CAR_O_12), .pin9(CR_O_13), .pin19(CAR_n_EN_Out),
    .pin18(CR_O_9), .pin17(in_CAR_O_16), .pin16(CR_O_10), .pin15(in_CAR_O_15), .pin14(CR_O_11),
    .pin13(in_CAR_O_14), .pin12(CR_O_12), .pin11(in_CAR_O_13));
  // also tied to VCC on the sheet: Power

  // Other names for the same wires on the sheet: AB_1 = AB1; AB_2 = AB2; AB_3 = AB3; AB_4 = AB4; AB_5 = AB5;
  //   AB_6 = AB6; AB_7 = AB7; AB_8 = AB8; AB_9 = AB9; AB_10 = AB10; AB_11 = AB11; AB_12 = AB12; AB_13 = AB13;
  //   AB_14 = AB14; AB_15 = AB15; AB_16 = AB16; C_Clock = CLK; DB_1 = B1; DB_2 = B2; DB_3 = B3; DB_4 = B4; DB_5 = B5;
  //   DB_6 = B6; DB_7 = B7; DB_8 = B8

  // Notes on the sheet:
  //   User Address Register
  //   Counter
  //   Current Address Register
endmodule

module USER_REGISTER_BLOCK (
  input  CLK,
  input  B_1,
  input  B_2,
  input  B_3,
  input  B_4,
  input  B_5,
  input  B_6,
  input  B_7,
  input  B_8,
  input  W_UREG_0,
  input  W_UREG_1,
  input  W_UREG_2,
  input  R_UREG_0,
  input  R_UREG_1,
  input  R_UREG_2,
  input  URB_READ,
  input  URB_WRITE,
  output OB_1,
  output OB_2,
  output OB_3,
  output OB_4,
  output OB_5,
  output OB_6,
  output OB_7,
  output OB_8
);

  wire R_REG_0, R_REG_1, R_REG_2, R_REG_3, R_REG_4, R_REG_5, R_REG_6, R_REG_7, URN_0, URN_1, URN_2, W_REG_0,
       W_REG_1, W_REG_2, W_REG_3, W_REG_4, W_REG_5, W_REG_6, W_REG_7;

  USER_REGISTER_BLOCK_Controls CONTROL (
    .URB_READ(URB_READ), .URB_WRITE(URB_WRITE), .URN_0(URN_0), .URN_1(URN_1), .URN_2(URN_2),
    .W_REG_0(W_REG_0), .W_REG_1(W_REG_1), .W_REG_2(W_REG_2), .W_REG_3(W_REG_3), .W_REG_4(W_REG_4),
    .W_REG_5(W_REG_5), .W_REG_6(W_REG_6), .W_REG_7(W_REG_7), .R_REG_0(R_REG_0), .R_REG_1(R_REG_1),
    .R_REG_2(R_REG_2), .R_REG_3(R_REG_3), .R_REG_4(R_REG_4), .R_REG_5(R_REG_5), .R_REG_6(R_REG_6),
    .R_REG_7(R_REG_7));
  // USER_REGISTER_BLOCK_Numbers NUMBERS_STORAGE: pin names not known; wires that end beside it: W_UREG_0, W_UREG_1, W_UREG_2, R_UREG_0, R_UREG_1, R_UREG_2, B_1, B_2, B_3, B_4, B_5, B_6, B_7, B_8, CLK, URN_0, URN_1, URN_2
  USER_REGISTER_BLOCK_Items CELLS (
    .CLK(CLK), .B_1(B_1), .B_2(B_2), .B_3(B_3), .B_4(B_4), .B_5(B_5), .B_6(B_6), .B_7(B_7), .B_8(B_8),
    .W_REG_0(W_REG_0), .W_REG_1(W_REG_1), .W_REG_2(W_REG_2), .W_REG_3(W_REG_3), .W_REG_4(W_REG_4),
    .W_REG_5(W_REG_5), .W_REG_6(W_REG_6), .W_REG_7(W_REG_7), .R_REG_0(R_REG_0), .R_REG_1(R_REG_1),
    .R_REG_2(R_REG_2), .R_REG_3(R_REG_3), .R_REG_4(R_REG_4), .R_REG_5(R_REG_5), .R_REG_6(R_REG_6),
    .R_REG_7(R_REG_7), .OB_1(OB_1), .OB_2(OB_2), .OB_3(OB_3), .OB_4(OB_4), .OB_5(OB_5), .OB_6(OB_6),
    .OB_7(OB_7), .OB_8(OB_8));

  // Other names for the same wires on the sheet: CPU_Clock = CLK; DB_1 = B_1; DB_2 = B_2; DB_3 = B_3; DB_4 = B_4;
  //   DB_5 = B_5; DB_6 = B_6; DB_7 = B_7; DB_8 = B_8; UserRegistersBlock_READ = URB_READ;
  //   UserRegistersBlock_WRITE = URB_WRITE

  // Notes on the sheet:
  //   USER REGISTERS BLOCK
endmodule

module USER_REGISTER_BLOCK_Controls (
  input  URB_READ,
  input  URB_WRITE,
  input  URN_0,
  input  URN_1,
  input  URN_2,
  output W_REG_0,
  output W_REG_1,
  output W_REG_2,
  output W_REG_3,
  output W_REG_4,
  output W_REG_5,
  output W_REG_6,
  output W_REG_7,
  output R_REG_0,
  output R_REG_1,
  output R_REG_2,
  output R_REG_3,
  output R_REG_4,
  output R_REG_5,
  output R_REG_6,
  output R_REG_7
);

  wire n74138_1_pin6, pull_resistor_1_node, pull_resistor_2_node, REG_0, REG_1, REG_2, REG_3, REG_4, REG_5,
       REG_6, REG_7, REG_IM_0, REG_IM_1, REG_IM_2, REG_IM_3, REG_IM_4, REG_IM_5, REG_IM_6, REG_IM_7,
       W_REG_IM_0, W_REG_IM_1, W_REG_IM_2, W_REG_IM_3, W_REG_IM_4, W_REG_IM_5, W_REG_IM_6, W_REG_IM_7;

  LED led_1 (.in(REG_0));
  LED led_2 (.in(REG_1));
  LED led_3 (.in(REG_2));
  LED led_4 (.in(REG_3));
  LED led_5 (.in(REG_4));
  LED led_6 (.in(REG_5));
  LED led_7 (.in(REG_6));
  LED led_8 (.in(REG_7));
  Pull_Resistor pull_resistor_1 (.node(pull_resistor_1_node));
  Pull_Resistor pull_resistor_2 (.node(pull_resistor_2_node));
  _74138 #(.ShowInternalStructure("true")) u_74138_1 (
    .pin1(URN_0), .pin2(URN_1), .pin3(URN_2), .pin4(pull_resistor_1_node), .pin5(pull_resistor_2_node),
    .pin6(n74138_1_pin6), .pin7(REG_7), .pin15(REG_0), .pin14(REG_1), .pin13(REG_2), .pin12(REG_3),
    .pin11(REG_4), .pin10(REG_5), .pin9(REG_6));
  _7436 #(.ShowInternalStructure("true")) u_7436_1 (
    .pin1(URB_READ), .pin2(REG_0), .pin3(REG_IM_0), .pin4(URB_READ), .pin5(REG_1), .pin6(REG_IM_1),
    .pin13(URB_READ), .pin12(REG_3), .pin11(REG_IM_3), .pin10(URB_READ), .pin9(REG_2), .pin8(REG_IM_2));
  _7432 #(.ShowInternalStructure("true")) u_7432_1 (
    .pin1(REG_IM_0), .pin2(REG_0), .pin3(R_REG_0), .pin4(REG_IM_1), .pin5(REG_1), .pin6(R_REG_1),
    .pin13(REG_IM_3), .pin12(REG_3), .pin11(R_REG_3), .pin10(REG_IM_2), .pin9(REG_2), .pin8(R_REG_2));
  _7436 #(.ShowInternalStructure("true")) u_7436_2 (
    .pin1(URB_READ), .pin2(REG_4), .pin3(REG_IM_4), .pin4(URB_READ), .pin5(REG_5), .pin6(REG_IM_5),
    .pin13(URB_READ), .pin12(REG_7), .pin11(REG_IM_7), .pin10(URB_READ), .pin9(REG_6), .pin8(REG_IM_6));
  _7432 #(.ShowInternalStructure("true")) u_7432_2 (
    .pin1(REG_IM_4), .pin2(REG_4), .pin3(R_REG_4), .pin4(REG_IM_5), .pin5(REG_5), .pin6(R_REG_5),
    .pin13(REG_IM_7), .pin12(REG_7), .pin11(R_REG_7), .pin10(REG_IM_6), .pin9(REG_6), .pin8(R_REG_6));
  _7436 #(.ShowInternalStructure("true")) u_7436_3 (
    .pin1(URB_WRITE), .pin2(REG_0), .pin3(W_REG_IM_0), .pin4(URB_WRITE), .pin5(REG_1), .pin6(W_REG_IM_1),
    .pin13(URB_WRITE), .pin12(REG_3), .pin11(W_REG_IM_3), .pin10(URB_WRITE), .pin9(REG_2), .pin8(W_REG_IM_2));
  _7432 #(.ShowInternalStructure("true")) u_7432_3 (
    .pin1(W_REG_IM_0), .pin2(REG_0), .pin3(W_REG_0), .pin4(W_REG_IM_1), .pin5(REG_1), .pin6(W_REG_1),
    .pin13(W_REG_IM_3), .pin12(REG_3), .pin11(W_REG_3), .pin10(W_REG_IM_2), .pin9(REG_2), .pin8(W_REG_2));
  _7436 #(.ShowInternalStructure("true")) u_7436_4 (
    .pin1(URB_WRITE), .pin2(REG_4), .pin3(W_REG_IM_4), .pin4(URB_WRITE), .pin5(REG_5), .pin6(W_REG_IM_5),
    .pin13(URB_WRITE), .pin12(REG_7), .pin11(W_REG_IM_7), .pin10(URB_WRITE), .pin9(REG_6), .pin8(W_REG_IM_6));
  _7432 #(.ShowInternalStructure("true")) u_7432_4 (
    .pin1(W_REG_IM_4), .pin2(REG_4), .pin3(W_REG_4), .pin4(W_REG_IM_5), .pin5(REG_5), .pin6(W_REG_5),
    .pin13(W_REG_IM_7), .pin12(REG_7), .pin11(W_REG_7), .pin10(W_REG_IM_6), .pin9(REG_6), .pin8(W_REG_6));
  // also tied to VCC on the sheet: n74138_1_pin6

  // Other names for the same wires on the sheet: UserRegistersBlock_READ = URB_READ;
  //   UserRegistersBlock_WRITE = URB_WRITE

  // Notes on the sheet:
  //   or(REG_N, not(or(EN, REG_N))
endmodule

module USER_REGISTER_BLOCK_Items (
  input  CLK,
  input  B_1,
  input  B_2,
  input  B_3,
  input  B_4,
  input  B_5,
  input  B_6,
  input  B_7,
  input  B_8,
  input  W_REG_0,
  input  W_REG_1,
  input  W_REG_2,
  input  W_REG_3,
  input  W_REG_4,
  input  W_REG_5,
  input  W_REG_6,
  input  W_REG_7,
  input  R_REG_0,
  input  R_REG_1,
  input  R_REG_2,
  input  R_REG_3,
  input  R_REG_4,
  input  R_REG_5,
  input  R_REG_6,
  input  R_REG_7,
  output OB_1,
  output OB_2,
  output OB_3,
  output OB_4,
  output OB_5,
  output OB_6,
  output OB_7,
  output OB_8
);

  wire REG_0_O0, REG_0_O1, REG_0_O2, REG_0_O3, REG_0_O4, REG_0_O5, REG_0_O6, REG_0_O7, REG_1_O0, REG_1_O1,
       REG_1_O2, REG_1_O3, REG_1_O4, REG_1_O5, REG_1_O6, REG_1_O7, REG_2_O0, REG_2_O1, REG_2_O2, REG_2_O3,
       REG_2_O4, REG_2_O5, REG_2_O6, REG_2_O7, REG_3_O0, REG_3_O1, REG_3_O2, REG_3_O3, REG_3_O4, REG_3_O5,
       REG_3_O6, REG_3_O7, REG_4_O0, REG_4_O1, REG_4_O2, REG_4_O3, REG_4_O4, REG_4_O5, REG_4_O6, REG_4_O7,
       REG_5_O0, REG_5_O1, REG_5_O2, REG_5_O3, REG_5_O4, REG_5_O5, REG_5_O6, REG_5_O7, REG_6_O0, REG_6_O1,
       REG_6_O2, REG_6_O3, REG_6_O4, REG_6_O5, REG_6_O6, REG_6_O7, REG_7_O0, REG_7_O1, REG_7_O2, REG_7_O3,
       REG_7_O4, REG_7_O5, REG_7_O6, REG_7_O7;

  _74377 #(.ShowInternalStructure("true")) u_74377_1 (
    .pin1(W_REG_0), .pin2(REG_0_O0), .pin3(B_1), .pin4(B_2), .pin5(REG_0_O1), .pin6(REG_0_O2), .pin7(B_3),
    .pin8(B_4), .pin9(REG_0_O3), .pin19(REG_0_O7), .pin18(B_8), .pin17(B_7), .pin16(REG_0_O6),
    .pin15(REG_0_O5), .pin14(B_6), .pin13(B_5), .pin12(REG_0_O4), .pin11(CLK));
  _74244 #(.ShowInternalStructure("true")) u_74244_1 (
    .pin1(R_REG_0), .pin2(REG_0_O0), .pin3(OB_8), .pin4(REG_0_O1), .pin5(OB_7), .pin6(REG_0_O2), .pin7(OB_6),
    .pin8(REG_0_O3), .pin9(OB_5), .pin19(R_REG_0), .pin18(OB_1), .pin17(REG_0_O7), .pin16(OB_2),
    .pin15(REG_0_O6), .pin14(OB_3), .pin13(REG_0_O5), .pin12(OB_4), .pin11(REG_0_O4));
  _74377 #(.ShowInternalStructure("true")) u_74377_2 (
    .pin1(W_REG_4), .pin2(REG_4_O0), .pin3(B_1), .pin4(B_2), .pin5(REG_4_O1), .pin6(REG_4_O2), .pin7(B_3),
    .pin8(B_4), .pin9(REG_4_O3), .pin19(REG_4_O7), .pin18(B_8), .pin17(B_7), .pin16(REG_4_O6),
    .pin15(REG_4_O5), .pin14(B_6), .pin13(B_5), .pin12(REG_4_O4), .pin11(CLK));
  _74244 #(.ShowInternalStructure("true")) u_74244_2 (
    .pin1(R_REG_4), .pin2(REG_4_O0), .pin3(OB_8), .pin4(REG_4_O1), .pin5(OB_7), .pin6(REG_4_O2), .pin7(OB_6),
    .pin8(REG_4_O3), .pin9(OB_5), .pin19(R_REG_4), .pin18(OB_1), .pin17(REG_4_O7), .pin16(OB_2),
    .pin15(REG_4_O6), .pin14(OB_3), .pin13(REG_4_O5), .pin12(OB_4), .pin11(REG_4_O4));
  _74377 #(.ShowInternalStructure("true")) u_74377_3 (
    .pin1(W_REG_1), .pin2(REG_1_O0), .pin3(B_1), .pin4(B_2), .pin5(REG_1_O1), .pin6(REG_1_O2), .pin7(B_3),
    .pin8(B_4), .pin9(REG_1_O3), .pin19(REG_1_O7), .pin18(B_8), .pin17(B_7), .pin16(REG_1_O6),
    .pin15(REG_1_O5), .pin14(B_6), .pin13(B_5), .pin12(REG_1_O4), .pin11(CLK));
  _74244 #(.ShowInternalStructure("true")) u_74244_3 (
    .pin1(R_REG_1), .pin2(REG_1_O0), .pin3(OB_8), .pin4(REG_1_O1), .pin5(OB_7), .pin6(REG_1_O2), .pin7(OB_6),
    .pin8(REG_1_O3), .pin9(OB_5), .pin19(R_REG_1), .pin18(OB_1), .pin17(REG_1_O7), .pin16(OB_2),
    .pin15(REG_1_O6), .pin14(OB_3), .pin13(REG_1_O5), .pin12(OB_4), .pin11(REG_1_O4));
  _74377 #(.ShowInternalStructure("true")) u_74377_4 (
    .pin1(W_REG_5), .pin2(REG_5_O0), .pin3(B_1), .pin4(B_2), .pin5(REG_5_O1), .pin6(REG_5_O2), .pin7(B_3),
    .pin8(B_4), .pin9(REG_5_O3), .pin19(REG_5_O7), .pin18(B_8), .pin17(B_7), .pin16(REG_5_O6),
    .pin15(REG_5_O5), .pin14(B_6), .pin13(B_5), .pin12(REG_5_O4), .pin11(CLK));
  _74244 #(.ShowInternalStructure("true")) u_74244_4 (
    .pin1(R_REG_5), .pin2(REG_5_O0), .pin3(OB_8), .pin4(REG_5_O1), .pin5(OB_7), .pin6(REG_5_O2), .pin7(OB_6),
    .pin8(REG_5_O3), .pin9(OB_5), .pin19(R_REG_5), .pin18(OB_1), .pin17(REG_5_O7), .pin16(OB_2),
    .pin15(REG_5_O6), .pin14(OB_3), .pin13(REG_5_O5), .pin12(OB_4), .pin11(REG_5_O4));
  _74377 #(.ShowInternalStructure("true")) u_74377_5 (
    .pin1(W_REG_2), .pin2(REG_2_O0), .pin3(B_1), .pin4(B_2), .pin5(REG_2_O1), .pin6(REG_2_O2), .pin7(B_3),
    .pin8(B_4), .pin9(REG_2_O3), .pin19(REG_2_O7), .pin18(B_8), .pin17(B_7), .pin16(REG_2_O6),
    .pin15(REG_2_O5), .pin14(B_6), .pin13(B_5), .pin12(REG_2_O4), .pin11(CLK));
  _74244 #(.ShowInternalStructure("true")) u_74244_5 (
    .pin1(R_REG_2), .pin2(REG_2_O0), .pin3(OB_8), .pin4(REG_2_O1), .pin5(OB_7), .pin6(REG_2_O2), .pin7(OB_6),
    .pin8(REG_2_O3), .pin9(OB_5), .pin19(R_REG_2), .pin18(OB_1), .pin17(REG_2_O7), .pin16(OB_2),
    .pin15(REG_2_O6), .pin14(OB_3), .pin13(REG_2_O5), .pin12(OB_4), .pin11(REG_2_O4));
  _74377 #(.ShowInternalStructure("true")) u_74377_6 (
    .pin1(W_REG_6), .pin2(REG_6_O0), .pin3(B_1), .pin4(B_2), .pin5(REG_6_O1), .pin6(REG_6_O2), .pin7(B_3),
    .pin8(B_4), .pin9(REG_6_O3), .pin19(REG_6_O7), .pin18(B_8), .pin17(B_7), .pin16(REG_6_O6),
    .pin15(REG_6_O5), .pin14(B_6), .pin13(B_5), .pin12(REG_6_O4), .pin11(CLK));
  _74244 #(.ShowInternalStructure("true")) u_74244_6 (
    .pin1(R_REG_6), .pin2(REG_6_O0), .pin3(OB_8), .pin4(REG_6_O1), .pin5(OB_7), .pin6(REG_6_O2), .pin7(OB_6),
    .pin8(REG_6_O3), .pin9(OB_5), .pin19(R_REG_6), .pin18(OB_1), .pin17(REG_6_O7), .pin16(OB_2),
    .pin15(REG_6_O6), .pin14(OB_3), .pin13(REG_6_O5), .pin12(OB_4), .pin11(REG_6_O4));
  _74377 #(.ShowInternalStructure("true")) u_74377_7 (
    .pin1(W_REG_3), .pin2(REG_3_O0), .pin3(B_1), .pin4(B_2), .pin5(REG_3_O1), .pin6(REG_3_O2), .pin7(B_3),
    .pin8(B_4), .pin9(REG_3_O3), .pin19(REG_3_O7), .pin18(B_8), .pin17(B_7), .pin16(REG_3_O6),
    .pin15(REG_3_O5), .pin14(B_6), .pin13(B_5), .pin12(REG_3_O4), .pin11(CLK));
  _74244 #(.ShowInternalStructure("true")) u_74244_7 (
    .pin1(R_REG_3), .pin2(REG_3_O0), .pin3(OB_8), .pin4(REG_3_O1), .pin5(OB_7), .pin6(REG_3_O2), .pin7(OB_6),
    .pin8(REG_3_O3), .pin9(OB_5), .pin19(R_REG_3), .pin18(OB_1), .pin17(REG_3_O7), .pin16(OB_2),
    .pin15(REG_3_O6), .pin14(OB_3), .pin13(REG_3_O5), .pin12(OB_4), .pin11(REG_3_O4));
  _74377 #(.ShowInternalStructure("true")) u_74377_8 (
    .pin1(W_REG_7), .pin2(REG_7_O0), .pin3(B_1), .pin4(B_2), .pin5(REG_7_O1), .pin6(REG_7_O2), .pin7(B_3),
    .pin8(B_4), .pin9(REG_7_O3), .pin19(REG_7_O7), .pin18(B_8), .pin17(B_7), .pin16(REG_7_O6),
    .pin15(REG_7_O5), .pin14(B_6), .pin13(B_5), .pin12(REG_7_O4), .pin11(CLK));
  _74244 #(.ShowInternalStructure("true")) u_74244_8 (
    .pin1(R_REG_7), .pin2(REG_7_O0), .pin3(OB_8), .pin4(REG_7_O1), .pin5(OB_7), .pin6(REG_7_O2), .pin7(OB_6),
    .pin8(REG_7_O3), .pin9(OB_5), .pin19(R_REG_7), .pin18(OB_1), .pin17(REG_7_O7), .pin16(OB_2),
    .pin15(REG_7_O6), .pin14(OB_3), .pin13(REG_7_O5), .pin12(OB_4), .pin11(REG_7_O4));

  // Other names for the same wires on the sheet: CPU_Clock = CLK; DB_1 = B_1; DB_2 = B_2; DB_3 = B_3; DB_4 = B_4;
  //   DB_5 = B_5; DB_6 = B_6; DB_7 = B_7; DB_8 = B_8
endmodule

module USER_REGISTER_BLOCK_Numbers (
  input  W_UREG_0,
  input  W_UREG_1,
  input  W_UREG_2,
  input  R_UREG_0,
  input  R_UREG_1,
  input  R_UREG_2,
  input  B_1,
  input  B_2,
  input  B_3,
  input  B_4,
  input  B_5,
  input  B_6,
  input  B_7,
  input  B_8,
  input  CLK,
  output URN_0,
  output URN_1,
  output URN_2
);

  wire n74244_1_pin7, n74244_1_pin9, n74244_1_pin11, n74244_1_pin12, n74244_1_pin13, n74244_1_pin15,
       n74244_1_pin17, n74244_2_pin7, n74244_2_pin9, n74244_2_pin11, n74244_2_pin12, n74244_2_pin13,
       n74244_2_pin15, n74244_2_pin17, n74244_3_pin7, n74244_3_pin9, n74244_3_pin11, n74244_3_pin12,
       n74244_3_pin13, n74244_3_pin15, n74244_3_pin17, n74377_1_pin9, n74377_1_pin12, n74377_1_pin15,
       n74377_1_pin16, n74377_1_pin19, n74377_2_pin9, n74377_2_pin12, n74377_2_pin15, n74377_2_pin16,
       n74377_2_pin19, n74377_3_pin9, n74377_3_pin12, n74377_3_pin15, n74377_3_pin16, n74377_3_pin19,
       n_R_UREG_0, n_R_UREG_1, n_R_UREG_2, n_W_UREG_0, n_W_UREG_1, n_W_UREG_2, pull_resistor_1_node,
       pull_resistor_2_node, pull_resistor_3_node, pull_resistor_8_node, pull_resistor_9_node,
       pull_resistor_10_node, pull_resistor_15_node, pull_resistor_16_node, pull_resistor_17_node, UREG_0_O0,
       UREG_0_O1, UREG_0_O2, UREG_1_O0, UREG_1_O1, UREG_1_O2, UREG_2_O0, UREG_2_O1, UREG_2_O2;

  // NoConnect on n74377_1_pin9
  Pull_Resistor pull_resistor_1 (.node(pull_resistor_1_node));
  Pull_Resistor pull_resistor_2 (.node(pull_resistor_2_node));
  // NoConnect on n74244_1_pin7
  Pull_Resistor pull_resistor_3 (.node(pull_resistor_3_node));
  // NoConnect on n74244_1_pin9
  _74377 #(.ShowInternalStructure("true")) u_74377_1 (
    .pin1(n_W_UREG_0), .pin2(UREG_0_O0), .pin3(B_1), .pin4(B_2), .pin5(UREG_0_O1), .pin6(UREG_0_O2),
    .pin7(B_3), .pin8(B_4), .pin9(n74377_1_pin9), .pin19(n74377_1_pin19), .pin18(B_8), .pin17(B_7),
    .pin16(n74377_1_pin16), .pin15(n74377_1_pin15), .pin14(B_6), .pin13(B_5), .pin12(n74377_1_pin12),
    .pin11(CLK));
  _74244 #(.ShowInternalStructure("true")) u_74244_1 (
    .pin1(n_R_UREG_0), .pin2(UREG_0_O0), .pin3(pull_resistor_1_node), .pin4(UREG_0_O1),
    .pin5(pull_resistor_2_node), .pin6(UREG_0_O2), .pin7(n74244_1_pin7), .pin8(pull_resistor_3_node),
    .pin9(n74244_1_pin9), .pin19(R_UREG_0), .pin18(URN_0), .pin17(n74244_1_pin17), .pin16(URN_1),
    .pin15(n74244_1_pin15), .pin14(URN_2), .pin13(n74244_1_pin13), .pin12(n74244_1_pin12),
    .pin11(n74244_1_pin11));
  Pull_Resistor pull_resistor_4 (.node(n74244_1_pin17));
  Pull_Resistor pull_resistor_5 (.node(n74244_1_pin15));
  Pull_Resistor pull_resistor_6 (.node(n74244_1_pin13));
  // NoConnect on n74244_1_pin12
  Pull_Resistor pull_resistor_7 (.node(n74244_1_pin11));
  // NoConnect on n74377_1_pin19
  // NoConnect on n74377_1_pin16
  // NoConnect on n74377_1_pin15
  // NoConnect on n74377_1_pin12
  // NoConnect on n74377_2_pin9
  Pull_Resistor pull_resistor_8 (.node(pull_resistor_8_node));
  Pull_Resistor pull_resistor_9 (.node(pull_resistor_9_node));
  // NoConnect on n74244_2_pin7
  Pull_Resistor pull_resistor_10 (.node(pull_resistor_10_node));
  // NoConnect on n74244_2_pin9
  _74377 #(.ShowInternalStructure("true")) u_74377_2 (
    .pin1(n_W_UREG_1), .pin2(UREG_1_O0), .pin3(B_1), .pin4(B_2), .pin5(UREG_1_O1), .pin6(UREG_1_O2),
    .pin7(B_3), .pin8(B_4), .pin9(n74377_2_pin9), .pin19(n74377_2_pin19), .pin18(B_8), .pin17(B_7),
    .pin16(n74377_2_pin16), .pin15(n74377_2_pin15), .pin14(B_6), .pin13(B_5), .pin12(n74377_2_pin12),
    .pin11(CLK));
  _74244 #(.ShowInternalStructure("true")) u_74244_2 (
    .pin1(n_R_UREG_1), .pin2(UREG_1_O0), .pin3(pull_resistor_8_node), .pin4(UREG_1_O1),
    .pin5(pull_resistor_9_node), .pin6(UREG_1_O2), .pin7(n74244_2_pin7), .pin8(pull_resistor_10_node),
    .pin9(n74244_2_pin9), .pin19(R_UREG_1), .pin18(URN_0), .pin17(n74244_2_pin17), .pin16(URN_1),
    .pin15(n74244_2_pin15), .pin14(URN_2), .pin13(n74244_2_pin13), .pin12(n74244_2_pin12),
    .pin11(n74244_2_pin11));
  Pull_Resistor pull_resistor_11 (.node(n74244_2_pin17));
  Pull_Resistor pull_resistor_12 (.node(n74244_2_pin15));
  Pull_Resistor pull_resistor_13 (.node(n74244_2_pin13));
  // NoConnect on n74244_2_pin12
  Pull_Resistor pull_resistor_14 (.node(n74244_2_pin11));
  // NoConnect on n74377_2_pin19
  // NoConnect on n74377_2_pin16
  // NoConnect on n74377_2_pin15
  // NoConnect on n74377_2_pin12
  // NoConnect on n74377_3_pin9
  Pull_Resistor pull_resistor_15 (.node(pull_resistor_15_node));
  Pull_Resistor pull_resistor_16 (.node(pull_resistor_16_node));
  // NoConnect on n74244_3_pin7
  Pull_Resistor pull_resistor_17 (.node(pull_resistor_17_node));
  // NoConnect on n74244_3_pin9
  _74377 #(.ShowInternalStructure("true")) u_74377_3 (
    .pin1(n_W_UREG_2), .pin2(UREG_2_O0), .pin3(B_1), .pin4(B_2), .pin5(UREG_2_O1), .pin6(UREG_2_O2),
    .pin7(B_3), .pin8(B_4), .pin9(n74377_3_pin9), .pin19(n74377_3_pin19), .pin18(B_8), .pin17(B_7),
    .pin16(n74377_3_pin16), .pin15(n74377_3_pin15), .pin14(B_6), .pin13(B_5), .pin12(n74377_3_pin12),
    .pin11(CLK));
  // NoConnect on n74377_3_pin19
  // NoConnect on n74377_3_pin16
  // NoConnect on n74377_3_pin15
  // NoConnect on n74377_3_pin12
  _74244 #(.ShowInternalStructure("true")) u_74244_3 (
    .pin1(n_R_UREG_2), .pin2(UREG_2_O0), .pin3(pull_resistor_15_node), .pin4(UREG_2_O1),
    .pin5(pull_resistor_16_node), .pin6(UREG_2_O2), .pin7(n74244_3_pin7), .pin8(pull_resistor_17_node),
    .pin9(n74244_3_pin9), .pin19(R_UREG_2), .pin18(URN_0), .pin17(n74244_3_pin17), .pin16(URN_1),
    .pin15(n74244_3_pin15), .pin14(URN_2), .pin13(n74244_3_pin13), .pin12(n74244_3_pin12),
    .pin11(n74244_3_pin11));
  Pull_Resistor pull_resistor_18 (.node(n74244_3_pin17));
  Pull_Resistor pull_resistor_19 (.node(n74244_3_pin15));
  Pull_Resistor pull_resistor_20 (.node(n74244_3_pin13));
  // NoConnect on n74244_3_pin12
  Pull_Resistor pull_resistor_21 (.node(n74244_3_pin11));
  _7419 #(.ShowInternalStructure("true")) u_7419_1 (
    .pin1(W_UREG_0), .pin2(n_W_UREG_0), .pin3(W_UREG_1), .pin4(n_W_UREG_1), .pin5(W_UREG_2),
    .pin6(n_W_UREG_2), .pin13(R_UREG_0), .pin12(n_R_UREG_0), .pin11(R_UREG_1), .pin10(n_R_UREG_1),
    .pin9(R_UREG_2), .pin8(n_R_UREG_2));

  // Other names for the same wires on the sheet: CPU_Clock = CLK; DB_1 = B_1; DB_2 = B_2; DB_3 = B_3; DB_4 = B_4;
  //   DB_5 = B_5; DB_6 = B_6; DB_7 = B_7; DB_8 = B_8
endmodule
